// Logisim project cpu-riscv-hust-2022.circ as structural Verilog
module PCType (
  input  Eq,
  input  Lt,
  input  Ge,
  input  URET,
  input  JALR,
  input  JAL,
  input  BEQ,
  input  BNE,
  input  BLT_U,
  output [1:0] JmpType,
  output Jmp,
  output ImmJmp,
  output LinkToReg,
  output UncondJmp,
  output CondBranch,
  output BranchInstr,
  output UncertainJmp
);

  wire and_1_out, and_2_out, and_3_out;

  Pull_Resistor pull_resistor_1 (.node(JmpType));
  Priority_Encoder #(.select(2), .disabled(0)) priority_encoder_1 (
    .in1(URET), .in2(JALR), .in3(ImmJmp), .out(JmpType), .gs(Jmp));  // open: in0, en_out, en_in
  or or_1 (LinkToReg, JALR, JAL);
  or or_2 (ImmJmp, JAL, and_1_out, and_2_out, and_3_out);
  and and_1 (and_1_out, Eq, BEQ);
  or or_3 (UncertainJmp, JALR, BEQ, BNE, BLT_U);
  or or_4 (CondBranch, and_1_out, and_2_out, and_3_out);
  and and_2 (and_2_out, ~Eq, BNE);  // AND_Gate
  and and_3 (and_3_out, Lt, BLT_U);
  or or_5 (BranchInstr, BLT_U, BNE, BEQ);

  assign UncondJmp = LinkToReg;
endmodule

// 单周期硬布线控制器
module \单周期硬布线控制器  (
  input  [4:0] OP,
  input  [4:0] Funct,
  input  in_3,
  input  [1:0] LegitIR,
  output [3:0] ALU_OP,
  output ALU_RESULT,
  output uret,
  output MemToReg,
  output ecall,
  output MemWrite,
  output ALU_SRC,
  output RegWrite,
  output S_type,
  output Beq,
  output Bne,
  output JALR,
  output JAL,
  output Blt_u,
  output R1Dep,
  output R2Dep,
  output CSR,
  output [2:0] Func3
);

  wire and_1_out, \控制信号自动生成_1_ecall ;

  and and_1 (and_1_out, LegitIR[0], LegitIR[1]);
  \运算控制器自动生成  \u_运算控制器自动生成_1  (
    .OP2(OP[0]), .OP3(OP[1]), .OP4(OP[2]), .OP5(OP[3]), .OP6(OP[4]), .F12(Funct[0]), .F13(Funct[1]),
    .F14(Funct[2]), .F25(Funct[3]), .F30(Funct[4]), .S0(ALU_OP[0]), .S1(ALU_OP[1]), .S2(ALU_OP[2]),
    .S3(ALU_OP[3]), .RE(ALU_RESULT));
  \控制信号自动生成  \u_控制信号自动生成_1  (
    .OP2(OP[0]), .OP3(OP[1]), .MemToReg(MemToReg), .OP4(OP[2]), .OP5(OP[3]), .OP6(OP[4]),
    .MemWrite(MemWrite), .F12(Funct[0]), .F13(Funct[1]), .F14(Funct[2]), .F25(Funct[3]), .F30(Funct[4]),
    .EN(and_1_out), .ALU_SRC(ALU_SRC), .RegWrite(RegWrite), .ecall(\控制信号自动生成_1_ecall ), .S_Type(S_type),
    .BEQ(Beq), .BNE(Bne), .JALR(JALR), .JAL(JAL), .BLTU(Blt_u), .R1Dep(R1Dep), .R2Dep(R2Dep), .CSR(CSR));
  and and_2 (uret, in_3, \控制信号自动生成_1_ecall );
  and and_3 (ecall, ~in_3, \控制信号自动生成_1_ecall );  // AND_Gate

  assign Func3 = Funct[2:0];

  // Other names for the same wires on the sheet: IR21 = in_3; OP_CODE[4:0] = OP

  // Notes on the sheet:
  //   控制信号生成，产生数据通路需要的其他控制信号
  //   运算器控制器，根据指令生成运算器功能选择信号
endmodule

module \单周期RISC_V  (
  input  IR1,
  input  IR2,
  input  IR3,
  output RegWrite,
  output MemWrite,
  output [31:0] PC,
  output [31:0] IR,
  output [31:0] RDin,
  output [31:0] MDin,
  output [31:0] LedData
);

  wire and_1_out, CLK, clock_1_out, comparator_1_eq, comparator_2_eq, comparator_2_lt, d_ff_1_q, ecall, Eq,
       Ge, Go, halt, IR1_t, IR2_t, IR3_t, IRA, IRB, IRC, JAL, LinkToReg, Lt, nand_1_out, not_1_out,
       not_2_out, RST, W1, W2, W3, \单周期硬布线控制器_1_alu_result , \单周期硬布线控制器_1_alu_src , \单周期硬布线控制器_1_beq ,
       \单周期硬布线控制器_1_blt_u , \单周期硬布线控制器_1_bne , \单周期硬布线控制器_1_jalr , \单周期硬布线控制器_1_s_type , \单周期硬布线控制器_1_uret ;
  wire [0:0] \单周期硬布线控制器_1_memtoreg ;
  wire [1:0] PCType, \单周期硬布线控制器_1_func3 ;
  wire [2:2] \单周期硬布线控制器_1_func3_2 ;
  wire [3:0] \单周期硬布线控制器_1_alu_op ;
  wire [4:0] multiplexer_2_out, multiplexer_3_out;
  wire [7:0] bitselector_1_out;
  wire [9:0] multiplexer_7_out_2;
  wire [11:0] multiplexer_4_out;
  wire [12:0] CNT_num;
  wire [15:0] bitselector_2_out, \总周期数 ;
  wire [31:0] alu_1_result_2, bit_extender_1_out, bit_extender_2_out, bit_extender_3_out, bit_extender_4_out,
       bit_extender_5_out, bit_extender_6_out, bit_extender_7_out, multiplexer_1_out, multiplexer_5_out,
       multiplexer_6_out, multiplexer_7_out, multiplexer_8_out, multiplexer_9_out, multiplexer_10_out, PCp4,
       PCRelJmp, R1, ram_1_data, RegRelJmp;

  Button \u_继续运行  (.out(Go));
  Button _1 (.out(IRA));
  Button _2 (.out(IRB));
  Button _3 (.out(IRC));
  Button \u_总复位  (.out(RST));
  LED led_1 (.in(W1));
  LED led_2 (.in(W2));
  LED led_3 (.in(W3));
  Hex_Digit_Display hex_digit_display_1 (.value(LedData[31:28]));  // open: dp
  // Probe on PCType
  // Probe on multiplexer_1_out
  Multiplexer #(.select(2), .width(32), .enable("false")) multiplexer_1 (
    .in0(PCp4), .in2(RegRelJmp), .in3(PCRelJmp), .out(multiplexer_1_out), .sel(PCType));  // open: in1
  not not_1 (not_1_out, halt);
  Adder #(.width(32)) adder_1 (.a(PC), .b(32'h4), .out(PCp4));  // open: cin, cout
  Hex_Digit_Display hex_digit_display_2 (.value(LedData[27:24]));  // open: dp
  Hex_Digit_Display hex_digit_display_3 (.value(LedData[23:20]));  // open: dp
  Register #(.width(32), .Select("low")) u_PC (.D(multiplexer_1_out), .en(not_1_out), .Q(PC), .clk(CLK), .clr(RST));
  not not_2 (not_2_out, halt);
  Counter #(.width(16), .max('hffff)) NXC (
    .count(not_2_out), .Q(\总周期数 ), .clk(CLK), .clr(RST));  // open: load, D, carry, preset, down
  Hex_Digit_Display hex_digit_display_4 (.value(LedData[19:16]));  // open: dp
  Hex_Digit_Display hex_digit_display_5 (.value(LedData[15:12]));  // open: dp
  // Probe on PC
  Hex_Digit_Display hex_digit_display_6 (.value(LedData[11:8]));  // open: dp
  Hex_Digit_Display hex_digit_display_7 (.value(LedData[7:4]));  // open: dp
  // Probe on \总周期数 
  // RiscV_Probe riscv_probe_1: pin names not known; wires that end beside it: IR
  Hex_Digit_Display hex_digit_display_8 (.value(LedData[3:0]));  // open: dp
  // Probe on IR
  ROM #(.addrWidth(10), .dataWidth(32), .Select("high")) rom_1 (.addr(PC[11:2]), .data(IR));
  or or_1 (IR1_t, IR1, IRA);
  PCType pctype_1 (
    .JmpType(PCType), .Eq(Eq), .Lt(Lt), .Ge(Ge), .URET(\单周期硬布线控制器_1_uret ), .JALR(\单周期硬布线控制器_1_jalr ),
    .JAL(JAL), .BEQ(\单周期硬布线控制器_1_beq ), .BNE(\单周期硬布线控制器_1_bne ), .BLT_U(\单周期硬布线控制器_1_blt_u ),
    .LinkToReg(LinkToReg));  // open: Jmp, UncondJmp, CondBranch, ImmJmp, UncertainJmp, BranchInstr
  \单周期硬布线控制器  \u_单周期硬布线控制器_1  (
    .Funct({IR[30], IR[25], IR[14:12]}), .OP(IR[6:2]), .ALU_OP(\单周期硬布线控制器_1_alu_op ),
    .MemToReg(\单周期硬布线控制器_1_memtoreg [0]), .MemWrite(MemWrite), .ALU_SRC(\单周期硬布线控制器_1_alu_src ),
    .RegWrite(RegWrite), .ecall(ecall), .S_type(\单周期硬布线控制器_1_s_type ), .JALR(\单周期硬布线控制器_1_jalr ),
    .Beq(\单周期硬布线控制器_1_beq ), .JAL(JAL), .Bne(\单周期硬布线控制器_1_bne ), .in_3(IR[21]), .uret(\单周期硬布线控制器_1_uret ),
    .Func3({\单周期硬布线控制器_1_func3_2 [2], \单周期硬布线控制器_1_func3 }), .ALU_RESULT(\单周期硬布线控制器_1_alu_result ),
    .Blt_u(\单周期硬布线控制器_1_blt_u ), .LegitIR(IR[1:0]));  // open: R1Dep, R2Dep, CSR
  Multiplexer #(.width(5), .enable("false")) multiplexer_2 (
    .in0(IR[19:15]), .in1(5'b01010), .out(multiplexer_2_out), .sel(ecall));
  Multiplexer #(.width(5), .enable("false")) multiplexer_3 (
    .in0(IR[24:20]), .in1(5'b10001), .out(multiplexer_3_out), .sel(ecall));
  Multiplexer #(.width(12), .enable("false")) multiplexer_4 (
    .in0(IR[31:20]), .in1({IR[31:25], IR[11:7]}), .out(multiplexer_4_out), .sel(\单周期硬布线控制器_1_s_type ));
  assign bit_extender_1_out = {{19{IR[31]}}, {IR[31], IR[7], IR[30:25], IR[11:8], 1'b0}};  // Bit_Extender bit_extender_1
  assign bit_extender_2_out = {{11{IR[31]}}, {IR[31], IR[19:12], IR[20], IR[30:21], 1'b0}};  // Bit_Extender bit_extender_2
  or or_2 (IR2_t, IR2, IRB);
  // Probe on multiplexer_2_out
  // Probe on multiplexer_3_out
  // Probe on IR[11:7]
  Adder #(.width(32)) adder_2 (.a(PC), .b(multiplexer_5_out), .out(PCRelJmp));  // open: cin, cout
  Multiplexer #(.width(32), .enable("false")) multiplexer_5 (
    .in0(bit_extender_1_out), .in1(bit_extender_2_out), .out(multiplexer_5_out), .sel(JAL));
  // Probe on multiplexer_5_out
  Regifile regifile_1 (
    .Din(RDin), .Clk(CLK), .R1(R1), .R2(MDin), .WE(RegWrite), .W_num(IR[11:7]), .R1_num(multiplexer_2_out),
    .R2_num(multiplexer_3_out));
  assign bit_extender_3_out = {{20{multiplexer_4_out[11]}}, multiplexer_4_out};  // Bit_Extender bit_extender_3
  // Probe on bit_extender_3_out
  or or_3 (IR3_t, IR3, IRC);
  // Probe on R1
  Multiplexer #(.width(32), .enable("false")) multiplexer_6 (
    .in0(MDin), .in1(bit_extender_3_out), .out(multiplexer_6_out), .sel(\单周期硬布线控制器_1_alu_src ));
  // Probe on multiplexer_6_out
  // Probe on \单周期硬布线控制器_1_alu_op 
  ALU alu_1 (
    .X(R1), .Y(multiplexer_6_out), .AluOP(\单周期硬布线控制器_1_alu_op ), .Equal(Eq), .Result(RegRelJmp),
    .Result_2(alu_1_result_2), .out_4(Ge), .out_6(Lt));
  and and_1 (and_1_out, ecall, comparator_1_eq);
  Comparator #(.width(32)) comparator_1 (.a(MDin), .b(32'h22), .eq(comparator_1_eq));  // open: gt, lt
  Multiplexer #(.width(32), .enable("false")) multiplexer_7 (
    .in0(RegRelJmp), .in1(alu_1_result_2),
    .out({multiplexer_7_out[31:12], multiplexer_7_out_2, multiplexer_7_out[1:0]}),
    .sel(\单周期硬布线控制器_1_alu_result ));
  Register #(.width(32), .Select("low")) register_1 (.D(R1), .en(and_1_out), .Q(LedData), .clk(CLK), .clr(RST));
  and and_2 (halt, ~comparator_1_eq, ecall, ~Go);  // AND_Gate
  // Probe on {multiplexer_7_out[31:12], multiplexer_7_out_2, multiplexer_7_out[1:0]}
  BitSelector #(.width(32), .group(8)) bitselector_1 (
    .in(ram_1_data), .out(bitselector_1_out), .sel(multiplexer_7_out[1:0]));
  RAM #(.addrWidth(10), .dataWidth(32), .bus("separate"), .Select("high"), .simpleMode("false")) ram_1 (
    .addr(multiplexer_7_out_2), .din(MDin), .data(ram_1_data), .str(MemWrite), .sel(1'b1), .clk(CLK),
    .clr(RST));  // open: ld
  BitSelector #(.width(32), .group(16)) bitselector_2 (
    .in(ram_1_data), .out(bitselector_2_out), .sel(multiplexer_7_out[1]));
  assign bit_extender_4_out = {{24{bitselector_1_out[7]}}, bitselector_1_out};  // Bit_Extender bit_extender_4
  assign bit_extender_5_out = {{24{1'b0}}, bitselector_1_out};  // Bit_Extender bit_extender_5
  assign bit_extender_6_out = {{16{bitselector_2_out[15]}}, bitselector_2_out};  // Bit_Extender bit_extender_6
  assign bit_extender_7_out = {{16{1'b0}}, bitselector_2_out};  // Bit_Extender bit_extender_7
  Multiplexer #(.width(32), .enable("false")) multiplexer_8 (
    .in0(bit_extender_4_out), .in1(bit_extender_5_out), .out(multiplexer_8_out),
    .sel(\单周期硬布线控制器_1_func3_2 [2]));
  Multiplexer #(.select(2), .width(32), .enable("false")) multiplexer_9 (
    .in0(multiplexer_8_out), .in1(multiplexer_10_out), .in2(ram_1_data), .out(multiplexer_9_out),
    .sel(\单周期硬布线控制器_1_func3 ));  // open: in3
  Multiplexer #(.width(32), .enable("false")) multiplexer_10 (
    .in0(bit_extender_6_out), .in1(bit_extender_7_out), .out(multiplexer_10_out),
    .sel(\单周期硬布线控制器_1_func3_2 [2]));
  D_Flip_Flop #(.trigger("high"), .Pre_Clr_Positions("LEGACY"), .enable("true"), .NewFFLayout("false")) d_ff_1 (.Q(d_ff_1_q));  // open: clk, D, Qn, preset, en, reset
  // Probe on 13'hc
  // Probe on {LinkToReg, \单周期硬布线控制器_1_memtoreg [0]}
  Multiplexer #(.select(2), .width(32), .enable("false")) multiplexer_11 (
    .in0({multiplexer_7_out[31:12], multiplexer_7_out_2, multiplexer_7_out[1:0]}), .in1(multiplexer_9_out),
    .in2(PCp4), .out(RDin), .sel({LinkToReg, \单周期硬布线控制器_1_memtoreg [0]}));  // open: in3
  // Probe on RDin
  Comparator #(.width(13)) comparator_2 (
    .a(CNT_num), .b(13'hc), .eq(comparator_2_eq), .lt(comparator_2_lt));  // open: gt
  Clock clock_1 (.out(clock_1_out));
  Counter #(.width(13), .max('h1fff), .ongoal("stay"), .behavior("old")) counter_1 (
    .count(comparator_2_lt), .Q(CNT_num), .clk(clock_1_out));  // open: load, D, carry, clr, preset
  nand nand_1 (nand_1_out, d_ff_1_q, comparator_2_eq);
  assign CLK = nand_1_out ? clock_1_out : 1'bz;  // Controlled_Buffer controlled_buffer_1
  Pull_Resistor #(.pull(1)) pull_resistor_1 (.node(CLK));

  // Other names for the same wires on the sheet: R2[31:0] = MDin

  // Notes on the sheet:
  //   中断源
  //   中断等待指示
  //   数码管输出应该用寄存器锁存，否则显示数据只能一闪而过
  //   数码管输出
  //   指令探针
  //   指令存储器
  //   指令字
  //   contents of rom_1 (hex, n*v repeats v):
  //   100493 100006f 100493 200913 300993 100006f 100493 200913 300993 100006f 100493 200913 300993
  //   100006f 100493 200913 300993 3c4000ef 100413 100493 1f49493 900533 2200893 73 24d493 48463 fedff06f
  //   900533 2200893 73 100493 249493 900533 2200893 73 48463 fedff06f 100493 1f49493 900533 2200893 73
  //   4034d493 900533 2200893 73 4044d493 900533 2200893 73 4044d493 900533 2200893 73 4044d493 900533
  //   2200893 73 4044d493 900533 2200893 73 4044d493 900533 2200893 73 4044d493 900533 2200893 73 4044d493
  //   900533 2200893 73 100413 1f41993 41f9d993 433 c00913 300b13 140413 f47413 800293 100313 499993
  //   89e9b3 1300533 2200893 73 406282b3 fe0294e3 140413 f00f93 1f47433 1c41413 800293 100313 49d993
  //   89e9b3 1300533 2200893 73 406282b3 fe0294e3 1c45413 406b0b33 b0463 f95ff06f 2b3 fff2c293 829293
  //   ff2e293 500533 2200893 73 fff00413 493 84a023 140413 448493 84a023 140413 448493 84a023 140413
  //   448493 84a023 140413 448493 84a023 140413 448493 84a023 140413 448493 84a023 140413 448493 84a023
  //   140413 448493 84a023 140413 448493 84a023 140413 448493 84a023 140413 448493 84a023 140413 448493
  //   84a023 140413 448493 84a023 140413 448493 84a023 140413 448493 84a023 140413 448493 140413 433
  //   3c00493 42983 4aa03 149a2b3 28663 134a023 1442023 ffc48493 fe9412e3 800533 2200893 73 440413 3c00493
  //   fc9416e3 3200893 73 200293 1100493 849493 1148493 1049493 900533 2200893 73 1c00e13 254d4b3 900533
  //   2200893 73 fffe0e13 fe0e16e3 a00893 73 8800493 849493 4848493 8700913 891913 5490913 2997933 1091913
  //   11096913 1200533 2200893 73 a00893 73 313 1000e13 8400493 849493 8348493 400913 891913 490913 849493
  //   8248493 849493 8148493 891913 490913 891913 490913 932023 12484b3 430313 fffe0e13 fe0e18e3 2000e13
  //   313 30483 900533 2200893 73 130313 fffe0e13 fe0e14e3 a00893 73 ff100493 900533 2200893 73 148493
  //   fe9068e3 900533 2200893 73 a00893 73 413 140413 800533 2200893 73 240413 800533 2200893 73 340413
  //   800533 2200893 73 440413 800533 2200893 73 540413 800533 2200893 73 640413 800533 2200893 73 740413
  //   800533 2200893 73 840413 800533 2200893 2200893 73 8067
  //   JALR
  //   URET
  //   I-Imm[11:0]
  //   S-Imm[11:0]
  //   B-Imm[12:1]
  //   J-Imm[20:1]
  //   JAL
  //   Beq
  //   Bne
  //   Blt[u]
  //   MemToReg
  //   MemWrite
  //   AluOP
  //   AluResult
  //   AluSrcB
  //   RegWrite
  //   I/S-ImmType
  //   为方便自动评测，需要输出PC，IR，寄存器堆写如数据RDin
  //   数据存储器
  //   RAM写使能MemWrite、RAM写入数据MDin等信号
  //   控制位
  //   暂停节拍，不能为0
  //   戳工具置1进入计数暂停模式，ctrl+k时钟自动运行到对应节拍暂停
  //   ctrl+k关闭时钟连续运行，将控制位置零，进入单步调试模式调试
  //   用这个时钟源需要去掉电路中的其他时钟源
  //   可计数暂停的时钟源
endmodule

// 运算器控制器
module \运算控制器自动生成  (
  input  OP2,
  input  OP3,
  input  OP4,
  input  OP5,
  input  OP6,
  input  F12,
  input  F13,
  input  F14,
  input  F25,
  input  F30,
  output S0,
  output S1,
  output S2,
  output S3,
  output RE
);

  wire and_1_out, and_2_out, and_3_out, and_4_out, and_5_out, and_6_out, and_7_out, and_8_out, and_9_out,
       and_10_out, and_11_out, and_12_out, and_13_out, and_14_out, and_15_out, and_16_out, and_17_out,
       and_18_out, and_19_out, and_20_out, and_21_out, and_22_out, and_23_out, and_24_out, and_25_out,
       and_26_out, and_27_out, and_28_out, and_29_out, and_30_out, and_31_out, and_32_out, and_33_out,
       and_34_out, and_35_out, and_36_out, and_37_out, and_38_out, and_39_out, not_1_out, not_2_out,
       not_3_out, not_4_out, not_5_out, not_6_out, not_7_out, not_8_out, not_9_out, not_10_out, not_11_out,
       not_12_out, not_13_out, not_14_out, not_15_out, not_16_out, not_17_out, not_18_out, not_19_out,
       not_20_out, not_21_out, not_22_out, not_23_out, not_24_out, not_25_out, not_26_out, not_27_out,
       not_28_out, not_29_out, not_30_out, not_31_out, not_32_out, not_33_out, not_34_out, not_35_out,
       not_36_out, not_37_out, not_38_out, not_39_out, not_40_out, not_41_out, not_42_out, not_43_out,
       not_44_out, not_45_out, not_46_out, not_47_out, not_48_out, not_49_out, not_50_out, not_51_out,
       not_52_out, not_53_out, not_54_out, not_55_out, not_56_out, not_57_out, not_58_out, not_59_out,
       not_60_out, not_61_out, not_62_out, not_63_out, not_64_out, not_65_out, not_66_out, not_67_out,
       not_68_out, not_69_out, not_70_out, not_71_out, not_72_out, not_73_out, not_74_out, not_75_out,
       not_76_out, not_77_out, not_78_out, not_79_out, not_80_out, not_81_out, not_82_out, not_83_out,
       not_84_out, not_85_out, not_86_out, not_87_out, not_88_out, not_89_out, not_90_out, not_91_out,
       not_92_out, not_93_out, not_94_out, not_95_out, not_96_out, not_97_out, not_98_out, not_99_out,
       not_100_out, not_101_out, not_102_out, not_103_out, not_104_out, not_105_out, not_106_out,
       not_107_out, not_108_out, not_109_out, not_110_out, not_111_out, not_112_out, not_113_out,
       not_114_out, not_115_out, not_116_out, not_117_out, not_118_out, not_119_out, not_120_out,
       not_121_out, not_122_out, not_123_out, not_124_out, not_125_out, not_126_out, not_127_out,
       not_128_out, not_129_out, not_130_out, not_131_out, not_132_out, not_133_out, not_134_out,
       not_135_out, not_136_out, not_137_out, not_138_out, not_139_out, not_140_out, not_141_out,
       not_142_out, not_143_out, not_144_out, not_145_out, not_146_out, not_147_out, not_148_out,
       not_149_out, not_150_out, not_151_out, not_152_out, not_153_out, not_154_out, not_155_out,
       not_156_out, not_157_out, not_158_out, not_159_out, not_160_out, not_161_out, not_162_out,
       not_163_out, not_164_out, not_165_out, not_166_out, not_167_out, not_168_out, not_169_out,
       not_170_out, not_171_out, not_172_out, not_173_out, not_174_out, not_175_out, not_176_out,
       not_177_out, not_178_out, not_179_out, not_180_out, not_181_out, not_182_out, not_183_out,
       not_184_out, not_185_out, not_186_out, not_187_out, not_188_out, not_189_out, not_190_out,
       not_191_out, not_192_out, not_193_out, not_194_out, not_195_out, not_196_out, not_197_out,
       not_198_out, not_199_out, not_200_out, not_201_out, not_202_out, not_203_out, not_204_out,
       not_205_out, not_206_out, not_207_out, not_208_out, not_209_out, not_210_out, not_211_out,
       not_212_out, not_213_out, not_214_out, not_215_out, not_216_out, not_217_out, not_218_out,
       not_219_out, not_220_out, not_221_out, not_222_out, not_223_out;

  not not_1 (not_1_out, F30);
  not not_2 (not_2_out, F25);
  not not_3 (not_3_out, F14);
  not not_4 (not_4_out, F13);
  not not_5 (not_5_out, F12);
  not not_6 (not_6_out, OP6);
  not not_7 (not_7_out, OP3);
  not not_8 (not_8_out, OP2);
  not not_9 (not_9_out, F30);
  not not_10 (not_10_out, F25);
  not not_11 (not_11_out, OP6);
  not not_12 (not_12_out, OP3);
  not not_13 (not_13_out, OP2);
  not not_14 (not_14_out, F30);
  not not_15 (not_15_out, F25);
  not not_16 (not_16_out, F14);
  not not_17 (not_17_out, F12);
  not not_18 (not_18_out, OP6);
  not not_19 (not_19_out, OP3);
  not not_20 (not_20_out, OP2);
  not not_21 (not_21_out, F14);
  not not_22 (not_22_out, F13);
  not not_23 (not_23_out, F12);
  not not_24 (not_24_out, OP6);
  not not_25 (not_25_out, OP5);
  not not_26 (not_26_out, OP3);
  not not_27 (not_27_out, OP2);
  not not_28 (not_28_out, OP6);
  not not_29 (not_29_out, OP5);
  not not_30 (not_30_out, OP3);
  not not_31 (not_31_out, OP2);
  not not_32 (not_32_out, F13);
  not not_33 (not_33_out, F12);
  not not_34 (not_34_out, OP6);
  not not_35 (not_35_out, OP5);
  not not_36 (not_36_out, OP3);
  not not_37 (not_37_out, OP2);
  not not_38 (not_38_out, F14);
  not not_39 (not_39_out, OP6);
  not not_40 (not_40_out, OP5);
  not not_41 (not_41_out, OP3);
  not not_42 (not_42_out, OP2);
  not not_43 (not_43_out, F25);
  not not_44 (not_44_out, F13);
  not not_45 (not_45_out, OP6);
  not not_46 (not_46_out, OP5);
  not not_47 (not_47_out, OP3);
  not not_48 (not_48_out, OP2);
  not not_49 (not_49_out, OP6);
  not not_50 (not_50_out, OP5);
  not not_51 (not_51_out, OP4);
  not not_52 (not_52_out, OP3);
  not not_53 (not_53_out, OP2);
  not not_54 (not_54_out, F14);
  not not_55 (not_55_out, F12);
  not not_56 (not_56_out, OP6);
  not not_57 (not_57_out, OP4);
  not not_58 (not_58_out, OP3);
  not not_59 (not_59_out, OP2);
  not not_60 (not_60_out, F14);
  not not_61 (not_61_out, F13);
  not not_62 (not_62_out, F12);
  not not_63 (not_63_out, OP4);
  not not_64 (not_64_out, OP3);
  not not_65 (not_65_out, F13);
  not not_66 (not_66_out, F12);
  not not_67 (not_67_out, OP4);
  not not_68 (not_68_out, OP3);
  not not_69 (not_69_out, OP2);
  not not_70 (not_70_out, F25);
  not not_71 (not_71_out, F14);
  not not_72 (not_72_out, F13);
  not not_73 (not_73_out, F12);
  not not_74 (not_74_out, OP6);
  not not_75 (not_75_out, OP3);
  not not_76 (not_76_out, OP2);
  not not_77 (not_77_out, F30);
  not not_78 (not_78_out, F25);
  not not_79 (not_79_out, OP6);
  not not_80 (not_80_out, OP3);
  not not_81 (not_81_out, OP2);
  not not_82 (not_82_out, F30);
  not not_83 (not_83_out, F25);
  not not_84 (not_84_out, F14);
  not not_85 (not_85_out, F12);
  not not_86 (not_86_out, OP6);
  not not_87 (not_87_out, OP3);
  not not_88 (not_88_out, OP2);
  not not_89 (not_89_out, OP6);
  not not_90 (not_90_out, OP5);
  not not_91 (not_91_out, OP3);
  not not_92 (not_92_out, OP2);
  not not_93 (not_93_out, F14);
  not not_94 (not_94_out, OP6);
  not not_95 (not_95_out, OP5);
  not not_96 (not_96_out, OP3);
  not not_97 (not_97_out, OP2);
  not not_98 (not_98_out, F30);
  not not_99 (not_99_out, F25);
  not not_100 (not_100_out, F13);
  not not_101 (not_101_out, OP6);
  not not_102 (not_102_out, OP5);
  not not_103 (not_103_out, OP3);
  not not_104 (not_104_out, OP2);
  not not_105 (not_105_out, F13);
  not not_106 (not_106_out, F12);
  not not_107 (not_107_out, OP4);
  not not_108 (not_108_out, OP3);
  not not_109 (not_109_out, OP2);
  not not_110 (not_110_out, F30);
  not not_111 (not_111_out, F25);
  not not_112 (not_112_out, F14);
  not not_113 (not_113_out, F13);
  not not_114 (not_114_out, F12);
  not not_115 (not_115_out, OP6);
  not not_116 (not_116_out, OP3);
  not not_117 (not_117_out, OP2);
  not not_118 (not_118_out, F25);
  not not_119 (not_119_out, F14);
  not not_120 (not_120_out, F13);
  not not_121 (not_121_out, F12);
  not not_122 (not_122_out, OP6);
  not not_123 (not_123_out, OP3);
  not not_124 (not_124_out, OP2);
  not not_125 (not_125_out, F30);
  not not_126 (not_126_out, F25);
  not not_127 (not_127_out, OP6);
  not not_128 (not_128_out, OP3);
  not not_129 (not_129_out, OP2);
  not not_130 (not_130_out, F30);
  not not_131 (not_131_out, F25);
  not not_132 (not_132_out, F14);
  not not_133 (not_133_out, OP6);
  not not_134 (not_134_out, OP3);
  not not_135 (not_135_out, OP2);
  not not_136 (not_136_out, F14);
  not not_137 (not_137_out, F13);
  not not_138 (not_138_out, F12);
  not not_139 (not_139_out, OP6);
  not not_140 (not_140_out, OP5);
  not not_141 (not_141_out, OP3);
  not not_142 (not_142_out, OP2);
  not not_143 (not_143_out, OP6);
  not not_144 (not_144_out, OP5);
  not not_145 (not_145_out, OP3);
  not not_146 (not_146_out, OP2);
  not not_147 (not_147_out, OP6);
  not not_148 (not_148_out, OP5);
  not not_149 (not_149_out, OP4);
  not not_150 (not_150_out, OP3);
  not not_151 (not_151_out, OP2);
  not not_152 (not_152_out, F14);
  not not_153 (not_153_out, F12);
  not not_154 (not_154_out, OP6);
  not not_155 (not_155_out, OP4);
  not not_156 (not_156_out, OP3);
  not not_157 (not_157_out, OP2);
  not not_158 (not_158_out, F14);
  not not_159 (not_159_out, F13);
  not not_160 (not_160_out, F12);
  not not_161 (not_161_out, OP4);
  not not_162 (not_162_out, OP3);
  not not_163 (not_163_out, F30);
  not not_164 (not_164_out, F13);
  not not_165 (not_165_out, OP6);
  not not_166 (not_166_out, OP3);
  not not_167 (not_167_out, OP2);
  not not_168 (not_168_out, F30);
  not not_169 (not_169_out, OP6);
  not not_170 (not_170_out, OP3);
  not not_171 (not_171_out, OP2);
  not not_172 (not_172_out, F12);
  not not_173 (not_173_out, OP4);
  not not_174 (not_174_out, OP3);
  not not_175 (not_175_out, OP2);
  not not_176 (not_176_out, F30);
  not not_177 (not_177_out, F25);
  not not_178 (not_178_out, F12);
  not not_179 (not_179_out, OP6);
  not not_180 (not_180_out, OP3);
  not not_181 (not_181_out, OP2);
  not not_182 (not_182_out, F30);
  not not_183 (not_183_out, F25);
  not not_184 (not_184_out, F14);
  not not_185 (not_185_out, F12);
  not not_186 (not_186_out, OP6);
  not not_187 (not_187_out, OP3);
  not not_188 (not_188_out, OP2);
  not not_189 (not_189_out, F30);
  not not_190 (not_190_out, F25);
  not not_191 (not_191_out, F14);
  not not_192 (not_192_out, OP6);
  not not_193 (not_193_out, OP3);
  not not_194 (not_194_out, OP2);
  not not_195 (not_195_out, F12);
  not not_196 (not_196_out, OP6);
  not not_197 (not_197_out, OP5);
  not not_198 (not_198_out, OP3);
  not not_199 (not_199_out, OP2);
  not not_200 (not_200_out, F13);
  not not_201 (not_201_out, F12);
  not not_202 (not_202_out, OP6);
  not not_203 (not_203_out, OP5);
  not not_204 (not_204_out, OP3);
  not not_205 (not_205_out, OP2);
  not not_206 (not_206_out, F14);
  not not_207 (not_207_out, OP6);
  not not_208 (not_208_out, OP5);
  not not_209 (not_209_out, OP3);
  not not_210 (not_210_out, OP2);
  not not_211 (not_211_out, F12);
  not not_212 (not_212_out, OP4);
  not not_213 (not_213_out, OP3);
  not not_214 (not_214_out, OP2);
  not not_215 (not_215_out, F13);
  not not_216 (not_216_out, F12);
  not not_217 (not_217_out, OP4);
  not not_218 (not_218_out, OP3);
  not not_219 (not_219_out, OP2);
  not not_220 (not_220_out, F30);
  not not_221 (not_221_out, OP6);
  not not_222 (not_222_out, OP3);
  not not_223 (not_223_out, OP2);
  and and_1 (and_1_out, not_1_out, not_2_out, not_3_out, not_4_out, not_5_out, not_6_out, OP5, OP4, not_7_out, not_8_out);
  and and_2 (and_2_out, not_9_out, not_10_out, F14, F13, F12, not_11_out, OP5, OP4, not_12_out, not_13_out);
  and and_3 (and_3_out, not_14_out, not_15_out, not_16_out, F13, not_17_out, not_18_out, OP5, OP4, not_19_out, not_20_out);
  and and_4 (and_4_out, not_21_out, not_22_out, not_23_out, not_24_out, not_25_out, OP4, not_26_out, not_27_out);
  and and_5 (and_5_out, F14, F13, F12, not_28_out, not_29_out, OP4, not_30_out, not_31_out);
  and and_6 (and_6_out, F14, not_32_out, not_33_out, not_34_out, not_35_out, OP4, not_36_out, not_37_out);
  and and_7 (and_7_out, not_38_out, F13, F12, not_39_out, not_40_out, OP4, not_41_out, not_42_out);
  and and_8 (and_8_out, F30, not_43_out, F14, not_44_out, F12, not_45_out, not_46_out, OP4, not_47_out, not_48_out);
  and and_9 (and_9_out, not_49_out, not_50_out, not_51_out, not_52_out, not_53_out);
  and and_10 (and_10_out, not_54_out, F13, not_55_out, not_56_out, OP5, not_57_out, not_58_out, not_59_out);
  and and_11 (and_11_out, not_60_out, not_61_out, not_62_out, OP6, OP5, not_63_out, not_64_out, OP2);
  and and_12 (and_12_out, F14, not_65_out, not_66_out, OP6, OP5, not_67_out, not_68_out, not_69_out);
  and and_13 (and_13_out, F30, not_70_out, not_71_out, not_72_out, not_73_out, not_74_out, OP5, OP4, not_75_out, not_76_out);
  and and_14 (and_14_out, not_77_out, not_78_out, F14, F13, F12, not_79_out, OP5, OP4, not_80_out, not_81_out);
  and and_15 (and_15_out, not_82_out, not_83_out, not_84_out, F13, not_85_out, not_86_out, OP5, OP4, not_87_out, not_88_out);
  and and_16 (and_16_out, F14, F13, F12, not_89_out, not_90_out, OP4, not_91_out, not_92_out);
  and and_17 (and_17_out, not_93_out, F13, F12, not_94_out, not_95_out, OP4, not_96_out, not_97_out);
  and and_18 (and_18_out, not_98_out, not_99_out, F14, not_100_out, F12, not_101_out, not_102_out, OP4, not_103_out, not_104_out);
  and and_19 (and_19_out, F14, not_105_out, not_106_out, OP6, OP5, not_107_out, not_108_out, not_109_out);
  and and_20 (and_20_out, not_110_out, not_111_out, not_112_out, not_113_out, not_114_out, not_115_out, OP5, OP4, not_116_out, not_117_out);
  and and_21 (and_21_out, F30, not_118_out, not_119_out, not_120_out, not_121_out, not_122_out, OP5, OP4, not_123_out, not_124_out);
  and and_22 (and_22_out, not_125_out, not_126_out, F14, F13, F12, not_127_out, OP5, OP4, not_128_out, not_129_out);
  and and_23 (and_23_out, not_130_out, not_131_out, not_132_out, F13, F12, not_133_out, OP5, OP4, not_134_out, not_135_out);
  and and_24 (and_24_out, not_136_out, not_137_out, not_138_out, not_139_out, not_140_out, OP4, not_141_out, not_142_out);
  and and_25 (and_25_out, F14, F13, F12, not_143_out, not_144_out, OP4, not_145_out, not_146_out);
  and and_26 (and_26_out, not_147_out, not_148_out, not_149_out, not_150_out, not_151_out);
  and and_27 (and_27_out, not_152_out, F13, not_153_out, not_154_out, OP5, not_155_out, not_156_out, not_157_out);
  and and_28 (and_28_out, not_158_out, not_159_out, not_160_out, OP6, OP5, not_161_out, not_162_out, OP2);
  and and_29 (and_29_out, not_163_out, F25, F14, not_164_out, F12, not_165_out, OP5, OP4, not_166_out, not_167_out);
  and and_30 (and_30_out, not_168_out, F25, F14, F13, F12, not_169_out, OP5, OP4, not_170_out, not_171_out);
  and and_31 (and_31_out, F14, F13, not_172_out, OP6, OP5, not_173_out, not_174_out, not_175_out);
  and and_32 (and_32_out, not_176_out, not_177_out, F14, F13, not_178_out, not_179_out, OP5, OP4, not_180_out, not_181_out);
  and and_33 (and_33_out, not_182_out, not_183_out, not_184_out, F13, not_185_out, not_186_out, OP5, OP4, not_187_out, not_188_out);
  and and_34 (and_34_out, not_189_out, not_190_out, not_191_out, F13, F12, not_192_out, OP5, OP4, not_193_out, not_194_out);
  and and_35 (and_35_out, F14, F13, not_195_out, not_196_out, not_197_out, OP4, not_198_out, not_199_out);
  and and_36 (and_36_out, F14, not_200_out, not_201_out, not_202_out, not_203_out, OP4, not_204_out, not_205_out);
  and and_37 (and_37_out, not_206_out, F13, F12, not_207_out, not_208_out, OP4, not_209_out, not_210_out);
  and and_38 (and_38_out, F14, F13, not_211_out, OP6, OP5, not_212_out, not_213_out, not_214_out);
  and and_39 (and_39_out, F14, not_215_out, not_216_out, OP6, OP5, not_217_out, not_218_out, not_219_out);
  and and_40 (RE, not_220_out, F25, F14, F13, F12, not_221_out, OP5, OP4, not_222_out, not_223_out);
  or or_1 (S0, and_1_out, and_2_out, and_3_out, and_4_out, and_5_out, and_6_out, and_7_out, and_8_out, and_9_out, and_10_out, and_11_out, and_12_out);
  or or_2 (S1, and_13_out, and_14_out, and_15_out, and_16_out, and_17_out, and_18_out, and_19_out);
  or or_3 (S2, and_20_out, and_21_out, and_22_out, and_23_out, and_24_out, and_25_out, and_26_out, and_27_out, and_28_out, and_29_out, and_30_out, and_31_out);
  or or_4 (S3, and_32_out, and_33_out, and_34_out, and_35_out, and_36_out, and_37_out, and_38_out, and_39_out);
endmodule

// 控制信号生成
module \控制信号自动生成  (
  input  OP2,
  input  OP3,
  input  OP4,
  input  OP5,
  input  OP6,
  input  F12,
  input  F13,
  input  F14,
  input  F25,
  input  F30,
  input  EN,
  output MemToReg,
  output MemWrite,
  output ALU_SRC,
  output RegWrite,
  output ecall,
  output S_Type,
  output BEQ,
  output BNE,
  output JALR,
  output JAL,
  output BLTU,
  output R1Dep,
  output R2Dep,
  output CSR
);

  wire and_4_out, and_5_out, and_6_out, and_7_out, and_8_out, and_9_out, and_10_out, and_11_out, and_12_out,
       and_13_out, and_14_out, and_15_out, and_16_out, and_17_out, and_18_out, and_19_out, and_20_out,
       and_21_out, and_22_out, and_23_out, and_24_out, and_25_out, and_26_out, and_27_out, and_28_out,
       and_29_out, and_30_out, and_31_out, and_32_out, and_33_out, and_39_out, and_40_out, and_41_out,
       and_42_out, and_43_out, and_44_out, and_45_out, and_46_out, and_47_out, and_48_out, and_49_out,
       and_50_out, and_51_out, and_52_out, and_53_out, and_54_out, and_55_out, and_56_out, and_57_out,
       and_58_out, and_59_out, and_60_out, and_61_out, and_62_out, and_63_out, and_64_out, and_65_out,
       and_66_out, and_67_out, and_68_out, and_69_out, and_70_out, and_71_out, and_72_out, and_73_out,
       and_74_out, and_75_out, and_76_out, and_77_out, and_78_out, and_79_out, and_80_out, and_81_out,
       and_82_out, not_1_out, not_2_out, not_3_out, not_4_out, not_5_out, not_6_out, not_7_out, not_8_out,
       not_9_out, not_10_out, not_11_out, not_12_out, not_13_out, not_14_out, not_15_out, not_16_out,
       not_17_out, not_18_out, not_19_out, not_20_out, not_21_out, not_22_out, not_23_out, not_24_out,
       not_25_out, not_26_out, not_27_out, not_28_out, not_29_out, not_30_out, not_31_out, not_32_out,
       not_33_out, not_34_out, not_35_out, not_36_out, not_37_out, not_38_out, not_39_out, not_40_out,
       not_41_out, not_42_out, not_43_out, not_44_out, not_45_out, not_46_out, not_47_out, not_48_out,
       not_49_out, not_50_out, not_51_out, not_52_out, not_53_out, not_54_out, not_55_out, not_56_out,
       not_57_out, not_58_out, not_59_out, not_60_out, not_61_out, not_62_out, not_63_out, not_64_out,
       not_65_out, not_66_out, not_67_out, not_68_out, not_69_out, not_70_out, not_71_out, not_72_out,
       not_73_out, not_74_out, not_75_out, not_76_out, not_77_out, not_78_out, not_79_out, not_80_out,
       not_81_out, not_82_out, not_83_out, not_84_out, not_85_out, not_86_out, not_87_out, not_88_out,
       not_89_out, not_90_out, not_91_out, not_92_out, not_93_out, not_94_out, not_95_out, not_96_out,
       not_97_out, not_98_out, not_99_out, not_100_out, not_101_out, not_102_out, not_103_out, not_104_out,
       not_105_out, not_106_out, not_107_out, not_108_out, not_109_out, not_110_out, not_111_out,
       not_112_out, not_113_out, not_114_out, not_115_out, not_116_out, not_117_out, not_118_out,
       not_119_out, not_120_out, not_121_out, not_122_out, not_123_out, not_124_out, not_125_out,
       not_126_out, not_127_out, not_128_out, not_129_out, not_130_out, not_131_out, not_132_out,
       not_133_out, not_134_out, not_135_out, not_136_out, not_137_out, not_138_out, not_139_out,
       not_140_out, not_141_out, not_142_out, not_143_out, not_144_out, not_145_out, not_146_out,
       not_147_out, not_148_out, not_149_out, not_150_out, not_151_out, not_152_out, not_153_out,
       not_154_out, not_155_out, not_156_out, not_157_out, not_158_out, not_159_out, not_160_out,
       not_161_out, not_162_out, not_163_out, not_164_out, not_165_out, not_166_out, not_167_out,
       not_168_out, not_169_out, not_170_out, not_171_out, not_172_out, not_173_out, not_174_out,
       not_175_out, not_176_out, not_177_out, not_178_out, not_179_out, not_180_out, not_181_out,
       not_182_out, not_183_out, not_184_out, not_185_out, not_186_out, not_187_out, not_188_out,
       not_189_out, not_190_out, not_191_out, not_192_out, not_193_out, not_194_out, not_195_out,
       not_196_out, not_197_out, not_198_out, not_199_out, not_200_out, not_201_out, not_202_out,
       not_203_out, not_204_out, not_205_out, not_206_out, not_207_out, not_208_out, not_209_out,
       not_210_out, not_211_out, not_212_out, not_213_out, not_214_out, not_215_out, not_216_out,
       not_217_out, not_218_out, not_219_out, not_220_out, not_221_out, not_222_out, not_223_out,
       not_224_out, not_225_out, not_226_out, not_227_out, not_228_out, not_229_out, not_230_out,
       not_231_out, not_232_out, not_233_out, not_234_out, not_235_out, not_236_out, not_237_out,
       not_238_out, not_239_out, not_240_out, not_241_out, not_242_out, not_243_out, not_244_out,
       not_245_out, not_246_out, not_247_out, not_248_out, not_249_out, not_250_out, not_251_out,
       not_252_out, not_253_out, not_254_out, not_255_out, not_256_out, not_257_out, not_258_out,
       not_259_out, not_260_out, not_261_out, not_262_out, not_263_out, not_264_out, not_265_out,
       not_266_out, not_267_out, not_268_out, not_269_out, not_270_out, not_271_out, not_272_out,
       not_273_out, not_274_out, not_275_out, not_276_out, not_277_out, not_278_out, not_279_out,
       not_280_out, not_281_out, not_282_out, not_283_out, not_284_out, not_285_out, not_286_out,
       not_287_out, not_288_out, not_289_out, not_290_out, not_291_out, not_292_out, not_293_out,
       not_294_out, not_295_out, not_296_out, not_297_out, not_298_out, not_299_out, not_300_out,
       not_301_out, not_302_out, not_303_out, not_304_out, not_305_out, not_306_out, not_307_out,
       not_308_out, not_309_out, not_310_out, not_311_out, not_312_out, not_313_out, not_314_out,
       not_315_out, not_316_out, not_317_out, not_318_out, not_319_out, not_320_out, not_321_out,
       not_322_out, not_323_out, not_324_out, not_325_out, not_326_out, not_327_out, not_328_out,
       not_329_out, not_330_out, not_331_out, not_332_out, not_333_out, not_334_out, not_335_out,
       not_336_out, not_337_out, not_338_out, not_339_out, not_340_out, not_341_out, not_342_out,
       not_343_out, not_344_out, not_345_out, not_346_out, not_347_out, not_348_out, not_349_out,
       not_350_out, not_351_out, not_352_out, not_353_out, not_354_out, not_355_out, not_356_out,
       not_357_out, not_358_out, not_359_out, not_360_out, not_361_out, not_362_out, not_363_out,
       not_364_out, not_365_out, not_366_out, not_367_out, not_368_out, not_369_out, not_370_out,
       not_371_out, not_372_out, not_373_out, not_374_out, not_375_out, not_376_out, not_377_out,
       not_378_out, not_379_out, not_380_out, not_381_out, not_382_out, not_383_out, not_384_out,
       not_385_out, not_386_out, not_387_out, not_388_out, not_389_out, not_390_out, not_391_out,
       not_392_out, not_393_out, not_394_out, not_395_out, not_396_out, not_397_out, not_398_out,
       not_399_out, not_400_out, not_401_out, not_402_out, not_403_out, not_404_out, not_405_out,
       not_406_out, not_407_out, not_408_out, not_409_out, not_410_out, not_411_out, not_412_out,
       not_413_out, not_414_out, not_415_out, not_416_out, not_417_out, not_418_out, not_419_out,
       not_420_out, not_421_out, not_422_out, not_423_out, not_424_out, not_425_out, not_426_out,
       not_427_out, not_428_out, not_429_out, not_430_out, not_431_out, not_432_out, not_433_out,
       not_434_out, not_435_out, not_436_out, not_437_out, not_438_out, not_439_out, not_440_out,
       not_441_out, not_442_out, not_443_out, not_444_out, not_445_out, or_1_out, or_2_out, or_3_out,
       or_4_out, or_5_out, or_6_out;

  not not_1 (not_1_out, OP6);
  not not_2 (not_2_out, OP5);
  not not_3 (not_3_out, OP4);
  not not_4 (not_4_out, OP3);
  not not_5 (not_5_out, OP2);
  not not_6 (not_6_out, F14);
  not not_7 (not_7_out, F12);
  not not_8 (not_8_out, OP6);
  not not_9 (not_9_out, OP4);
  not not_10 (not_10_out, OP3);
  not not_11 (not_11_out, OP2);
  not not_12 (not_12_out, F14);
  not not_13 (not_13_out, F13);
  not not_14 (not_14_out, F12);
  not not_15 (not_15_out, OP6);
  not not_16 (not_16_out, OP5);
  not not_17 (not_17_out, OP3);
  not not_18 (not_18_out, OP2);
  not not_19 (not_19_out, OP6);
  not not_20 (not_20_out, OP5);
  not not_21 (not_21_out, OP3);
  not not_22 (not_22_out, OP2);
  not not_23 (not_23_out, F12);
  not not_24 (not_24_out, OP6);
  not not_25 (not_25_out, OP5);
  not not_26 (not_26_out, OP3);
  not not_27 (not_27_out, OP2);
  not not_28 (not_28_out, F13);
  not not_29 (not_29_out, F12);
  not not_30 (not_30_out, OP6);
  not not_31 (not_31_out, OP5);
  not not_32 (not_32_out, OP3);
  not not_33 (not_33_out, OP2);
  not not_34 (not_34_out, F14);
  not not_35 (not_35_out, OP6);
  not not_36 (not_36_out, OP5);
  not not_37 (not_37_out, OP3);
  not not_38 (not_38_out, OP2);
  not not_39 (not_39_out, F14);
  not not_40 (not_40_out, F13);
  not not_41 (not_41_out, OP6);
  not not_42 (not_42_out, OP5);
  not not_43 (not_43_out, OP3);
  not not_44 (not_44_out, OP2);
  not not_45 (not_45_out, F30);
  not not_46 (not_46_out, F25);
  not not_47 (not_47_out, F13);
  not not_48 (not_48_out, OP6);
  not not_49 (not_49_out, OP5);
  not not_50 (not_50_out, OP3);
  not not_51 (not_51_out, OP2);
  not not_52 (not_52_out, F25);
  not not_53 (not_53_out, F13);
  not not_54 (not_54_out, OP6);
  not not_55 (not_55_out, OP5);
  not not_56 (not_56_out, OP3);
  not not_57 (not_57_out, OP2);
  not not_58 (not_58_out, F14);
  not not_59 (not_59_out, F12);
  not not_60 (not_60_out, OP6);
  not not_61 (not_61_out, OP4);
  not not_62 (not_62_out, OP3);
  not not_63 (not_63_out, OP2);
  not not_64 (not_64_out, F14);
  not not_65 (not_65_out, F13);
  not not_66 (not_66_out, F12);
  not not_67 (not_67_out, OP4);
  not not_68 (not_68_out, OP3);
  not not_69 (not_69_out, F30);
  not not_70 (not_70_out, F25);
  not not_71 (not_71_out, F14);
  not not_72 (not_72_out, F13);
  not not_73 (not_73_out, F12);
  not not_74 (not_74_out, OP6);
  not not_75 (not_75_out, OP3);
  not not_76 (not_76_out, OP2);
  not not_77 (not_77_out, F25);
  not not_78 (not_78_out, F14);
  not not_79 (not_79_out, F13);
  not not_80 (not_80_out, F12);
  not not_81 (not_81_out, OP6);
  not not_82 (not_82_out, OP3);
  not not_83 (not_83_out, OP2);
  not not_84 (not_84_out, F30);
  not not_85 (not_85_out, F25);
  not not_86 (not_86_out, OP6);
  not not_87 (not_87_out, OP3);
  not not_88 (not_88_out, OP2);
  not not_89 (not_89_out, F30);
  not not_90 (not_90_out, F25);
  not not_91 (not_91_out, F12);
  not not_92 (not_92_out, OP6);
  not not_93 (not_93_out, OP3);
  not not_94 (not_94_out, OP2);
  not not_95 (not_95_out, F30);
  not not_96 (not_96_out, F25);
  not not_97 (not_97_out, F14);
  not not_98 (not_98_out, F12);
  not not_99 (not_99_out, OP6);
  not not_100 (not_100_out, OP3);
  not not_101 (not_101_out, OP2);
  not not_102 (not_102_out, F30);
  not not_103 (not_103_out, F25);
  not not_104 (not_104_out, F14);
  not not_105 (not_105_out, OP6);
  not not_106 (not_106_out, OP3);
  not not_107 (not_107_out, OP2);
  not not_108 (not_108_out, F14);
  not not_109 (not_109_out, F13);
  not not_110 (not_110_out, F12);
  not not_111 (not_111_out, OP6);
  not not_112 (not_112_out, OP5);
  not not_113 (not_113_out, OP3);
  not not_114 (not_114_out, OP2);
  not not_115 (not_115_out, OP6);
  not not_116 (not_116_out, OP5);
  not not_117 (not_117_out, OP3);
  not not_118 (not_118_out, OP2);
  not not_119 (not_119_out, F12);
  not not_120 (not_120_out, OP6);
  not not_121 (not_121_out, OP5);
  not not_122 (not_122_out, OP3);
  not not_123 (not_123_out, OP2);
  not not_124 (not_124_out, F13);
  not not_125 (not_125_out, F12);
  not not_126 (not_126_out, OP6);
  not not_127 (not_127_out, OP5);
  not not_128 (not_128_out, OP3);
  not not_129 (not_129_out, OP2);
  not not_130 (not_130_out, F14);
  not not_131 (not_131_out, OP6);
  not not_132 (not_132_out, OP5);
  not not_133 (not_133_out, OP3);
  not not_134 (not_134_out, OP2);
  not not_135 (not_135_out, F14);
  not not_136 (not_136_out, F13);
  not not_137 (not_137_out, OP6);
  not not_138 (not_138_out, OP5);
  not not_139 (not_139_out, OP3);
  not not_140 (not_140_out, OP2);
  not not_141 (not_141_out, F30);
  not not_142 (not_142_out, F25);
  not not_143 (not_143_out, F13);
  not not_144 (not_144_out, OP6);
  not not_145 (not_145_out, OP5);
  not not_146 (not_146_out, OP3);
  not not_147 (not_147_out, OP2);
  not not_148 (not_148_out, F25);
  not not_149 (not_149_out, F13);
  not not_150 (not_150_out, OP6);
  not not_151 (not_151_out, OP5);
  not not_152 (not_152_out, OP3);
  not not_153 (not_153_out, OP2);
  not not_154 (not_154_out, F14);
  not not_155 (not_155_out, F13);
  not not_156 (not_156_out, F12);
  not not_157 (not_157_out, OP4);
  not not_158 (not_158_out, OP3);
  not not_159 (not_159_out, F30);
  not not_160 (not_160_out, F13);
  not not_161 (not_161_out, OP6);
  not not_162 (not_162_out, OP3);
  not not_163 (not_163_out, OP2);
  not not_164 (not_164_out, F30);
  not not_165 (not_165_out, OP6);
  not not_166 (not_166_out, OP3);
  not not_167 (not_167_out, OP2);
  not not_168 (not_168_out, F30);
  not not_169 (not_169_out, F25);
  not not_170 (not_170_out, F14);
  not not_171 (not_171_out, F13);
  not not_172 (not_172_out, F12);
  not not_173 (not_173_out, OP3);
  not not_174 (not_174_out, OP2);
  not not_175 (not_175_out, F14);
  not not_176 (not_176_out, F12);
  not not_177 (not_177_out, OP6);
  not not_178 (not_178_out, OP4);
  not not_179 (not_179_out, OP3);
  not not_180 (not_180_out, OP2);
  not not_181 (not_181_out, OP2);
  not not_182 (not_182_out, OP3);
  not not_183 (not_183_out, OP4);
  not not_184 (not_184_out, F12);
  not not_185 (not_185_out, F13);
  not not_186 (not_186_out, F14);
  not not_187 (not_187_out, OP2);
  not not_188 (not_188_out, OP3);
  not not_189 (not_189_out, OP4);
  not not_190 (not_190_out, F13);
  not not_191 (not_191_out, F14);
  not not_192 (not_192_out, OP3);
  not not_193 (not_193_out, OP4);
  not not_194 (not_194_out, F12);
  not not_195 (not_195_out, F13);
  not not_196 (not_196_out, F14);
  not not_197 (not_197_out, OP4);
  not not_198 (not_198_out, F12);
  not not_199 (not_199_out, OP4);
  not not_200 (not_200_out, OP3);
  not not_201 (not_201_out, OP2);
  not not_202 (not_202_out, F13);
  not not_203 (not_203_out, F12);
  not not_204 (not_204_out, OP4);
  not not_205 (not_205_out, OP3);
  not not_206 (not_206_out, OP2);
  not not_207 (not_207_out, F30);
  not not_208 (not_208_out, F25);
  not not_209 (not_209_out, F14);
  not not_210 (not_210_out, F13);
  not not_211 (not_211_out, F12);
  not not_212 (not_212_out, OP6);
  not not_213 (not_213_out, OP3);
  not not_214 (not_214_out, OP2);
  not not_215 (not_215_out, F25);
  not not_216 (not_216_out, F14);
  not not_217 (not_217_out, F13);
  not not_218 (not_218_out, F12);
  not not_219 (not_219_out, OP6);
  not not_220 (not_220_out, OP3);
  not not_221 (not_221_out, OP2);
  not not_222 (not_222_out, F30);
  not not_223 (not_223_out, F25);
  not not_224 (not_224_out, OP6);
  not not_225 (not_225_out, OP3);
  not not_226 (not_226_out, OP2);
  not not_227 (not_227_out, F30);
  not not_228 (not_228_out, F25);
  not not_229 (not_229_out, F12);
  not not_230 (not_230_out, OP6);
  not not_231 (not_231_out, OP3);
  not not_232 (not_232_out, OP2);
  not not_233 (not_233_out, F30);
  not not_234 (not_234_out, F25);
  not not_235 (not_235_out, F14);
  not not_236 (not_236_out, F12);
  not not_237 (not_237_out, OP6);
  not not_238 (not_238_out, OP3);
  not not_239 (not_239_out, OP2);
  not not_240 (not_240_out, F30);
  not not_241 (not_241_out, F25);
  not not_242 (not_242_out, F14);
  not not_243 (not_243_out, OP6);
  not not_244 (not_244_out, OP3);
  not not_245 (not_245_out, OP2);
  not not_246 (not_246_out, F14);
  not not_247 (not_247_out, F13);
  not not_248 (not_248_out, F12);
  not not_249 (not_249_out, OP6);
  not not_250 (not_250_out, OP5);
  not not_251 (not_251_out, OP3);
  not not_252 (not_252_out, OP2);
  not not_253 (not_253_out, OP6);
  not not_254 (not_254_out, OP5);
  not not_255 (not_255_out, OP3);
  not not_256 (not_256_out, OP2);
  not not_257 (not_257_out, F12);
  not not_258 (not_258_out, OP6);
  not not_259 (not_259_out, OP5);
  not not_260 (not_260_out, OP3);
  not not_261 (not_261_out, OP2);
  not not_262 (not_262_out, F13);
  not not_263 (not_263_out, F12);
  not not_264 (not_264_out, OP6);
  not not_265 (not_265_out, OP5);
  not not_266 (not_266_out, OP3);
  not not_267 (not_267_out, OP2);
  not not_268 (not_268_out, F14);
  not not_269 (not_269_out, OP6);
  not not_270 (not_270_out, OP5);
  not not_271 (not_271_out, OP3);
  not not_272 (not_272_out, OP2);
  not not_273 (not_273_out, F14);
  not not_274 (not_274_out, F13);
  not not_275 (not_275_out, OP6);
  not not_276 (not_276_out, OP5);
  not not_277 (not_277_out, OP3);
  not not_278 (not_278_out, OP2);
  not not_279 (not_279_out, F30);
  not not_280 (not_280_out, F25);
  not not_281 (not_281_out, F13);
  not not_282 (not_282_out, OP6);
  not not_283 (not_283_out, OP5);
  not not_284 (not_284_out, OP3);
  not not_285 (not_285_out, OP2);
  not not_286 (not_286_out, F25);
  not not_287 (not_287_out, F13);
  not not_288 (not_288_out, OP6);
  not not_289 (not_289_out, OP5);
  not not_290 (not_290_out, OP3);
  not not_291 (not_291_out, OP2);
  not not_292 (not_292_out, F14);
  not not_293 (not_293_out, F12);
  not not_294 (not_294_out, OP6);
  not not_295 (not_295_out, OP4);
  not not_296 (not_296_out, OP3);
  not not_297 (not_297_out, OP2);
  not not_298 (not_298_out, F30);
  not not_299 (not_299_out, F25);
  not not_300 (not_300_out, F14);
  not not_301 (not_301_out, F13);
  not not_302 (not_302_out, F12);
  not not_303 (not_303_out, OP3);
  not not_304 (not_304_out, OP2);
  not not_305 (not_305_out, F14);
  not not_306 (not_306_out, F13);
  not not_307 (not_307_out, F12);
  not not_308 (not_308_out, OP4);
  not not_309 (not_309_out, OP3);
  not not_310 (not_310_out, OP2);
  not not_311 (not_311_out, F14);
  not not_312 (not_312_out, F13);
  not not_313 (not_313_out, OP4);
  not not_314 (not_314_out, OP3);
  not not_315 (not_315_out, OP2);
  not not_316 (not_316_out, F14);
  not not_317 (not_317_out, F13);
  not not_318 (not_318_out, F12);
  not not_319 (not_319_out, OP4);
  not not_320 (not_320_out, OP3);
  not not_321 (not_321_out, F12);
  not not_322 (not_322_out, OP3);
  not not_323 (not_323_out, OP2);
  not not_324 (not_324_out, OP3);
  not not_325 (not_325_out, OP2);
  not not_326 (not_326_out, F30);
  not not_327 (not_327_out, F13);
  not not_328 (not_328_out, OP6);
  not not_329 (not_329_out, OP3);
  not not_330 (not_330_out, OP2);
  not not_331 (not_331_out, F30);
  not not_332 (not_332_out, OP6);
  not not_333 (not_333_out, OP3);
  not not_334 (not_334_out, OP2);
  not not_335 (not_335_out, F12);
  not not_336 (not_336_out, OP4);
  not not_337 (not_337_out, OP3);
  not not_338 (not_338_out, OP2);
  not not_339 (not_339_out, F13);
  not not_340 (not_340_out, F12);
  not not_341 (not_341_out, OP4);
  not not_342 (not_342_out, OP3);
  not not_343 (not_343_out, OP2);
  not not_344 (not_344_out, F30);
  not not_345 (not_345_out, F25);
  not not_346 (not_346_out, F14);
  not not_347 (not_347_out, F13);
  not not_348 (not_348_out, F12);
  not not_349 (not_349_out, OP6);
  not not_350 (not_350_out, OP3);
  not not_351 (not_351_out, OP2);
  not not_352 (not_352_out, F25);
  not not_353 (not_353_out, F14);
  not not_354 (not_354_out, F13);
  not not_355 (not_355_out, F12);
  not not_356 (not_356_out, OP6);
  not not_357 (not_357_out, OP3);
  not not_358 (not_358_out, OP2);
  not not_359 (not_359_out, F30);
  not not_360 (not_360_out, F25);
  not not_361 (not_361_out, OP6);
  not not_362 (not_362_out, OP3);
  not not_363 (not_363_out, OP2);
  not not_364 (not_364_out, F30);
  not not_365 (not_365_out, F25);
  not not_366 (not_366_out, F12);
  not not_367 (not_367_out, OP6);
  not not_368 (not_368_out, OP3);
  not not_369 (not_369_out, OP2);
  not not_370 (not_370_out, F30);
  not not_371 (not_371_out, F25);
  not not_372 (not_372_out, F14);
  not not_373 (not_373_out, F12);
  not not_374 (not_374_out, OP6);
  not not_375 (not_375_out, OP3);
  not not_376 (not_376_out, OP2);
  not not_377 (not_377_out, F30);
  not not_378 (not_378_out, F25);
  not not_379 (not_379_out, F14);
  not not_380 (not_380_out, OP6);
  not not_381 (not_381_out, OP3);
  not not_382 (not_382_out, OP2);
  not not_383 (not_383_out, F14);
  not not_384 (not_384_out, F12);
  not not_385 (not_385_out, OP6);
  not not_386 (not_386_out, OP4);
  not not_387 (not_387_out, OP3);
  not not_388 (not_388_out, OP2);
  not not_389 (not_389_out, F30);
  not not_390 (not_390_out, F25);
  not not_391 (not_391_out, F14);
  not not_392 (not_392_out, F13);
  not not_393 (not_393_out, F12);
  not not_394 (not_394_out, OP3);
  not not_395 (not_395_out, OP2);
  not not_396 (not_396_out, F14);
  not not_397 (not_397_out, F13);
  not not_398 (not_398_out, F12);
  not not_399 (not_399_out, OP4);
  not not_400 (not_400_out, OP3);
  not not_401 (not_401_out, OP2);
  not not_402 (not_402_out, F14);
  not not_403 (not_403_out, F13);
  not not_404 (not_404_out, OP4);
  not not_405 (not_405_out, OP3);
  not not_406 (not_406_out, OP2);
  not not_407 (not_407_out, F30);
  not not_408 (not_408_out, F13);
  not not_409 (not_409_out, OP6);
  not not_410 (not_410_out, OP3);
  not not_411 (not_411_out, OP2);
  not not_412 (not_412_out, F30);
  not not_413 (not_413_out, OP6);
  not not_414 (not_414_out, OP3);
  not not_415 (not_415_out, OP2);
  not not_416 (not_416_out, F12);
  not not_417 (not_417_out, OP4);
  not not_418 (not_418_out, OP3);
  not not_419 (not_419_out, OP2);
  not not_420 (not_420_out, F13);
  not not_421 (not_421_out, F12);
  not not_422 (not_422_out, OP4);
  not not_423 (not_423_out, OP3);
  not not_424 (not_424_out, OP2);
  not not_425 (not_425_out, F12);
  not not_426 (not_426_out, OP3);
  not not_427 (not_427_out, OP2);
  not not_428 (not_428_out, OP3);
  not not_429 (not_429_out, OP2);
  and and_1 (MemToReg, not_1_out, not_2_out, not_3_out, not_4_out, not_5_out, EN);
  not not_430 (not_430_out, OP6);
  not not_431 (not_431_out, OP5);
  not not_432 (not_432_out, OP4);
  not not_433 (not_433_out, OP3);
  not not_434 (not_434_out, OP2);
  not not_435 (not_435_out, OP6);
  not not_436 (not_436_out, OP5);
  not not_437 (not_437_out, OP4);
  not not_438 (not_438_out, OP3);
  not not_439 (not_439_out, OP2);
  not not_440 (not_440_out, OP4);
  and and_2 (JAL, OP2, OP3, not_197_out, OP5, OP6, EN);
  not not_441 (not_441_out, OP6);
  not not_442 (not_442_out, OP5);
  not not_443 (not_443_out, OP4);
  not not_444 (not_444_out, OP3);
  not not_445 (not_445_out, OP2);
  and and_3 (MemWrite, not_6_out, F13, not_7_out, not_8_out, OP5, not_9_out, not_10_out, not_11_out, EN);
  and and_4 (and_4_out, not_12_out, not_13_out, not_14_out, not_15_out, not_16_out, OP4, not_17_out, not_18_out);
  and and_5 (and_5_out, F14, F13, F12, not_19_out, not_20_out, OP4, not_21_out, not_22_out);
  and and_6 (and_6_out, F14, F13, not_23_out, not_24_out, not_25_out, OP4, not_26_out, not_27_out);
  and and_7 (and_7_out, F14, not_28_out, not_29_out, not_30_out, not_31_out, OP4, not_32_out, not_33_out);
  and and_8 (and_8_out, not_34_out, F13, F12, not_35_out, not_36_out, OP4, not_37_out, not_38_out);
  and and_9 (and_9_out, not_39_out, not_40_out, F12, not_41_out, not_42_out, OP4, not_43_out, not_44_out);
  and and_10 (and_10_out, not_45_out, not_46_out, F14, not_47_out, F12, not_48_out, not_49_out, OP4, not_50_out, not_51_out);
  and and_11 (and_11_out, F30, not_52_out, F14, not_53_out, F12, not_54_out, not_55_out, OP4, not_56_out, not_57_out);
  and and_12 (and_12_out, not_430_out, not_431_out, not_432_out, not_433_out, not_434_out);
  and and_13 (and_13_out, not_58_out, F13, not_59_out, not_60_out, OP5, not_61_out, not_62_out, not_63_out);
  and and_14 (and_14_out, not_64_out, not_65_out, not_66_out, OP6, OP5, not_67_out, not_68_out, OP2);
  and and_15 (and_15_out, not_69_out, not_70_out, not_71_out, not_72_out, not_73_out, not_74_out, OP5, OP4, not_75_out, not_76_out);
  and and_16 (and_16_out, F30, not_77_out, not_78_out, not_79_out, not_80_out, not_81_out, OP5, OP4, not_82_out, not_83_out);
  and and_17 (and_17_out, not_84_out, not_85_out, F14, F13, F12, not_86_out, OP5, OP4, not_87_out, not_88_out);
  and and_18 (and_18_out, not_89_out, not_90_out, F14, F13, not_91_out, not_92_out, OP5, OP4, not_93_out, not_94_out);
  and and_19 (and_19_out, not_95_out, not_96_out, not_97_out, F13, not_98_out, not_99_out, OP5, OP4, not_100_out, not_101_out);
  and and_20 (and_20_out, not_102_out, not_103_out, not_104_out, F13, F12, not_105_out, OP5, OP4, not_106_out, not_107_out);
  and and_21 (and_21_out, not_108_out, not_109_out, not_110_out, not_111_out, not_112_out, OP4, not_113_out, not_114_out);
  and and_22 (and_22_out, F14, F13, F12, not_115_out, not_116_out, OP4, not_117_out, not_118_out);
  and and_23 (and_23_out, F14, F13, not_119_out, not_120_out, not_121_out, OP4, not_122_out, not_123_out);
  and and_24 (and_24_out, F14, not_124_out, not_125_out, not_126_out, not_127_out, OP4, not_128_out, not_129_out);
  and and_25 (and_25_out, not_130_out, F13, F12, not_131_out, not_132_out, OP4, not_133_out, not_134_out);
  and and_26 (and_26_out, not_135_out, not_136_out, F12, not_137_out, not_138_out, OP4, not_139_out, not_140_out);
  and and_27 (and_27_out, not_141_out, not_142_out, F14, not_143_out, F12, not_144_out, not_145_out, OP4, not_146_out, not_147_out);
  and and_28 (and_28_out, F30, not_148_out, F14, not_149_out, F12, not_150_out, not_151_out, OP4, not_152_out, not_153_out);
  and and_29 (and_29_out, not_435_out, not_436_out, not_437_out, not_438_out, not_439_out);
  and and_30 (and_30_out, OP6, OP5, not_440_out, OP3, OP2);
  and and_31 (and_31_out, not_154_out, not_155_out, not_156_out, OP6, OP5, not_157_out, not_158_out, OP2);
  and and_32 (and_32_out, not_159_out, F25, F14, not_160_out, F12, not_161_out, OP5, OP4, not_162_out, not_163_out);
  and and_33 (and_33_out, not_164_out, F25, F14, F13, F12, not_165_out, OP5, OP4, not_166_out, not_167_out);
  and and_34 (ecall, not_168_out, not_169_out, not_170_out, not_171_out, not_172_out, OP6, OP5, OP4, not_173_out, not_174_out, EN);
  and and_35 (S_Type, not_175_out, F13, not_176_out, not_177_out, OP5, not_178_out, not_179_out, not_180_out, EN);
  and and_36 (BEQ, not_181_out, not_182_out, not_183_out, OP5, OP6, not_184_out, not_185_out, not_186_out, EN);
  and and_37 (BNE, not_187_out, not_188_out, not_189_out, OP5, OP6, F12, not_190_out, not_191_out, EN);
  and and_38 (JALR, OP2, not_192_out, not_193_out, OP5, OP6, not_194_out, not_195_out, not_196_out, EN);
  and and_39 (and_39_out, F14, F13, not_198_out, OP6, OP5, not_199_out, not_200_out, not_201_out);
  or or_1 (or_1_out, and_39_out, and_40_out);
  and and_40 (and_40_out, F14, not_202_out, not_203_out, OP6, OP5, not_204_out, not_205_out, not_206_out);
  and and_41 (and_41_out, not_207_out, not_208_out, not_209_out, not_210_out, not_211_out, not_212_out, OP5, OP4, not_213_out, not_214_out);
  and and_42 (and_42_out, F30, not_215_out, not_216_out, not_217_out, not_218_out, not_219_out, OP5, OP4, not_220_out, not_221_out);
  and and_43 (and_43_out, not_222_out, not_223_out, F14, F13, F12, not_224_out, OP5, OP4, not_225_out, not_226_out);
  and and_44 (and_44_out, not_227_out, not_228_out, F14, F13, not_229_out, not_230_out, OP5, OP4, not_231_out, not_232_out);
  and and_45 (and_45_out, not_233_out, not_234_out, not_235_out, F13, not_236_out, not_237_out, OP5, OP4, not_238_out, not_239_out);
  and and_46 (and_46_out, not_240_out, not_241_out, not_242_out, F13, F12, not_243_out, OP5, OP4, not_244_out, not_245_out);
  and and_47 (and_47_out, not_246_out, not_247_out, not_248_out, not_249_out, not_250_out, OP4, not_251_out, not_252_out);
  and and_48 (and_48_out, F14, F13, F12, not_253_out, not_254_out, OP4, not_255_out, not_256_out);
  and and_49 (and_49_out, F14, F13, not_257_out, not_258_out, not_259_out, OP4, not_260_out, not_261_out);
  and and_50 (and_50_out, F14, not_262_out, not_263_out, not_264_out, not_265_out, OP4, not_266_out, not_267_out);
  and and_51 (and_51_out, not_268_out, F13, F12, not_269_out, not_270_out, OP4, not_271_out, not_272_out);
  and and_52 (and_52_out, not_273_out, not_274_out, F12, not_275_out, not_276_out, OP4, not_277_out, not_278_out);
  and and_53 (and_53_out, not_279_out, not_280_out, F14, not_281_out, F12, not_282_out, not_283_out, OP4, not_284_out, not_285_out);
  and and_54 (and_54_out, F30, not_286_out, F14, not_287_out, F12, not_288_out, not_289_out, OP4, not_290_out, not_291_out);
  and and_55 (and_55_out, not_441_out, not_442_out, not_443_out, not_444_out, not_445_out);
  and and_56 (and_56_out, not_292_out, F13, not_293_out, not_294_out, OP5, not_295_out, not_296_out, not_297_out);
  and and_57 (and_57_out, not_298_out, not_299_out, not_300_out, not_301_out, not_302_out, OP6, OP5, OP4, not_303_out, not_304_out);
  and and_58 (and_58_out, not_305_out, not_306_out, not_307_out, OP6, OP5, not_308_out, not_309_out, not_310_out);
  and and_59 (and_59_out, not_311_out, not_312_out, F12, OP6, OP5, not_313_out, not_314_out, not_315_out);
  and and_60 (and_60_out, not_316_out, not_317_out, not_318_out, OP6, OP5, not_319_out, not_320_out, OP2);
  and and_61 (and_61_out, F14, F13, not_321_out, OP6, OP5, OP4, not_322_out, not_323_out);
  and and_62 (and_62_out, F14, F13, F12, OP6, OP5, OP4, not_324_out, not_325_out);
  and and_63 (and_63_out, not_326_out, F25, F14, not_327_out, F12, not_328_out, OP5, OP4, not_329_out, not_330_out);
  and and_64 (and_64_out, not_331_out, F25, F14, F13, F12, not_332_out, OP5, OP4, not_333_out, not_334_out);
  and and_65 (and_65_out, F14, F13, not_335_out, OP6, OP5, not_336_out, not_337_out, not_338_out);
  and and_66 (and_66_out, F14, not_339_out, not_340_out, OP6, OP5, not_341_out, not_342_out, not_343_out);
  and and_67 (and_67_out, not_344_out, not_345_out, not_346_out, not_347_out, not_348_out, not_349_out, OP5, OP4, not_350_out, not_351_out);
  and and_68 (and_68_out, F30, not_352_out, not_353_out, not_354_out, not_355_out, not_356_out, OP5, OP4, not_357_out, not_358_out);
  and and_69 (and_69_out, not_359_out, not_360_out, F14, F13, F12, not_361_out, OP5, OP4, not_362_out, not_363_out);
  and and_70 (and_70_out, not_364_out, not_365_out, F14, F13, not_366_out, not_367_out, OP5, OP4, not_368_out, not_369_out);
  and and_71 (and_71_out, not_370_out, not_371_out, not_372_out, F13, not_373_out, not_374_out, OP5, OP4, not_375_out, not_376_out);
  and and_72 (and_72_out, not_377_out, not_378_out, not_379_out, F13, F12, not_380_out, OP5, OP4, not_381_out, not_382_out);
  and and_73 (and_73_out, not_383_out, F13, not_384_out, not_385_out, OP5, not_386_out, not_387_out, not_388_out);
  and and_74 (and_74_out, not_389_out, not_390_out, not_391_out, not_392_out, not_393_out, OP6, OP5, OP4, not_394_out, not_395_out);
  and and_75 (and_75_out, not_396_out, not_397_out, not_398_out, OP6, OP5, not_399_out, not_400_out, not_401_out);
  and and_76 (and_76_out, not_402_out, not_403_out, F12, OP6, OP5, not_404_out, not_405_out, not_406_out);
  and and_77 (and_77_out, not_407_out, F25, F14, not_408_out, F12, not_409_out, OP5, OP4, not_410_out, not_411_out);
  and and_78 (and_78_out, not_412_out, F25, F14, F13, F12, not_413_out, OP5, OP4, not_414_out, not_415_out);
  and and_79 (and_79_out, F14, F13, not_416_out, OP6, OP5, not_417_out, not_418_out, not_419_out);
  and and_80 (and_80_out, F14, not_420_out, not_421_out, OP6, OP5, not_422_out, not_423_out, not_424_out);
  and and_81 (and_81_out, F14, F13, not_425_out, OP6, OP5, OP4, not_426_out, not_427_out);
  or or_2 (or_2_out, and_81_out, and_82_out);
  and and_82 (and_82_out, F14, F13, F12, OP6, OP5, OP4, not_428_out, not_429_out);
  or or_3 (or_3_out, and_4_out, and_5_out, and_6_out, and_7_out, and_8_out, and_9_out, and_10_out, and_11_out, and_12_out, and_13_out, and_14_out);
  and and_83 (BLTU, EN, or_1_out);
  or or_4 (or_4_out, and_67_out, and_68_out, and_69_out, and_70_out, and_71_out, and_72_out, and_73_out, and_74_out, and_75_out, and_76_out, and_77_out, and_78_out, and_79_out, and_80_out);
  and and_84 (CSR, or_2_out, EN);
  and and_85 (ALU_SRC, EN, or_3_out);
  and and_86 (RegWrite, EN, or_5_out);
  or or_5 (or_5_out, and_15_out, and_16_out, and_17_out, and_18_out, and_19_out, and_20_out, and_21_out, and_22_out, and_23_out, and_24_out, and_25_out, and_26_out, and_27_out, and_28_out, and_29_out, and_30_out, and_31_out, and_32_out, and_33_out);
  or or_6 (or_6_out, and_41_out, and_42_out, and_43_out, and_44_out, and_45_out, and_46_out, and_47_out, and_48_out, and_49_out, and_50_out, and_51_out, and_52_out, and_53_out, and_54_out, and_55_out, and_56_out, and_57_out, and_58_out, and_59_out, and_60_out, and_61_out, and_62_out, and_63_out, and_64_out, and_65_out, and_66_out);
  and and_87 (R2Dep, EN, or_4_out);
  and and_88 (R1Dep, EN, or_6_out);
endmodule

// ALU
module ALU (
  input  [31:0] X,
  input  [31:0] Y,
  input  [3:0] AluOP,
  output out_4,
  output Equal,
  output out_6,
  output [31:0] Result,
  output [31:0] Result_2
);

  wire [0:0] comparator_1_lt, comparator_2_lt;
  wire [31:0] adder_1_out, AND_out, divider_1_out, divider_1_rem, multiplier_1_cout, multiplier_1_out,
       NOR_out, OR_out, shifter_1_out, shifter_2_out, shifter_3_out, subtractor_1_out, XOR_out;

  assign AND_out = X & Y;  // AND_Gate AND, 32 bits wide
  assign OR_out = X | Y;  // OR_Gate OR, 32 bits wide
  Shifter #(.width(32)) shifter_1 (.in(X), .\dist (Y[4:0]), .out(shifter_1_out));
  Shifter #(.width(32), .shift("ar")) shifter_2 (.in(X), .\dist (Y[4:0]), .out(shifter_2_out));
  Shifter #(.width(32), .shift("lr")) shifter_3 (.in(X), .\dist (Y[4:0]), .out(shifter_3_out));
  Multiplier #(.width(32)) multiplier_1 (.a(X), .b(Y), .out(multiplier_1_out), .cout(multiplier_1_cout));  // open: cin
  Divider #(.width(32)) divider_1 (.a(X), .b(Y), .out(divider_1_out), .rem(divider_1_rem));  // open: upper
  Adder #(.width(32)) adder_1 (.a(X), .b(Y), .out(adder_1_out));  // open: cin, cout
  Subtractor #(.width(32)) subtractor_1 (.a(X), .b(Y), .out(subtractor_1_out));  // open: bin, bout
  assign XOR_out = X ^ Y;  // XOR_Gate XOR, 32 bits wide
  assign NOR_out = ~(X | Y);  // NOR_Gate NOR, 32 bits wide
  Comparator #(.width(32)) comparator_1 (.a(X), .b(Y), .eq(Equal), .lt(comparator_1_lt[0]));  // open: gt
  Comparator #(.width(32), .mode("unsigned")) comparator_2 (.a(X), .b(Y), .lt(comparator_2_lt[0]));  // open: gt, eq
  Multiplexer #(.select(4), .width(32), .enable("false")) multiplexer_1 (
    .in0(shifter_1_out), .in1(shifter_2_out), .in2(shifter_3_out), .in3(multiplier_1_out),
    .in4(divider_1_out), .in5(adder_1_out), .in6(subtractor_1_out), .in7(AND_out), .in8(OR_out),
    .in9(XOR_out), .in10(NOR_out), .in11({{31{1'b0}}, comparator_1_lt[0]}),
    .in12({{31{1'b0}}, comparator_2_lt[0]}), .in13({32{1'b0}}), .in14({32{1'b0}}), .in15({32{1'b0}}),
    .out(Result), .sel(AluOP));
  Multiplexer #(.select(4), .width(32), .enable("false")) multiplexer_2 (
    .in0({32{1'b0}}), .in1({32{1'b0}}), .in2({32{1'b0}}), .in3(multiplier_1_cout), .in4(divider_1_rem),
    .in5({32{1'b0}}), .in6({32{1'b0}}), .in7({32{1'b0}}), .in8({32{1'b0}}), .in9({32{1'b0}}),
    .in10({32{1'b0}}), .in11({32{1'b0}}), .in12({32{1'b0}}), .in13({32{1'b0}}), .in14({32{1'b0}}),
    .in15({32{1'b0}}), .out(Result_2), .sel(AluOP));
  Multiplexer #(.select(4), .enable("false")) multiplexer_3 (
    .in0(1'b0), .in1(1'b0), .in2(1'b0), .in3(1'b0), .in4(1'b0), .in5(1'b0), .in6(1'b0), .in7(1'b0),
    .in8(1'b0), .in9(1'b0), .in10(1'b0), .in11(comparator_1_lt[0]), .in12(comparator_2_lt[0]), .in13(1'b0),
    .in14(1'b0), .in15(1'b0), .out(out_6), .sel(AluOP));
  not not_1 (out_4, out_6);

  // Other names for the same wires on the sheet: Result2[31:0] = Result_2; S[3:0] = AluOP; tunnel = out_6;
  //   tunnel_t = out_4

  // Notes on the sheet:
  //   不要改变此引脚区域内容，也不要改变ALU封装形式
  //   输入引脚
  //   输出引脚
endmodule

module Regifile (
  input  [31:0] Din,
  input  Clk,
  input  WE,
  input  [4:0] R1_num,
  input  [4:0] W_num,
  input  [4:0] R2_num,
  output [31:0] R1,
  output [31:0] R2
);

  // RegisterFile registerfile_1: pin names not known; wires that end beside it: Din, Clk, WE, W_num, R1_num, R2_num, R1, R2
endmodule

module IF_ID (
  input  [31:0] IR,
  input  EN,
  input  [31:0] PC,
  input  PredictBranch,
  input  FLUSH,
  input  RST,
  input  CLK,
  output [31:0] IR_2,
  output [31:0] PC_2,
  output PredictBranch_2
);

  wire multiplexer_3_out, or_1_out;
  wire [31:0] multiplexer_1_out, multiplexer_2_out;

  Multiplexer #(.width(32), .enable("false")) multiplexer_1 (
    .in0(IR), .in1({32{1'b0}}), .out(multiplexer_1_out), .sel(or_1_out));
  Multiplexer #(.width(32), .enable("false")) multiplexer_2 (
    .in0(PC), .in1({32{1'b0}}), .out(multiplexer_2_out), .sel(or_1_out));
  Multiplexer #(.enable("false")) multiplexer_3 (
    .in0(PredictBranch), .in1(1'b0), .out(multiplexer_3_out), .sel(or_1_out));
  or or_1 (or_1_out, FLUSH, RST);
  Register #(.width(32), .Select("low")) register_1 (.D(multiplexer_1_out), .en(EN), .Q(IR_2), .clk(CLK));  // open: clr
  Register #(.width(32), .Select("low")) register_2 (.D(multiplexer_2_out), .en(EN), .Q(PC_2), .clk(CLK));  // open: clr
  Register #(.width(1), .Select("low")) register_3 (
    .D(multiplexer_3_out), .en(EN), .Q(PredictBranch_2), .clk(CLK));  // open: clr
endmodule

module ID_EX (
  input  EN,
  input  [1:0] R1ForwardSrc,
  input  [1:0] R2ForwardSrc,
  input  URET,
  input  JALR,
  input  JAL,
  input  BEQ,
  input  BNE,
  input  BLT_U,
  input  MemToReg,
  input  MemWrite,
  input  [3:0] AluOP,
  input  AluResult,
  input  AluSrcB,
  input  RegWrite,
  input  [2:0] MemVariant,
  input  ECALL,
  input  [31:0] R1,
  input  [31:0] R2,
  input  [31:0] AluImm,
  input  [31:0] JmpImm,
  input  [4:0] Rd_num,
  input  [31:0] IR,
  input  [31:0] PC,
  input  PredictBranch,
  input  FLUSH,
  input  RST,
  input  CLK,
  output [1:0] R1ForwardSrc_2,
  output [1:0] R2ForwardSrc_2,
  output URET_2,
  output JALR_2,
  output JAL_2,
  output BEQ_2,
  output BNE_2,
  output BLT_U_2,
  output MemToReg_2,
  output MemWrite_2,
  output [3:0] AluOP_2,
  output AluResult_2,
  output AluSrcB_2,
  output RegWrite_2,
  output [2:0] MemVariant_2,
  output ECALL_2,
  output [31:0] R1_2,
  output [31:0] R2_2,
  output [31:0] AluImm_2,
  output [31:0] JmpImm_2,
  output [4:0] Rd_num_2,
  output [31:0] IR_2,
  output [31:0] PC_2,
  output PredictBranch_2
);

  wire multiplexer_3_out, multiplexer_4_out, multiplexer_5_out, multiplexer_6_out, multiplexer_7_out,
       multiplexer_8_out, multiplexer_9_out, multiplexer_10_out, multiplexer_12_out, multiplexer_13_out,
       multiplexer_14_out, multiplexer_16_out, multiplexer_24_out, or_1_out;
  wire [1:0] multiplexer_1_out, multiplexer_2_out;
  wire [2:0] multiplexer_15_out;
  wire [3:0] multiplexer_11_out;
  wire [4:0] multiplexer_21_out;
  wire [31:0] multiplexer_17_out, multiplexer_18_out, multiplexer_19_out, multiplexer_20_out,
       multiplexer_22_out, multiplexer_23_out;

  Multiplexer #(.width(2), .enable("false")) multiplexer_1 (
    .in0(R1ForwardSrc), .in1(2'b00), .out(multiplexer_1_out), .sel(or_1_out));
  Multiplexer #(.width(2), .enable("false")) multiplexer_2 (
    .in0(R2ForwardSrc), .in1(2'b00), .out(multiplexer_2_out), .sel(or_1_out));
  Multiplexer #(.enable("false")) multiplexer_3 (.in0(URET), .in1(1'b0), .out(multiplexer_3_out), .sel(or_1_out));
  Multiplexer #(.enable("false")) multiplexer_4 (.in0(JALR), .in1(1'b0), .out(multiplexer_4_out), .sel(or_1_out));
  Multiplexer #(.enable("false")) multiplexer_5 (.in0(JAL), .in1(1'b0), .out(multiplexer_5_out), .sel(or_1_out));
  Multiplexer #(.enable("false")) multiplexer_6 (.in0(BEQ), .in1(1'b0), .out(multiplexer_6_out), .sel(or_1_out));
  Multiplexer #(.enable("false")) multiplexer_7 (.in0(BNE), .in1(1'b0), .out(multiplexer_7_out), .sel(or_1_out));
  Multiplexer #(.enable("false")) multiplexer_8 (.in0(BLT_U), .in1(1'b0), .out(multiplexer_8_out), .sel(or_1_out));
  Multiplexer #(.enable("false")) multiplexer_9 (.in0(MemToReg), .in1(1'b0), .out(multiplexer_9_out), .sel(or_1_out));
  Multiplexer #(.enable("false")) multiplexer_10 (.in0(MemWrite), .in1(1'b0), .out(multiplexer_10_out), .sel(or_1_out));
  Multiplexer #(.width(4), .enable("false")) multiplexer_11 (
    .in0(AluOP), .in1(4'b0000), .out(multiplexer_11_out), .sel(or_1_out));
  Multiplexer #(.enable("false")) multiplexer_12 (
    .in0(AluResult), .in1(1'b0), .out(multiplexer_12_out), .sel(or_1_out));
  Multiplexer #(.enable("false")) multiplexer_13 (.in0(AluSrcB), .in1(1'b0), .out(multiplexer_13_out), .sel(or_1_out));
  Multiplexer #(.enable("false")) multiplexer_14 (.in0(RegWrite), .in1(1'b0), .out(multiplexer_14_out), .sel(or_1_out));
  Multiplexer #(.width(3), .enable("false")) multiplexer_15 (
    .in0(MemVariant), .in1(3'b000), .out(multiplexer_15_out), .sel(or_1_out));
  Multiplexer #(.enable("false")) multiplexer_16 (.in0(ECALL), .in1(1'b0), .out(multiplexer_16_out), .sel(or_1_out));
  Multiplexer #(.width(32), .enable("false")) multiplexer_17 (
    .in0(R1), .in1({32{1'b0}}), .out(multiplexer_17_out), .sel(or_1_out));
  Multiplexer #(.width(32), .enable("false")) multiplexer_18 (
    .in0(R2), .in1({32{1'b0}}), .out(multiplexer_18_out), .sel(or_1_out));
  Multiplexer #(.width(32), .enable("false")) multiplexer_19 (
    .in0(AluImm), .in1({32{1'b0}}), .out(multiplexer_19_out), .sel(or_1_out));
  Multiplexer #(.width(32), .enable("false")) multiplexer_20 (
    .in0(JmpImm), .in1({32{1'b0}}), .out(multiplexer_20_out), .sel(or_1_out));
  Multiplexer #(.width(5), .enable("false")) multiplexer_21 (
    .in0(Rd_num), .in1({5{1'b0}}), .out(multiplexer_21_out), .sel(or_1_out));
  Multiplexer #(.width(32), .enable("false")) multiplexer_22 (
    .in0(IR), .in1({32{1'b0}}), .out(multiplexer_22_out), .sel(or_1_out));
  Multiplexer #(.width(32), .enable("false")) multiplexer_23 (
    .in0(PC), .in1({32{1'b0}}), .out(multiplexer_23_out), .sel(or_1_out));
  Multiplexer #(.enable("false")) multiplexer_24 (
    .in0(PredictBranch), .in1(1'b0), .out(multiplexer_24_out), .sel(or_1_out));
  or or_1 (or_1_out, FLUSH, RST);
  Register #(.width(2), .Select("low")) register_1 (
    .D(multiplexer_1_out), .en(EN), .Q(R1ForwardSrc_2), .clk(CLK));  // open: clr
  Register #(.width(2), .Select("low")) register_2 (
    .D(multiplexer_2_out), .en(EN), .Q(R2ForwardSrc_2), .clk(CLK));  // open: clr
  Register #(.width(1), .Select("low")) register_3 (
    .D(multiplexer_3_out), .en(EN), .Q(URET_2), .clk(CLK));  // open: clr
  Register #(.width(1), .Select("low")) register_4 (
    .D(multiplexer_4_out), .en(EN), .Q(JALR_2), .clk(CLK));  // open: clr
  Register #(.width(1), .Select("low")) register_5 (.D(multiplexer_5_out), .en(EN), .Q(JAL_2), .clk(CLK));  // open: clr
  Register #(.width(1), .Select("low")) register_6 (.D(multiplexer_6_out), .en(EN), .Q(BEQ_2), .clk(CLK));  // open: clr
  Register #(.width(1), .Select("low")) register_7 (.D(multiplexer_7_out), .en(EN), .Q(BNE_2), .clk(CLK));  // open: clr
  Register #(.width(1), .Select("low")) register_8 (
    .D(multiplexer_8_out), .en(EN), .Q(BLT_U_2), .clk(CLK));  // open: clr
  Register #(.width(1), .Select("low")) register_9 (
    .D(multiplexer_9_out), .en(EN), .Q(MemToReg_2), .clk(CLK));  // open: clr
  Register #(.width(1), .Select("low")) register_10 (
    .D(multiplexer_10_out), .en(EN), .Q(MemWrite_2), .clk(CLK));  // open: clr
  Register #(.width(4), .Select("low")) register_11 (
    .D(multiplexer_11_out), .en(EN), .Q(AluOP_2), .clk(CLK));  // open: clr
  Register #(.width(1), .Select("low")) register_12 (
    .D(multiplexer_12_out), .en(EN), .Q(AluResult_2), .clk(CLK));  // open: clr
  Register #(.width(1), .Select("low")) register_13 (
    .D(multiplexer_13_out), .en(EN), .Q(AluSrcB_2), .clk(CLK));  // open: clr
  Register #(.width(1), .Select("low")) register_14 (
    .D(multiplexer_14_out), .en(EN), .Q(RegWrite_2), .clk(CLK));  // open: clr
  Register #(.width(3), .Select("low")) register_15 (
    .D(multiplexer_15_out), .en(EN), .Q(MemVariant_2), .clk(CLK));  // open: clr
  Register #(.width(1), .Select("low")) register_16 (
    .D(multiplexer_16_out), .en(EN), .Q(ECALL_2), .clk(CLK));  // open: clr
  Register #(.width(32), .Select("low")) register_17 (
    .D(multiplexer_17_out), .en(EN), .Q(R1_2), .clk(CLK));  // open: clr
  Register #(.width(32), .Select("low")) register_18 (
    .D(multiplexer_18_out), .en(EN), .Q(R2_2), .clk(CLK));  // open: clr
  Register #(.width(32), .Select("low")) register_19 (
    .D(multiplexer_19_out), .en(EN), .Q(AluImm_2), .clk(CLK));  // open: clr
  Register #(.width(32), .Select("low")) register_20 (
    .D(multiplexer_20_out), .en(EN), .Q(JmpImm_2), .clk(CLK));  // open: clr
  Register #(.width(5), .Select("low")) register_21 (
    .D(multiplexer_21_out), .en(EN), .Q(Rd_num_2), .clk(CLK));  // open: clr
  Register #(.width(32), .Select("low")) register_22 (
    .D(multiplexer_22_out), .en(EN), .Q(IR_2), .clk(CLK));  // open: clr
  Register #(.width(32), .Select("low")) register_23 (
    .D(multiplexer_23_out), .en(EN), .Q(PC_2), .clk(CLK));  // open: clr
  Register #(.width(1), .Select("low")) register_24 (
    .D(multiplexer_24_out), .en(EN), .Q(PredictBranch_2), .clk(CLK));  // open: clr
endmodule

module EX_MEM (
  input  EN,
  input  MemToReg,
  input  MemWrite,
  input  RegWrite,
  input  [2:0] MemVariant,
  input  Halt,
  input  [31:0] Result,
  input  [31:0] MemWriteData,
  input  [4:0] Rd_num,
  input  [31:0] IR,
  input  [31:0] PC,
  input  FLUSH,
  input  RST,
  input  CLK,
  output MemToReg_2,
  output MemWrite_2,
  output RegWrite_2,
  output [2:0] MemVariant_2,
  output Halt_2,
  output [31:0] Result_2,
  output [31:0] MemWriteData_2,
  output [4:0] Rd_num_2,
  output [31:0] IR_2,
  output [31:0] PC_2
);

  wire multiplexer_1_out, multiplexer_2_out, multiplexer_3_out, multiplexer_5_out, or_1_out;
  wire [2:0] multiplexer_4_out;
  wire [4:0] multiplexer_8_out;
  wire [31:0] multiplexer_6_out, multiplexer_7_out, multiplexer_9_out, multiplexer_10_out;

  Multiplexer #(.enable("false")) multiplexer_1 (.in0(MemToReg), .in1(1'b0), .out(multiplexer_1_out), .sel(or_1_out));
  Multiplexer #(.enable("false")) multiplexer_2 (.in0(MemWrite), .in1(1'b0), .out(multiplexer_2_out), .sel(or_1_out));
  Multiplexer #(.enable("false")) multiplexer_3 (.in0(RegWrite), .in1(1'b0), .out(multiplexer_3_out), .sel(or_1_out));
  Multiplexer #(.width(3), .enable("false")) multiplexer_4 (
    .in0(MemVariant), .in1(3'b000), .out(multiplexer_4_out), .sel(or_1_out));
  Multiplexer #(.enable("false")) multiplexer_5 (.in0(Halt), .in1(1'b0), .out(multiplexer_5_out), .sel(or_1_out));
  Multiplexer #(.width(32), .enable("false")) multiplexer_6 (
    .in0(Result), .in1({32{1'b0}}), .out(multiplexer_6_out), .sel(or_1_out));
  Multiplexer #(.width(32), .enable("false")) multiplexer_7 (
    .in0(MemWriteData), .in1({32{1'b0}}), .out(multiplexer_7_out), .sel(or_1_out));
  Multiplexer #(.width(5), .enable("false")) multiplexer_8 (
    .in0(Rd_num), .in1({5{1'b0}}), .out(multiplexer_8_out), .sel(or_1_out));
  Multiplexer #(.width(32), .enable("false")) multiplexer_9 (
    .in0(IR), .in1({32{1'b0}}), .out(multiplexer_9_out), .sel(or_1_out));
  Multiplexer #(.width(32), .enable("false")) multiplexer_10 (
    .in0(PC), .in1({32{1'b0}}), .out(multiplexer_10_out), .sel(or_1_out));
  or or_1 (or_1_out, FLUSH, RST);
  Register #(.width(1), .Select("low")) register_1 (
    .D(multiplexer_1_out), .en(EN), .Q(MemToReg_2), .clk(CLK));  // open: clr
  Register #(.width(1), .Select("low")) register_2 (
    .D(multiplexer_2_out), .en(EN), .Q(MemWrite_2), .clk(CLK));  // open: clr
  Register #(.width(1), .Select("low")) register_3 (
    .D(multiplexer_3_out), .en(EN), .Q(RegWrite_2), .clk(CLK));  // open: clr
  Register #(.width(3), .Select("low")) register_4 (
    .D(multiplexer_4_out), .en(EN), .Q(MemVariant_2), .clk(CLK));  // open: clr
  Register #(.width(1), .Select("low")) register_5 (
    .D(multiplexer_5_out), .en(EN), .Q(Halt_2), .clk(CLK));  // open: clr
  Register #(.width(32), .Select("low")) register_6 (
    .D(multiplexer_6_out), .en(EN), .Q(Result_2), .clk(CLK));  // open: clr
  Register #(.width(32), .Select("low")) register_7 (
    .D(multiplexer_7_out), .en(EN), .Q(MemWriteData_2), .clk(CLK));  // open: clr
  Register #(.width(5), .Select("low")) register_8 (
    .D(multiplexer_8_out), .en(EN), .Q(Rd_num_2), .clk(CLK));  // open: clr
  Register #(.width(32), .Select("low")) register_9 (.D(multiplexer_9_out), .en(EN), .Q(IR_2), .clk(CLK));  // open: clr
  Register #(.width(32), .Select("low")) register_10 (
    .D(multiplexer_10_out), .en(EN), .Q(PC_2), .clk(CLK));  // open: clr
endmodule

module MEM_WB (
  input  EN,
  input  MemToReg,
  input  RegWrite,
  input  Halt,
  input  [31:0] Result,
  input  [31:0] MemReadData,
  input  [4:0] Rd_num,
  input  [31:0] IR,
  input  [31:0] PC,
  input  FLUSH,
  input  RST,
  input  CLK,
  output MemToReg_2,
  output RegWrite_2,
  output Halt_2,
  output [31:0] Result_2,
  output [31:0] MemReadData_2,
  output [4:0] Rd_num_2,
  output [31:0] IR_2,
  output [31:0] PC_2
);

  wire multiplexer_1_out, multiplexer_2_out, multiplexer_3_out, or_1_out;
  wire [4:0] multiplexer_6_out;
  wire [31:0] multiplexer_4_out, multiplexer_5_out, multiplexer_7_out, multiplexer_8_out;

  Multiplexer #(.enable("false")) multiplexer_1 (.in0(MemToReg), .in1(1'b0), .out(multiplexer_1_out), .sel(or_1_out));
  Multiplexer #(.enable("false")) multiplexer_2 (.in0(RegWrite), .in1(1'b0), .out(multiplexer_2_out), .sel(or_1_out));
  Multiplexer #(.enable("false")) multiplexer_3 (.in0(Halt), .in1(1'b0), .out(multiplexer_3_out), .sel(or_1_out));
  Multiplexer #(.width(32), .enable("false")) multiplexer_4 (
    .in0(Result), .in1({32{1'b0}}), .out(multiplexer_4_out), .sel(or_1_out));
  Multiplexer #(.width(32), .enable("false")) multiplexer_5 (
    .in0(MemReadData), .in1({32{1'b0}}), .out(multiplexer_5_out), .sel(or_1_out));
  Multiplexer #(.width(5), .enable("false")) multiplexer_6 (
    .in0(Rd_num), .in1({5{1'b0}}), .out(multiplexer_6_out), .sel(or_1_out));
  Multiplexer #(.width(32), .enable("false")) multiplexer_7 (
    .in0(IR), .in1({32{1'b0}}), .out(multiplexer_7_out), .sel(or_1_out));
  Multiplexer #(.width(32), .enable("false")) multiplexer_8 (
    .in0(PC), .in1({32{1'b0}}), .out(multiplexer_8_out), .sel(or_1_out));
  or or_1 (or_1_out, FLUSH, RST);
  Register #(.width(1), .Select("low")) register_1 (
    .D(multiplexer_1_out), .en(EN), .Q(MemToReg_2), .clk(CLK));  // open: clr
  Register #(.width(1), .Select("low")) register_2 (
    .D(multiplexer_2_out), .en(EN), .Q(RegWrite_2), .clk(CLK));  // open: clr
  Register #(.width(1), .Select("low")) register_3 (
    .D(multiplexer_3_out), .en(EN), .Q(Halt_2), .clk(CLK));  // open: clr
  Register #(.width(32), .Select("low")) register_4 (
    .D(multiplexer_4_out), .en(EN), .Q(Result_2), .clk(CLK));  // open: clr
  Register #(.width(32), .Select("low")) register_5 (
    .D(multiplexer_5_out), .en(EN), .Q(MemReadData_2), .clk(CLK));  // open: clr
  Register #(.width(5), .Select("low")) register_6 (
    .D(multiplexer_6_out), .en(EN), .Q(Rd_num_2), .clk(CLK));  // open: clr
  Register #(.width(32), .Select("low")) register_7 (.D(multiplexer_7_out), .en(EN), .Q(IR_2), .clk(CLK));  // open: clr
  Register #(.width(32), .Select("low")) register_8 (.D(multiplexer_8_out), .en(EN), .Q(PC_2), .clk(CLK));  // open: clr
endmodule

module \理想流水线  (
  output RegWrite,
  output MemWrite,
  output [31:0] IF_PC,
  output [31:0] ID_PC,
  output [31:0] EX_PC,
  output [31:0] M_PC,
  output [31:0] WB_PC,
  output [31:0] RDin,
  output [31:0] MDin,
  output [31:0] LedData
);

  wire and_1_out, CLK, clock_1_out, comparator_1_eq, comparator_1_lt, comparator_2_eq, d_ff_1_q, Eq,
       EX_ECALL, EX_Halt, ex_mem_1_halt_2, ex_mem_1_memtoreg_2, ex_mem_1_regwrite_2, Ge, Go, halt,
       id_ex_1_alusrcb_2, id_ex_1_beq_2, id_ex_1_blt_u_2, id_ex_1_bne_2, id_ex_1_jal_2, id_ex_1_jalr_2,
       id_ex_1_memtoreg_2, id_ex_1_memwrite_2, id_ex_1_regwrite_2, id_ex_1_uret_2, IR1, IR2, IR3, JAL, Lt,
       mem_wb_1_halt_2, mem_wb_1_memtoreg_2, nand_1_out, not_1_out, not_2_out, not_3_out, not_4_out,
       not_5_out, not_6_out, not_7_out, or_1_out, RST, W1, W2, W3, \单周期硬布线控制器_1_alu_result ,
       \单周期硬布线控制器_1_alu_src , \单周期硬布线控制器_1_beq , \单周期硬布线控制器_1_blt_u , \单周期硬布线控制器_1_bne , \单周期硬布线控制器_1_ecall ,
       \单周期硬布线控制器_1_jalr , \单周期硬布线控制器_1_memtoreg , \单周期硬布线控制器_1_memwrite , \单周期硬布线控制器_1_regwrite ,
       \单周期硬布线控制器_1_s_type , \单周期硬布线控制器_1_uret ;
  wire [1:0] PCType, pctype_1_linktoreg;
  wire [2:0] ex_mem_1_memvariant_2, id_ex_1_memvariant_2, \单周期硬布线控制器_1_func3 ;
  wire [3:0] id_ex_1_aluop_2, \单周期硬布线控制器_1_alu_op ;
  wire [4:0] ex_mem_1_rd_num_2, id_ex_1_rd_num_2, multiplexer_2_out, multiplexer_3_out, WB_Rd;
  wire [7:0] bitselector_1_out;
  wire [9:0] ex_mem_1_result_2_2;
  wire [11:0] multiplexer_4_out;
  wire [12:0] CNT_num;
  wire [15:0] bitselector_2_out, \LoadUse次数 , \总周期数 , \插入气泡数 , \无条件分支数 , \条件分支成功数 ;
  wire [31:0] alu_1_result_2, bit_extender_1_out, bit_extender_2_out, bit_extender_3_out, bit_extender_4_out,
       bit_extender_5_out, bit_extender_6_out, bit_extender_7_out, EX_IR, ex_mem_1_result_2, EX_PCp4, EX_R1,
       EX_R2, id_ex_1_aluimm_2, id_ex_1_jmpimm_2, ID_IR, IF_IR, IF_PCp4, MEM_IR, mem_wb_1_memreaddata_2,
       mem_wb_1_result_2, multiplexer_1_out, multiplexer_5_out, multiplexer_6_out, multiplexer_7_out,
       multiplexer_8_out, multiplexer_9_out, multiplexer_10_out, PCRelJmp, ram_1_data, regifile_1_r1,
       regifile_1_r2, RegRelJmp, WB_IR;

  Button \u_总复位  (.out(RST));
  Button _1 (.out(IR1));
  Button _2 (.out(IR2));
  Button _3 (.out(IR3));
  // Probe on \总周期数 
  // Probe on \总周期数 
  Button \u_继续运行  (.out(Go));
  LED led_1 (.in(W1));
  LED led_2 (.in(W2));
  LED led_3 (.in(W3));
  // Probe on PCType
  Multiplexer #(.select(2), .width(32), .enable("false")) multiplexer_1 (
    .in0(IF_PCp4), .in2(RegRelJmp), .in3(PCRelJmp), .out(multiplexer_1_out), .sel(PCType));  // open: in1
  // Probe on multiplexer_1_out
  Hex_Digit_Display hex_digit_display_1 (.value(LedData[31:28]));  // open: dp
  // Probe on IF_PC[19:0]
  // RiscV_Probe riscv_probe_1: pin names not known; wires that end beside it: IF_IR
  Hex_Digit_Display hex_digit_display_2 (.value(LedData[23:20]));  // open: dp
  Hex_Digit_Display hex_digit_display_3 (.value(LedData[27:24]));  // open: dp
  // Probe on ID_PC[19:0]
  // RiscV_Probe riscv_probe_2: pin names not known; wires that end beside it: ID_IR
  Register #(.width(32), .Select("low")) PC (.D(multiplexer_1_out), .en(not_1_out), .Q(IF_PC), .clk(CLK), .clr(RST));
  not not_1 (not_1_out, halt);
  Hex_Digit_Display hex_digit_display_4 (.value(LedData[15:12]));  // open: dp
  Hex_Digit_Display hex_digit_display_5 (.value(LedData[19:16]));  // open: dp
  Hex_Digit_Display hex_digit_display_6 (.value(LedData[7:4]));  // open: dp
  Hex_Digit_Display hex_digit_display_7 (.value(LedData[11:8]));  // open: dp
  // Probe on EX_PC[19:0]
  // RiscV_Probe riscv_probe_3: pin names not known; wires that end beside it: EX_IR
  ROM #(.addrWidth(10), .dataWidth(32), .Select("high")) rom_1 (.addr(IF_PC[11:2]), .data(IF_IR));
  Adder #(.width(32)) adder_1 (.a(IF_PC), .b(32'h4), .out(IF_PCp4));  // open: cin, cout
  Hex_Digit_Display hex_digit_display_8 (.value(LedData[3:0]));  // open: dp
  not not_2 (not_2_out, halt);
  IF_ID if_id_1 (
    .IR(IF_IR), .PC(IF_PC), .FLUSH(1'b0), .IR_2(ID_IR), .PC_2(ID_PC), .RST(RST), .EN(not_2_out), .CLK(CLK));  // open: PredictBranch, PredictBranch_2
  // Probe on \总周期数 
  // Probe on M_PC[19:0]
  // RiscV_Probe riscv_probe_4: pin names not known; wires that end beside it: MEM_IR
  // Probe on \总周期数 
  // Probe on \无条件分支数 
  // Probe on \条件分支成功数 
  // Probe on \插入气泡数 
  // Probe on \LoadUse次数 
  \单周期硬布线控制器  \u_单周期硬布线控制器_1  (
    .Funct({ID_IR[30], ID_IR[25], ID_IR[14:12]}), .OP(ID_IR[6:2]), .ALU_OP(\单周期硬布线控制器_1_alu_op ),
    .MemToReg(\单周期硬布线控制器_1_memtoreg ), .MemWrite(\单周期硬布线控制器_1_memwrite ), .ALU_SRC(\单周期硬布线控制器_1_alu_src ),
    .RegWrite(\单周期硬布线控制器_1_regwrite ), .ecall(\单周期硬布线控制器_1_ecall ), .S_type(\单周期硬布线控制器_1_s_type ),
    .JALR(\单周期硬布线控制器_1_jalr ), .Beq(\单周期硬布线控制器_1_beq ), .JAL(JAL), .Bne(\单周期硬布线控制器_1_bne ), .in_3(ID_IR[21]),
    .uret(\单周期硬布线控制器_1_uret ), .Func3(\单周期硬布线控制器_1_func3 ), .ALU_RESULT(\单周期硬布线控制器_1_alu_result ),
    .Blt_u(\单周期硬布线控制器_1_blt_u ), .LegitIR(ID_IR[1:0]));  // open: R1Dep, R2Dep, CSR
  Multiplexer #(.width(5), .enable("false")) multiplexer_2 (
    .in0(ID_IR[19:15]), .in1(5'b01010), .out(multiplexer_2_out), .sel(\单周期硬布线控制器_1_ecall ));
  Multiplexer #(.width(5), .enable("false")) multiplexer_3 (
    .in0(ID_IR[24:20]), .in1(5'b10001), .out(multiplexer_3_out), .sel(\单周期硬布线控制器_1_ecall ));
  // Probe on IF_PC[11:0]
  // Probe on WB_PC[19:0]
  // RiscV_Probe riscv_probe_5: pin names not known; wires that end beside it: WB_IR
  // Probe on multiplexer_2_out
  // Probe on multiplexer_3_out
  // Probe on WB_Rd
  Multiplexer #(.width(12), .enable("false")) multiplexer_4 (
    .in0(ID_IR[31:20]), .in1({ID_IR[31:25], ID_IR[11:7]}), .out(multiplexer_4_out), .sel(\单周期硬布线控制器_1_s_type ));
  assign bit_extender_1_out = {{19{ID_IR[31]}}, {ID_IR[31], ID_IR[7], ID_IR[30:25], ID_IR[11:8], 1'b0}};  // Bit_Extender bit_extender_1
  Multiplexer #(.width(32), .enable("false")) multiplexer_5 (
    .in0(bit_extender_1_out), .in1(bit_extender_2_out), .out(multiplexer_5_out), .sel(JAL));
  assign bit_extender_2_out = {{11{ID_IR[31]}}, {ID_IR[31], ID_IR[19:12], ID_IR[20], ID_IR[30:21], 1'b0}};  // Bit_Extender bit_extender_2
  // Probe on ID_PC[11:0]
  // Probe on EX_PC[11:0]
  not not_3 (not_3_out, CLK);
  assign bit_extender_3_out = {{20{multiplexer_4_out[11]}}, multiplexer_4_out};  // Bit_Extender bit_extender_3
  // Probe on M_PC[11:0]
  D_Flip_Flop #(.trigger("high"), .Pre_Clr_Positions("LEGACY"), .enable("true"), .NewFFLayout("false")) d_ff_1 (.Q(d_ff_1_q));  // open: clk, D, Qn, preset, en, reset
  // Probe on 13'hc
  Regifile regifile_1 (
    .Din(RDin), .Clk(not_3_out), .R1(regifile_1_r1), .R2(regifile_1_r2), .WE(RegWrite), .W_num(WB_Rd),
    .R1_num(multiplexer_2_out), .R2_num(multiplexer_3_out));
  // Probe on bit_extender_3_out
  // Probe on WB_PC[11:0]
  Comparator #(.width(13)) comparator_1 (
    .a(CNT_num), .b(13'hc), .eq(comparator_1_eq), .lt(comparator_1_lt));  // open: gt
  Clock clock_1 (.out(clock_1_out));
  ID_EX id_ex_1 (
    .IR(ID_IR), .PC(ID_PC), .FLUSH(1'b0), .IR_2(EX_IR), .PC_2(EX_PC), .RST(RST), .EN(not_4_out), .CLK(CLK),
    .URET(\单周期硬布线控制器_1_uret ), .URET_2(id_ex_1_uret_2), .JALR(\单周期硬布线控制器_1_jalr ), .JALR_2(id_ex_1_jalr_2),
    .JAL(JAL), .JAL_2(id_ex_1_jal_2), .BEQ(\单周期硬布线控制器_1_beq ), .BEQ_2(id_ex_1_beq_2),
    .BNE(\单周期硬布线控制器_1_bne ), .BNE_2(id_ex_1_bne_2), .BLT_U(\单周期硬布线控制器_1_blt_u ), .BLT_U_2(id_ex_1_blt_u_2),
    .MemToReg(\单周期硬布线控制器_1_memtoreg ), .MemToReg_2(id_ex_1_memtoreg_2), .MemWrite(\单周期硬布线控制器_1_memwrite ),
    .MemWrite_2(id_ex_1_memwrite_2), .AluOP(\单周期硬布线控制器_1_alu_op ), .AluOP_2(id_ex_1_aluop_2),
    .AluResult(\单周期硬布线控制器_1_alu_result ), .AluResult_2(pctype_1_linktoreg[1]),
    .AluSrcB(\单周期硬布线控制器_1_alu_src ), .AluSrcB_2(id_ex_1_alusrcb_2), .RegWrite(\单周期硬布线控制器_1_regwrite ),
    .RegWrite_2(id_ex_1_regwrite_2), .MemVariant(\单周期硬布线控制器_1_func3 ), .MemVariant_2(id_ex_1_memvariant_2),
    .Rd_num(ID_IR[11:7]), .Rd_num_2(id_ex_1_rd_num_2), .ECALL(\单周期硬布线控制器_1_ecall ), .ECALL_2(EX_ECALL),
    .JmpImm(multiplexer_5_out), .JmpImm_2(id_ex_1_jmpimm_2), .AluImm(bit_extender_3_out),
    .AluImm_2(id_ex_1_aluimm_2), .R2(regifile_1_r2), .R2_2(EX_R2), .R1(regifile_1_r1), .R1_2(EX_R1));  // open: PredictBranch, PredictBranch_2, R1ForwardSrc, R1ForwardSrc_2, R2ForwardSrc, R2ForwardSrc_2
  not not_4 (not_4_out, halt);
  nand nand_1 (nand_1_out, d_ff_1_q, comparator_1_eq);
  Counter #(.width(13), .max('h1fff), .ongoal("stay"), .behavior("old")) counter_1 (
    .count(comparator_1_lt), .Q(CNT_num), .clk(clock_1_out));  // open: load, D, carry, clr, preset
  Adder #(.width(32)) adder_2 (.a(id_ex_1_jmpimm_2), .b(EX_PC), .out(PCRelJmp));  // open: cin, cout
  assign CLK = nand_1_out ? clock_1_out : 1'bz;  // Controlled_Buffer controlled_buffer_1
  PCType pctype_1 (
    .JmpType(PCType), .Eq(Eq), .Lt(Lt), .Ge(Ge), .URET(id_ex_1_uret_2), .JALR(id_ex_1_jalr_2),
    .JAL(id_ex_1_jal_2), .BEQ(id_ex_1_beq_2), .BNE(id_ex_1_bne_2), .BLT_U(id_ex_1_blt_u_2),
    .LinkToReg(pctype_1_linktoreg[0]));  // open: Jmp, UncondJmp, CondBranch, ImmJmp, UncertainJmp, BranchInstr
  Multiplexer #(.width(32), .enable("false")) multiplexer_6 (
    .in0(EX_R2), .in1(id_ex_1_aluimm_2), .out(multiplexer_6_out), .sel(id_ex_1_alusrcb_2));
  Adder #(.width(32)) adder_3 (.a(EX_PC), .b(32'h4), .out(EX_PCp4));  // open: cin, cout
  Pull_Resistor #(.pull(1)) pull_resistor_1 (.node(CLK));
  ALU alu_1 (
    .X(EX_R1), .Y(multiplexer_6_out), .AluOP(id_ex_1_aluop_2), .Equal(Eq), .Result(RegRelJmp),
    .Result_2(alu_1_result_2), .out_4(Ge), .out_6(Lt));
  Multiplexer #(.select(2), .width(32), .enable("false")) multiplexer_7 (
    .in0(RegRelJmp), .in1(EX_PCp4), .in2(alu_1_result_2), .out(multiplexer_7_out), .sel(pctype_1_linktoreg));  // open: in3
  EX_MEM ex_mem_1 (
    .EN(not_5_out), .MemToReg(id_ex_1_memtoreg_2), .MemToReg_2(ex_mem_1_memtoreg_2),
    .MemWrite(id_ex_1_memwrite_2), .MemWrite_2(MemWrite), .RegWrite(id_ex_1_regwrite_2),
    .RegWrite_2(ex_mem_1_regwrite_2), .MemVariant(id_ex_1_memvariant_2),
    .MemVariant_2(ex_mem_1_memvariant_2), .Halt(EX_Halt), .Halt_2(ex_mem_1_halt_2),
    .Result(multiplexer_7_out),
    .Result_2({ex_mem_1_result_2[31:12], ex_mem_1_result_2_2, ex_mem_1_result_2[1:0]}), .MemWriteData(EX_R2),
    .MemWriteData_2(MDin), .Rd_num(id_ex_1_rd_num_2), .Rd_num_2(ex_mem_1_rd_num_2), .IR(EX_IR),
    .IR_2(MEM_IR), .PC(EX_PC), .PC_2(M_PC), .FLUSH(1'b0), .RST(RST), .CLK(CLK));
  not not_5 (not_5_out, halt);
  // Probe on {ex_mem_1_result_2[31:12], ex_mem_1_result_2_2, ex_mem_1_result_2[1:0]}
  BitSelector #(.width(32), .group(8)) bitselector_1 (
    .in(ram_1_data), .out(bitselector_1_out), .sel(ex_mem_1_result_2[1:0]));
  RAM #(.addrWidth(10), .dataWidth(32), .bus("separate"), .Select("high"), .simpleMode("false")) ram_1 (
    .addr(ex_mem_1_result_2_2), .din(MDin), .data(ram_1_data), .str(MemWrite), .sel(1'b1), .clk(CLK),
    .clr(RST));  // open: ld
  BitSelector #(.width(32), .group(16)) bitselector_2 (
    .in(ram_1_data), .out(bitselector_2_out), .sel(ex_mem_1_result_2[1]));
  assign bit_extender_4_out = {{24{bitselector_1_out[7]}}, bitselector_1_out};  // Bit_Extender bit_extender_4
  Multiplexer #(.width(32), .enable("false")) multiplexer_8 (
    .in0(bit_extender_4_out), .in1(bit_extender_5_out), .out(multiplexer_8_out),
    .sel(ex_mem_1_memvariant_2[2]));
  assign bit_extender_5_out = {{24{1'b0}}, bitselector_1_out};  // Bit_Extender bit_extender_5
  assign bit_extender_6_out = {{16{bitselector_2_out[15]}}, bitselector_2_out};  // Bit_Extender bit_extender_6
  Multiplexer #(.width(32), .enable("false")) multiplexer_9 (
    .in0(bit_extender_6_out), .in1(bit_extender_7_out), .out(multiplexer_9_out),
    .sel(ex_mem_1_memvariant_2[2]));
  assign bit_extender_7_out = {{16{1'b0}}, bitselector_2_out};  // Bit_Extender bit_extender_7
  Multiplexer #(.select(2), .width(32), .enable("false")) multiplexer_10 (
    .in0(multiplexer_8_out), .in1(multiplexer_9_out), .in2(ram_1_data), .out(multiplexer_10_out),
    .sel(ex_mem_1_memvariant_2[1:0]));  // open: in3
  not not_6 (not_6_out, halt);
  MEM_WB mem_wb_1 (
    .EN(not_6_out), .MemToReg(ex_mem_1_memtoreg_2), .MemToReg_2(mem_wb_1_memtoreg_2),
    .RegWrite(ex_mem_1_regwrite_2), .RegWrite_2(RegWrite), .Halt(ex_mem_1_halt_2), .Halt_2(mem_wb_1_halt_2),
    .Result({ex_mem_1_result_2[31:12], ex_mem_1_result_2_2, ex_mem_1_result_2[1:0]}),
    .Result_2(mem_wb_1_result_2), .MemReadData(multiplexer_10_out), .MemReadData_2(mem_wb_1_memreaddata_2),
    .Rd_num(ex_mem_1_rd_num_2), .Rd_num_2(WB_Rd), .IR(MEM_IR), .IR_2(WB_IR), .PC(M_PC), .PC_2(WB_PC),
    .FLUSH(1'b0), .RST(RST), .CLK(CLK));
  // Probe on mem_wb_1_memtoreg_2
  Multiplexer #(.width(32), .enable("false")) multiplexer_11 (
    .in0(mem_wb_1_result_2), .in1(mem_wb_1_memreaddata_2), .out(RDin), .sel(mem_wb_1_memtoreg_2));
  // Probe on RDin
  S_R_Flip_Flop #(.trigger("latch")) s_r_ff_1 (
    .S(mem_wb_1_halt_2), .R(1'b0), .Q(halt), .reset(or_1_out));  // open: Qn, preset
  or or_1 (or_1_out, Go, RST);
  not not_7 (not_7_out, halt);
  Counter #(.width(16), .max('hffff)) NXC (
    .count(not_7_out), .Q(\总周期数 ), .clk(CLK), .clr(RST));  // open: load, D, carry, preset, down
  Comparator #(.width(32)) comparator_2 (.a(EX_R2), .b(32'h22), .eq(comparator_2_eq));  // open: gt, lt
  and and_1 (and_1_out, EX_ECALL, comparator_2_eq);
  and and_2 (EX_Halt, ~comparator_2_eq, EX_ECALL);  // AND_Gate
  Register #(.width(32), .Select("low")) register_1 (.D(EX_R1), .en(and_1_out), .Q(LedData), .clk(CLK), .clr(RST));

  // Other names for the same wires on the sheet: MEM_PC[31:0] = M_PC

  // Notes on the sheet:
  //   中断源
  //   时空图监测，可删除
  //   中断等待指示
  //   数码管输出
  //   指令存储器
  //   contents of rom_1 (hex, n*v repeats v):
  //   413 493 913 993 46413 14e493 296913 39e993 842023 942223 1242423 1342623 a00893 493 913 993 73
  //   Rd[4:0]
  //   JALR
  //   URET
  //   I-Imm[11:0]
  //   S-Imm[11:0]
  //   B-Imm[12:1]
  //   J-Imm[20:1]
  //   JAL
  //   Beq
  //   Bne
  //   Blt[u]
  //   MemToReg
  //   MemWrite
  //   AluOP
  //   AluResult
  //   AluSrcB
  //   RegWrite
  //   MemVariant
  //   I/S-ImmType
  //   控制位
  //   流水调试日志用
  //   暂停节拍，不能为0
  //   戳工具置1进入计数暂停模式，ctrl+k时钟自动运行到对应节拍暂停
  //   ctrl+k关闭时钟连续运行，将控制位置零，进入单步调试模式调试
  //   用这个时钟源需要去掉电路中的其他时钟源
  //   可计数暂停的时钟源
  //   为方便自动评测，需要输出流水线各段保存的PC值，注意是PC不是PC+4，另外ID段寄存器写入信息，Mem段内存写入信息也要输出
  //   数据存储器
endmodule

module BubbleGenerator (
  input  Halt,
  input  R1Dep,
  input  EX_RegWrite,
  input  [4:0] EX_Rd,
  input  [4:0] R1,
  input  Jmp,
  input  R2Dep,
  input  MEM_RegWrite,
  input  [4:0] MEM_Rd,
  input  [4:0] R2,
  output Stall,
  output PC_EN,
  output IF_ID_EN,
  output IF_ID_FLUSH,
  output ID_EX_FLUSH,
  output ID_EX_EN,
  output EX_MEM_EN,
  output MEM_WB_EN,
  output Flush,
  output DataHazzard
);

  wire and_1_out, and_2_out, and_3_out, and_4_out, comparator_1_eq, comparator_2_eq, comparator_3_eq,
       comparator_4_eq, comparator_5_eq, comparator_6_eq, comparator_7_eq, comparator_8_eq;

  Comparator #(.width(5)) comparator_1 (.a({5{1'b0}}), .b(R1), .eq(comparator_1_eq));  // open: gt, lt
  Comparator #(.width(5)) comparator_2 (.a(R1), .b(EX_Rd), .eq(comparator_2_eq));  // open: gt, lt
  Comparator #(.width(5)) comparator_3 (.a({5{1'b0}}), .b(R1), .eq(comparator_3_eq));  // open: gt, lt
  Comparator #(.width(5)) comparator_4 (.a(R1), .b(MEM_Rd), .eq(comparator_4_eq));  // open: gt, lt
  Comparator #(.width(5)) comparator_5 (.a({5{1'b0}}), .b(R2), .eq(comparator_5_eq));  // open: gt, lt
  Comparator #(.width(5)) comparator_6 (.a(R2), .b(EX_Rd), .eq(comparator_6_eq));  // open: gt, lt
  Comparator #(.width(5)) comparator_7 (.a({5{1'b0}}), .b(R2), .eq(comparator_7_eq));  // open: gt, lt
  Comparator #(.width(5)) comparator_8 (.a(R2), .b(MEM_Rd), .eq(comparator_8_eq));  // open: gt, lt
  and and_1 (and_1_out, R1Dep, ~comparator_1_eq, comparator_2_eq, EX_RegWrite);  // AND_Gate
  and and_2 (and_2_out, R1Dep, ~comparator_3_eq, comparator_4_eq, MEM_RegWrite);  // AND_Gate
  and and_3 (and_3_out, R2Dep, ~comparator_5_eq, comparator_6_eq, EX_RegWrite);  // AND_Gate
  and and_4 (and_4_out, R2Dep, ~comparator_7_eq, comparator_8_eq, MEM_RegWrite);  // AND_Gate
  or or_1 (DataHazzard, and_1_out, and_2_out, and_3_out, and_4_out);
  not not_1 (Stall, IF_ID_EN);
  nor nor_1 (IF_ID_EN, Halt, DataHazzard);
  or or_2 (Flush, Jmp, DataHazzard);
  not not_2 (EX_MEM_EN, Halt);

  assign ID_EX_EN = EX_MEM_EN;
  assign ID_EX_FLUSH = Flush;
  assign IF_ID_FLUSH = Jmp;
  assign MEM_WB_EN = EX_MEM_EN;
  assign PC_EN = IF_ID_EN;
endmodule
module \气泡流水线  (
  output RegWrite,
  output MemWrite,
  output [31:0] IF_PC,
  output [31:0] ID_PC,
  output [31:0] EX_PC,
  output [31:0] M_PC,
  output [31:0] WB_PC,
  output [31:0] RDin,
  output [31:0] MDin,
  output [31:0] LedData
);

  wire and_1_out, and_2_out, and_4_out, and_5_out, and_6_out, bubblegenerator_1_ex_mem_en,
       bubblegenerator_1_id_ex_en, bubblegenerator_1_id_ex_flush, bubblegenerator_1_if_id_en,
       bubblegenerator_1_if_id_flush, bubblegenerator_1_mem_wb_en, bubblegenerator_1_pc_en, CLK, clock_1_out,
       comparator_1_eq, comparator_1_lt, comparator_2_eq, CondBranch, d_ff_1_q, DataHazzard, Eq, EX_ECALL,
       EX_Halt, ex_mem_1_halt_2, ex_mem_1_memtoreg_2, ex_mem_1_regwrite_2, Flush, Ge, Go, halt,
       id_ex_1_alusrcb_2, id_ex_1_beq_2, id_ex_1_blt_u_2, id_ex_1_bne_2, id_ex_1_jal_2, id_ex_1_jalr_2,
       id_ex_1_memtoreg_2, id_ex_1_memwrite_2, id_ex_1_regwrite_2, id_ex_1_uret_2, IR1, IR2, IR3, JAL, Lt,
       mem_wb_1_halt_2, mem_wb_1_memtoreg_2, nand_1_out, not_1_out, not_2_out, or_1_out, pctype_1_jmp, RST,
       UncondJmp, W1, W2, W3, \单周期硬布线控制器_1_alu_result , \单周期硬布线控制器_1_alu_src , \单周期硬布线控制器_1_beq ,
       \单周期硬布线控制器_1_blt_u , \单周期硬布线控制器_1_bne , \单周期硬布线控制器_1_ecall , \单周期硬布线控制器_1_jalr ,
       \单周期硬布线控制器_1_memtoreg , \单周期硬布线控制器_1_memwrite , \单周期硬布线控制器_1_r1dep , \单周期硬布线控制器_1_r2dep ,
       \单周期硬布线控制器_1_regwrite , \单周期硬布线控制器_1_s_type , \单周期硬布线控制器_1_uret ;
  wire [1:0] PCType, pctype_1_linktoreg;
  wire [2:0] ex_mem_1_memvariant_2, id_ex_1_memvariant_2, \单周期硬布线控制器_1_func3 ;
  wire [3:0] id_ex_1_aluop_2, \单周期硬布线控制器_1_alu_op ;
  wire [4:0] ex_mem_1_rd_num_2, id_ex_1_rd_num_2, multiplexer_2_out, multiplexer_3_out, WB_Rd;
  wire [7:0] bitselector_1_out;
  wire [11:0] multiplexer_4_out;
  wire [12:0] CNT_num;
  wire [15:0] bitselector_2_out, \DataHazzard次数 , \总周期数 , \插入气泡数 , \无条件分支数 , \条件分支成功数 ;
  wire [31:0] alu_1_result_2, bit_extender_1_out, bit_extender_2_out, bit_extender_3_out, bit_extender_4_out,
       bit_extender_5_out, bit_extender_6_out, bit_extender_7_out, EX_IR, ex_mem_1_result_2, EX_PCp4, EX_R1,
       EX_R2, id_ex_1_aluimm_2, id_ex_1_jmpimm_2, ID_IR, IF_IR, IF_PCp4, MEM_IR, mem_wb_1_memreaddata_2,
       mem_wb_1_result_2, multiplexer_1_out, multiplexer_5_out, multiplexer_6_out, multiplexer_7_out,
       multiplexer_8_out, multiplexer_9_out, multiplexer_10_out, PCRelJmp, ram_1_data, regifile_1_r1,
       regifile_1_r2, RegRelJmp, WB_IR;

  Button \u_总复位  (.out(RST));
  Button _1 (.out(IR1));
  Button _2 (.out(IR2));
  Button _3 (.out(IR3));
  // Probe on \总周期数 
  // Probe on \总周期数 
  BubbleGenerator bubblegenerator_1 (
    .Halt(halt), .R1Dep(\单周期硬布线控制器_1_r1dep ), .R2Dep(\单周期硬布线控制器_1_r2dep ), .EX_RegWrite(id_ex_1_regwrite_2),
    .MEM_RegWrite(ex_mem_1_regwrite_2), .EX_Rd(id_ex_1_rd_num_2), .MEM_Rd(ex_mem_1_rd_num_2),
    .R1(multiplexer_2_out), .R2(multiplexer_3_out), .IF_ID_EN(bubblegenerator_1_if_id_en),
    .PC_EN(bubblegenerator_1_pc_en), .IF_ID_FLUSH(bubblegenerator_1_if_id_flush),
    .ID_EX_FLUSH(bubblegenerator_1_id_ex_flush), .ID_EX_EN(bubblegenerator_1_id_ex_en), .Jmp(pctype_1_jmp),
    .EX_MEM_EN(bubblegenerator_1_ex_mem_en), .MEM_WB_EN(bubblegenerator_1_mem_wb_en),
    .DataHazzard(DataHazzard), .Flush(Flush));  // open: Stall
  Button \u_继续运行  (.out(Go));
  LED led_1 (.in(W1));
  LED led_2 (.in(W2));
  LED led_3 (.in(W3));
  // Probe on PCType
  Multiplexer #(.select(2), .width(32), .enable("false")) multiplexer_1 (
    .in0(IF_PCp4), .in2(RegRelJmp), .in3(PCRelJmp), .out(multiplexer_1_out), .sel(PCType));  // open: in1
  // Probe on multiplexer_1_out
  Hex_Digit_Display hex_digit_display_1 (.value(LedData[31:28]));  // open: dp
  // Probe on IF_PC[19:0]
  // RiscV_Probe riscv_probe_1: pin names not known; wires that end beside it: IF_IR
  Hex_Digit_Display hex_digit_display_2 (.value(LedData[23:20]));  // open: dp
  Hex_Digit_Display hex_digit_display_3 (.value(LedData[27:24]));  // open: dp
  // Probe on ID_PC[19:0]
  // RiscV_Probe riscv_probe_2: pin names not known; wires that end beside it: ID_IR
  Register #(.width(32), .Select("low")) PC (
    .D(multiplexer_1_out), .en(bubblegenerator_1_pc_en), .Q(IF_PC), .clk(CLK), .clr(RST));
  Hex_Digit_Display hex_digit_display_4 (.value(LedData[15:12]));  // open: dp
  Hex_Digit_Display hex_digit_display_5 (.value(LedData[19:16]));  // open: dp
  Hex_Digit_Display hex_digit_display_6 (.value(LedData[7:4]));  // open: dp
  Hex_Digit_Display hex_digit_display_7 (.value(LedData[11:8]));  // open: dp
  // Probe on EX_PC[19:0]
  // RiscV_Probe riscv_probe_3: pin names not known; wires that end beside it: EX_IR
  ROM #(.addrWidth(10), .dataWidth(32), .Select("high")) rom_1 (.addr(IF_PC[11:2]), .data(IF_IR));
  Adder #(.width(32)) adder_1 (.a(IF_PC), .b(32'h4), .out(IF_PCp4));  // open: cin, cout
  Hex_Digit_Display hex_digit_display_8 (.value(LedData[3:0]));  // open: dp
  IF_ID if_id_1 (
    .IR(IF_IR), .PC(IF_PC), .FLUSH(bubblegenerator_1_if_id_flush), .IR_2(ID_IR), .PC_2(ID_PC), .RST(RST),
    .EN(bubblegenerator_1_if_id_en), .CLK(CLK));  // open: PredictBranch, PredictBranch_2
  // Probe on \总周期数 
  // Probe on M_PC[19:0]
  // RiscV_Probe riscv_probe_4: pin names not known; wires that end beside it: MEM_IR
  // Probe on \总周期数 
  // Probe on \无条件分支数 
  // Probe on \条件分支成功数 
  // Probe on \插入气泡数 
  // Probe on \DataHazzard次数 
  \单周期硬布线控制器  \u_单周期硬布线控制器_1  (
    .Funct({ID_IR[30], ID_IR[25], ID_IR[14:12]}), .OP(ID_IR[6:2]), .ALU_OP(\单周期硬布线控制器_1_alu_op ),
    .MemToReg(\单周期硬布线控制器_1_memtoreg ), .MemWrite(\单周期硬布线控制器_1_memwrite ), .ALU_SRC(\单周期硬布线控制器_1_alu_src ),
    .RegWrite(\单周期硬布线控制器_1_regwrite ), .ecall(\单周期硬布线控制器_1_ecall ), .S_type(\单周期硬布线控制器_1_s_type ),
    .JALR(\单周期硬布线控制器_1_jalr ), .Beq(\单周期硬布线控制器_1_beq ), .JAL(JAL), .Bne(\单周期硬布线控制器_1_bne ), .in_3(ID_IR[21]),
    .uret(\单周期硬布线控制器_1_uret ), .Func3(\单周期硬布线控制器_1_func3 ), .ALU_RESULT(\单周期硬布线控制器_1_alu_result ),
    .Blt_u(\单周期硬布线控制器_1_blt_u ), .R1Dep(\单周期硬布线控制器_1_r1dep ), .R2Dep(\单周期硬布线控制器_1_r2dep ),
    .LegitIR(ID_IR[1:0]));  // open: CSR
  Multiplexer #(.width(5), .enable("false")) multiplexer_2 (
    .in0(ID_IR[19:15]), .in1(5'b01010), .out(multiplexer_2_out), .sel(\单周期硬布线控制器_1_ecall ));
  Multiplexer #(.width(5), .enable("false")) multiplexer_3 (
    .in0(ID_IR[24:20]), .in1(5'b10001), .out(multiplexer_3_out), .sel(\单周期硬布线控制器_1_ecall ));
  // Probe on IF_PC[11:0]
  // Probe on WB_PC[19:0]
  // RiscV_Probe riscv_probe_5: pin names not known; wires that end beside it: WB_IR
  // Probe on multiplexer_2_out
  // Probe on multiplexer_3_out
  // Probe on WB_Rd
  Multiplexer #(.width(12), .enable("false")) multiplexer_4 (
    .in0(ID_IR[31:20]), .in1({ID_IR[31:25], ID_IR[11:7]}), .out(multiplexer_4_out), .sel(\单周期硬布线控制器_1_s_type ));
  assign bit_extender_1_out = {{19{ID_IR[31]}}, {ID_IR[31], ID_IR[7], ID_IR[30:25], ID_IR[11:8], 1'b0}};  // Bit_Extender bit_extender_1
  Multiplexer #(.width(32), .enable("false")) multiplexer_5 (
    .in0(bit_extender_1_out), .in1(bit_extender_2_out), .out(multiplexer_5_out), .sel(JAL));
  assign bit_extender_2_out = {{11{ID_IR[31]}}, {ID_IR[31], ID_IR[19:12], ID_IR[20], ID_IR[30:21], 1'b0}};  // Bit_Extender bit_extender_2
  // Probe on ID_PC[11:0]
  // Probe on EX_PC[11:0]
  not not_1 (not_1_out, CLK);
  assign bit_extender_3_out = {{20{multiplexer_4_out[11]}}, multiplexer_4_out};  // Bit_Extender bit_extender_3
  // Probe on M_PC[11:0]
  D_Flip_Flop #(.trigger("high"), .Pre_Clr_Positions("LEGACY"), .enable("true"), .NewFFLayout("false")) d_ff_1 (.Q(d_ff_1_q));  // open: clk, D, Qn, preset, en, reset
  // Probe on 13'hc
  Regifile regifile_1 (
    .Din(RDin), .Clk(not_1_out), .R1(regifile_1_r1), .R2(regifile_1_r2), .WE(RegWrite), .W_num(WB_Rd),
    .R1_num(multiplexer_2_out), .R2_num(multiplexer_3_out));
  // Probe on bit_extender_3_out
  // Probe on WB_PC[11:0]
  Comparator #(.width(13)) comparator_1 (
    .a(CNT_num), .b(13'hc), .eq(comparator_1_eq), .lt(comparator_1_lt));  // open: gt
  Clock clock_1 (.out(clock_1_out));
  ID_EX id_ex_1 (
    .IR(ID_IR), .PC(ID_PC), .FLUSH(bubblegenerator_1_id_ex_flush), .IR_2(EX_IR), .PC_2(EX_PC), .RST(RST),
    .EN(bubblegenerator_1_id_ex_en), .CLK(CLK), .URET(\单周期硬布线控制器_1_uret ), .URET_2(id_ex_1_uret_2),
    .JALR(\单周期硬布线控制器_1_jalr ), .JALR_2(id_ex_1_jalr_2), .JAL(JAL), .JAL_2(id_ex_1_jal_2),
    .BEQ(\单周期硬布线控制器_1_beq ), .BEQ_2(id_ex_1_beq_2), .BNE(\单周期硬布线控制器_1_bne ), .BNE_2(id_ex_1_bne_2),
    .BLT_U(\单周期硬布线控制器_1_blt_u ), .BLT_U_2(id_ex_1_blt_u_2), .MemToReg(\单周期硬布线控制器_1_memtoreg ),
    .MemToReg_2(id_ex_1_memtoreg_2), .MemWrite(\单周期硬布线控制器_1_memwrite ), .MemWrite_2(id_ex_1_memwrite_2),
    .AluOP(\单周期硬布线控制器_1_alu_op ), .AluOP_2(id_ex_1_aluop_2), .AluResult(\单周期硬布线控制器_1_alu_result ),
    .AluResult_2(pctype_1_linktoreg[1]), .AluSrcB(\单周期硬布线控制器_1_alu_src ), .AluSrcB_2(id_ex_1_alusrcb_2),
    .RegWrite(\单周期硬布线控制器_1_regwrite ), .RegWrite_2(id_ex_1_regwrite_2), .MemVariant(\单周期硬布线控制器_1_func3 ),
    .MemVariant_2(id_ex_1_memvariant_2), .Rd_num(ID_IR[11:7]), .Rd_num_2(id_ex_1_rd_num_2),
    .ECALL(\单周期硬布线控制器_1_ecall ), .ECALL_2(EX_ECALL), .JmpImm(multiplexer_5_out), .JmpImm_2(id_ex_1_jmpimm_2),
    .AluImm(bit_extender_3_out), .AluImm_2(id_ex_1_aluimm_2), .R2(regifile_1_r2), .R2_2(EX_R2),
    .R1(regifile_1_r1), .R1_2(EX_R1));  // open: PredictBranch, PredictBranch_2, R1ForwardSrc, R1ForwardSrc_2, R2ForwardSrc, R2ForwardSrc_2
  nand nand_1 (nand_1_out, d_ff_1_q, comparator_1_eq);
  Counter #(.width(13), .max('h1fff), .ongoal("stay"), .behavior("old")) counter_1 (
    .count(comparator_1_lt), .Q(CNT_num), .clk(clock_1_out));  // open: load, D, carry, clr, preset
  Adder #(.width(32)) adder_2 (.a(id_ex_1_jmpimm_2), .b(EX_PC), .out(PCRelJmp));  // open: cin, cout
  assign CLK = nand_1_out ? clock_1_out : 1'bz;  // Controlled_Buffer controlled_buffer_1
  PCType pctype_1 (
    .JmpType(PCType), .Jmp(pctype_1_jmp), .Eq(Eq), .Lt(Lt), .Ge(Ge), .URET(id_ex_1_uret_2),
    .JALR(id_ex_1_jalr_2), .JAL(id_ex_1_jal_2), .BEQ(id_ex_1_beq_2), .BNE(id_ex_1_bne_2),
    .BLT_U(id_ex_1_blt_u_2), .LinkToReg(pctype_1_linktoreg[0]), .UncondJmp(UncondJmp), .CondBranch(CondBranch));  // open: ImmJmp, UncertainJmp, BranchInstr
  Multiplexer #(.width(32), .enable("false")) multiplexer_6 (
    .in0(EX_R2), .in1(id_ex_1_aluimm_2), .out(multiplexer_6_out), .sel(id_ex_1_alusrcb_2));
  Adder #(.width(32)) adder_3 (.a(EX_PC), .b(32'h4), .out(EX_PCp4));  // open: cin, cout
  Pull_Resistor #(.pull(1)) pull_resistor_1 (.node(CLK));
  ALU alu_1 (
    .X(EX_R1), .Y(multiplexer_6_out), .AluOP(id_ex_1_aluop_2), .Equal(Eq), .Result(RegRelJmp),
    .Result_2(alu_1_result_2), .out_4(Ge), .out_6(Lt));
  Multiplexer #(.select(2), .width(32), .enable("false")) multiplexer_7 (
    .in0(RegRelJmp), .in1(EX_PCp4), .in2(alu_1_result_2), .out(multiplexer_7_out), .sel(pctype_1_linktoreg));  // open: in3
  EX_MEM ex_mem_1 (
    .EN(bubblegenerator_1_ex_mem_en), .MemToReg(id_ex_1_memtoreg_2), .MemToReg_2(ex_mem_1_memtoreg_2),
    .MemWrite(id_ex_1_memwrite_2), .MemWrite_2(MemWrite), .RegWrite(id_ex_1_regwrite_2),
    .RegWrite_2(ex_mem_1_regwrite_2), .MemVariant(id_ex_1_memvariant_2),
    .MemVariant_2(ex_mem_1_memvariant_2), .Halt(EX_Halt), .Halt_2(ex_mem_1_halt_2),
    .Result(multiplexer_7_out), .Result_2(ex_mem_1_result_2), .MemWriteData(EX_R2), .MemWriteData_2(MDin),
    .Rd_num(id_ex_1_rd_num_2), .Rd_num_2(ex_mem_1_rd_num_2), .IR(EX_IR), .IR_2(MEM_IR), .PC(EX_PC),
    .PC_2(M_PC), .FLUSH(1'b0), .RST(RST), .CLK(CLK));
  // Probe on ex_mem_1_result_2
  BitSelector #(.width(32), .group(8)) bitselector_1 (
    .in(ram_1_data), .out(bitselector_1_out), .sel(ex_mem_1_result_2[1:0]));
  RAM #(.addrWidth(10), .dataWidth(32), .bus("separate"), .Select("high"), .simpleMode("false")) ram_1 (
    .addr(ex_mem_1_result_2[11:2]), .din(MDin), .data(ram_1_data), .str(MemWrite), .sel(1'b1), .clk(CLK),
    .clr(RST));  // open: ld
  BitSelector #(.width(32), .group(16)) bitselector_2 (
    .in(ram_1_data), .out(bitselector_2_out), .sel(ex_mem_1_result_2[1]));
  assign bit_extender_4_out = {{24{bitselector_1_out[7]}}, bitselector_1_out};  // Bit_Extender bit_extender_4
  Multiplexer #(.width(32), .enable("false")) multiplexer_8 (
    .in0(bit_extender_4_out), .in1(bit_extender_5_out), .out(multiplexer_8_out),
    .sel(ex_mem_1_memvariant_2[2]));
  assign bit_extender_5_out = {{24{1'b0}}, bitselector_1_out};  // Bit_Extender bit_extender_5
  assign bit_extender_6_out = {{16{bitselector_2_out[15]}}, bitselector_2_out};  // Bit_Extender bit_extender_6
  Multiplexer #(.width(32), .enable("false")) multiplexer_9 (
    .in0(bit_extender_6_out), .in1(bit_extender_7_out), .out(multiplexer_9_out),
    .sel(ex_mem_1_memvariant_2[2]));
  assign bit_extender_7_out = {{16{1'b0}}, bitselector_2_out};  // Bit_Extender bit_extender_7
  Multiplexer #(.select(2), .width(32), .enable("false")) multiplexer_10 (
    .in0(multiplexer_8_out), .in1(multiplexer_9_out), .in2(ram_1_data), .out(multiplexer_10_out),
    .sel(ex_mem_1_memvariant_2[1:0]));  // open: in3
  MEM_WB mem_wb_1 (
    .EN(bubblegenerator_1_mem_wb_en), .MemToReg(ex_mem_1_memtoreg_2), .MemToReg_2(mem_wb_1_memtoreg_2),
    .RegWrite(ex_mem_1_regwrite_2), .RegWrite_2(RegWrite), .Halt(ex_mem_1_halt_2), .Halt_2(mem_wb_1_halt_2),
    .Result(ex_mem_1_result_2), .Result_2(mem_wb_1_result_2), .MemReadData(multiplexer_10_out),
    .MemReadData_2(mem_wb_1_memreaddata_2), .Rd_num(ex_mem_1_rd_num_2), .Rd_num_2(WB_Rd), .IR(MEM_IR),
    .IR_2(WB_IR), .PC(M_PC), .PC_2(WB_PC), .FLUSH(1'b0), .RST(RST), .CLK(CLK));
  // Probe on mem_wb_1_memtoreg_2
  Multiplexer #(.width(32), .enable("false")) multiplexer_11 (
    .in0(mem_wb_1_result_2), .in1(mem_wb_1_memreaddata_2), .out(RDin), .sel(mem_wb_1_memtoreg_2));
  // Probe on RDin
  S_R_Flip_Flop #(.trigger("latch")) s_r_ff_1 (
    .S(mem_wb_1_halt_2), .R(1'b0), .Q(halt), .reset(or_1_out));  // open: Qn, preset
  or or_1 (or_1_out, Go, RST);
  not not_2 (not_2_out, halt);
  Counter #(.width(16), .max('hffff)) NXC (
    .count(not_2_out), .Q(\总周期数 ), .clk(CLK), .clr(RST));  // open: load, D, carry, preset, down
  and and_1 (and_1_out, ~halt, UncondJmp);  // AND_Gate
  Counter #(.width(16), .max('hffff)) counter_2 (
    .count(and_1_out), .Q(\无条件分支数 ), .clk(CLK), .clr(RST));  // open: load, D, carry, preset, down
  Comparator #(.width(32)) comparator_2 (.a(EX_R2), .b(32'h22), .eq(comparator_2_eq));  // open: gt, lt
  and and_2 (and_2_out, EX_ECALL, comparator_2_eq);
  and and_3 (EX_Halt, ~comparator_2_eq, EX_ECALL);  // AND_Gate
  and and_4 (and_4_out, ~halt, CondBranch);  // AND_Gate
  and and_5 (and_5_out, ~halt, DataHazzard);  // AND_Gate
  Register #(.width(32), .Select("low")) register_1 (.D(EX_R1), .en(and_2_out), .Q(LedData), .clk(CLK), .clr(RST));
  Counter #(.width(16), .max('hffff)) counter_3 (
    .count(and_4_out), .Q(\条件分支成功数 ), .clk(CLK), .clr(RST));  // open: load, D, carry, preset, down
  Counter #(.width(16), .max('hffff)) counter_4 (
    .count(and_5_out), .Q(\DataHazzard次数 ), .clk(CLK), .clr(RST));  // open: load, D, carry, preset, down
  and and_6 (and_6_out, ~halt, Flush);  // AND_Gate
  Counter #(.width(16), .max('hffff)) counter_5 (
    .count(and_6_out), .Q(\插入气泡数 ), .clk(CLK), .clr(RST));  // open: load, D, carry, preset, down

  // Other names for the same wires on the sheet: MEM_PC[31:0] = M_PC

  // Notes on the sheet:
  //   中断源
  //   时空图监测，可删除
  //   中断等待指示
  //   数码管输出
  //   指令存储器
  //   contents of rom_1 (hex, n*v repeats v):
  //   100493 100006f 100493 200913 300993 100006f 100493 200913 300993 100006f 100493 200913 300993
  //   100006f 100493 200913 300993 3c4000ef 100413 100493 1f49493 900533 2200893 73 24d493 48463 fedff06f
  //   900533 2200893 73 100493 249493 900533 2200893 73 48463 fedff06f 100493 1f49493 900533 2200893 73
  //   4034d493 900533 2200893 73 4044d493 900533 2200893 73 4044d493 900533 2200893 73 4044d493 900533
  //   2200893 73 4044d493 900533 2200893 73 4044d493 900533 2200893 73 4044d493 900533 2200893 73 4044d493
  //   900533 2200893 73 100413 1f41993 41f9d993 433 c00913 300b13 140413 f47413 800293 100313 499993
  //   89e9b3 1300533 2200893 73 406282b3 fe0294e3 140413 f00f93 1f47433 1c41413 800293 100313 49d993
  //   89e9b3 1300533 2200893 73 406282b3 fe0294e3 1c45413 406b0b33 b0463 f95ff06f 2b3 fff2c293 829293
  //   ff2e293 500533 2200893 73 fff00413 493 84a023 140413 448493 84a023 140413 448493 84a023 140413
  //   448493 84a023 140413 448493 84a023 140413 448493 84a023 140413 448493 84a023 140413 448493 84a023
  //   140413 448493 84a023 140413 448493 84a023 140413 448493 84a023 140413 448493 84a023 140413 448493
  //   84a023 140413 448493 84a023 140413 448493 84a023 140413 448493 84a023 140413 448493 140413 433
  //   3c00493 42983 4aa03 149a2b3 28663 134a023 1442023 ffc48493 fe9412e3 800533 2200893 73 440413 3c00493
  //   fc9416e3 3200893 73 200293 1100493 849493 1148493 1049493 900533 2200893 73 1c00e13 254d4b3 900533
  //   2200893 73 fffe0e13 fe0e16e3 a00893 73 8800493 849493 4848493 8700913 891913 5490913 2997933 1091913
  //   11096913 1200533 2200893 73 a00893 73 313 1000e13 8400493 849493 8348493 400913 891913 490913 849493
  //   8248493 849493 8148493 891913 490913 891913 490913 932023 12484b3 430313 fffe0e13 fe0e18e3 2000e13
  //   313 30483 900533 2200893 73 130313 fffe0e13 fe0e14e3 a00893 73 ff100493 900533 2200893 73 148493
  //   fe9068e3 900533 2200893 73 a00893 73 413 140413 800533 2200893 73 240413 800533 2200893 73 340413
  //   800533 2200893 73 440413 800533 2200893 73 540413 800533 2200893 73 640413 800533 2200893 73 740413
  //   800533 2200893 73 840413 800533 2200893 2200893 73 8067
  //   Rd[4:0]
  //   JALR
  //   URET
  //   I-Imm[11:0]
  //   S-Imm[11:0]
  //   B-Imm[12:1]
  //   J-Imm[20:1]
  //   JAL
  //   Beq
  //   Bne
  //   Blt[u]
  //   MemToReg
  //   MemWrite
  //   AluOP
  //   AluResult
  //   AluSrcB
  //   RegWrite
  //   MemVariant
  //   I/S-ImmType
  //   控制位
  //   流水调试日志用
  //   暂停节拍，不能为0
  //   戳工具置1进入计数暂停模式，ctrl+k时钟自动运行到对应节拍暂停
  //   ctrl+k关闭时钟连续运行，将控制位置零，进入单步调试模式调试
  //   用这个时钟源需要去掉电路中的其他时钟源
  //   可计数暂停的时钟源
  //   为方便自动评测，需要输出流水线各段保存的PC值，注意是PC不是PC+4，另外ID段寄存器写入信息，Mem段内存写入信息也要输出
  //   数据存储器
endmodule

module ForwardBubbleGen (
  input  Halt,
  input  R1Dep,
  input  EX_RegWrite,
  input  [4:0] EX_Rd,
  input  [4:0] R1,
  input  PredictFail,
  input  Jmp,
  input  R2Dep,
  input  MEM_RegWrite,
  input  [4:0] MEM_Rd,
  input  [4:0] R2,
  input  Intr,
  input  EX_MemToReg,
  output Stall,
  output PC_EN,
  output IF_ID_EN,
  output IF_ID_FLUSH,
  output ID_EX_FLUSH,
  output [1:0] R1ForwardSrc,
  output ID_EX_EN,
  output EX_MEM_EN,
  output MEM_WB_EN,
  output Flush,
  output LoadUse,
  output [1:0] R2ForwardSrc
);

  wire and_1_out, and_2_out, and_3_out, and_4_out, comparator_1_eq, comparator_2_eq, comparator_3_eq,
       comparator_4_eq, comparator_5_eq, comparator_6_eq, comparator_7_eq, comparator_8_eq, or_1_out;

  Comparator #(.width(5)) comparator_1 (.a({5{1'b0}}), .b(R1), .eq(comparator_1_eq));  // open: gt, lt
  Comparator #(.width(5)) comparator_2 (.a(R1), .b(EX_Rd), .eq(comparator_2_eq));  // open: gt, lt
  Comparator #(.width(5)) comparator_3 (.a({5{1'b0}}), .b(R1), .eq(comparator_3_eq));  // open: gt, lt
  Comparator #(.width(5)) comparator_4 (.a(R1), .b(MEM_Rd), .eq(comparator_4_eq));  // open: gt, lt
  Comparator #(.width(5)) comparator_5 (.a({5{1'b0}}), .b(R2), .eq(comparator_5_eq));  // open: gt, lt
  Comparator #(.width(5)) comparator_6 (.a(R2), .b(EX_Rd), .eq(comparator_6_eq));  // open: gt, lt
  Comparator #(.width(5)) comparator_7 (.a({5{1'b0}}), .b(R2), .eq(comparator_7_eq));  // open: gt, lt
  Comparator #(.width(5)) comparator_8 (.a(R2), .b(MEM_Rd), .eq(comparator_8_eq));  // open: gt, lt
  and and_1 (and_1_out, R1Dep, ~comparator_1_eq, comparator_2_eq, EX_RegWrite);  // AND_Gate
  and and_2 (and_2_out, R1Dep, ~comparator_3_eq, comparator_4_eq, MEM_RegWrite);  // AND_Gate
  and and_3 (and_3_out, R2Dep, ~comparator_5_eq, comparator_6_eq, EX_RegWrite);  // AND_Gate
  and and_4 (and_4_out, R2Dep, ~comparator_7_eq, comparator_8_eq, MEM_RegWrite);  // AND_Gate
  or or_1 (or_1_out, and_1_out, and_3_out);
  Priority_Encoder #(.select(2)) priority_encoder_1 (
    .in0(1'b1), .in1(and_2_out), .in2(and_1_out), .out(R1ForwardSrc));  // open: in3, gs, en_out, en_in
  Priority_Encoder #(.select(2)) priority_encoder_2 (
    .in0(1'b1), .in1(and_4_out), .in2(and_3_out), .out(R2ForwardSrc));  // open: in3, gs, en_out, en_in
  and and_5 (LoadUse, or_1_out, EX_MemToReg);
  not not_1 (Stall, IF_ID_EN);
  nor nor_1 (IF_ID_EN, Halt, LoadUse);
  or or_2 (Flush, Jmp, LoadUse);
  not not_2 (EX_MEM_EN, Halt);
  Pull_Resistor pull_resistor_1 (.node(PredictFail));
  Pull_Resistor pull_resistor_2 (.node(Intr));

  assign ID_EX_EN = EX_MEM_EN;
  assign ID_EX_FLUSH = Flush;
  assign IF_ID_FLUSH = Jmp;
  assign MEM_WB_EN = EX_MEM_EN;
  assign PC_EN = IF_ID_EN;
endmodule

module \重定向流水线  (
  output RegWrite,
  output MemWrite,
  output [31:0] IF_PC,
  output [31:0] ID_PC,
  output [31:0] EX_PC,
  output [31:0] M_PC,
  output [31:0] WB_PC,
  output [31:0] RDin,
  output [31:0] MDin,
  output [31:0] LedData
);

  wire and_1_out, and_2_out, and_4_out, and_5_out, and_6_out, CLK, clock_1_out, comparator_1_eq,
       comparator_1_lt, comparator_2_eq, CondBranch, d_ff_1_q, Eq, EX_ECALL, EX_Halt, ex_mem_1_halt_2,
       ex_mem_1_memtoreg_2, ex_mem_1_regwrite_2, Flush, forwardbubblegen_1_ex_mem_en,
       forwardbubblegen_1_id_ex_en, forwardbubblegen_1_id_ex_flush, forwardbubblegen_1_if_id_en,
       forwardbubblegen_1_if_id_flush, forwardbubblegen_1_mem_wb_en, forwardbubblegen_1_pc_en, Ge, Go, halt,
       id_ex_1_alusrcb_2, id_ex_1_beq_2, id_ex_1_blt_u_2, id_ex_1_bne_2, id_ex_1_jal_2, id_ex_1_jalr_2,
       id_ex_1_memtoreg_2, id_ex_1_memwrite_2, id_ex_1_regwrite_2, id_ex_1_uret_2, IR1, IR2, IR3, JAL,
       LoadUse, Lt, mem_wb_1_halt_2, mem_wb_1_memtoreg_2, nand_1_out, not_1_out, not_2_out, or_1_out,
       pctype_1_jmp, pull_resistor_1_node, pull_resistor_2_node, RST, UncondJmp, W1, W2, W3,
       \单周期硬布线控制器_1_alu_result , \单周期硬布线控制器_1_alu_src , \单周期硬布线控制器_1_beq , \单周期硬布线控制器_1_blt_u ,
       \单周期硬布线控制器_1_bne , \单周期硬布线控制器_1_ecall , \单周期硬布线控制器_1_jalr , \单周期硬布线控制器_1_memtoreg ,
       \单周期硬布线控制器_1_memwrite , \单周期硬布线控制器_1_r1dep , \单周期硬布线控制器_1_r2dep , \单周期硬布线控制器_1_regwrite ,
       \单周期硬布线控制器_1_s_type , \单周期硬布线控制器_1_uret ;
  wire [1:0] forwardbubblegen_1_r1forwardsrc, forwardbubblegen_1_r2forwardsrc, id_ex_1_r1forwardsrc_2,
       id_ex_1_r2forwardsrc_2, PCType, pctype_1_linktoreg;
  wire [2:0] ex_mem_1_memvariant_2, id_ex_1_memvariant_2, \单周期硬布线控制器_1_func3 ;
  wire [3:0] id_ex_1_aluop_2, \单周期硬布线控制器_1_alu_op ;
  wire [4:0] ex_mem_1_rd_num_2, id_ex_1_rd_num_2, multiplexer_2_out, multiplexer_3_out, WB_Rd;
  wire [7:0] bitselector_1_out;
  wire [11:0] multiplexer_4_out;
  wire [12:0] CNT_num;
  wire [15:0] bitselector_2_out, \LoadUse次数 , \总周期数 , \插入气泡数 , \无条件分支数 , \条件分支成功数 ;
  wire [31:0] alu_1_result_2, bit_extender_1_out, bit_extender_2_out, bit_extender_3_out, bit_extender_4_out,
       bit_extender_5_out, bit_extender_6_out, bit_extender_7_out, EX_IR, EX_PCp4, EX_R1, EX_R2,
       id_ex_1_aluimm_2, id_ex_1_jmpimm_2, id_ex_1_r1_2, id_ex_1_r2_2, ID_IR, IF_IR, IF_PCp4, MEM_IR,
       MEM_RDin, mem_wb_1_memreaddata_2, mem_wb_1_result_2, multiplexer_1_out, multiplexer_5_out,
       multiplexer_8_out, multiplexer_9_out, multiplexer_10_out, multiplexer_11_out, multiplexer_12_out,
       PCRelJmp, ram_1_data, regifile_1_r1, regifile_1_r2, RegRelJmp, WB_IR;

  Button \u_总复位  (.out(RST));
  Button _1 (.out(IR1));
  Button _2 (.out(IR2));
  Button _3 (.out(IR3));
  // Probe on \总周期数 
  // Probe on \总周期数 
  ForwardBubbleGen forwardbubblegen_1 (
    .Halt(halt), .R1Dep(\单周期硬布线控制器_1_r1dep ), .EX_RegWrite(id_ex_1_regwrite_2), .EX_Rd(id_ex_1_rd_num_2),
    .R1(multiplexer_2_out), .Jmp(pctype_1_jmp), .R2Dep(\单周期硬布线控制器_1_r2dep ),
    .MEM_RegWrite(ex_mem_1_regwrite_2), .MEM_Rd(ex_mem_1_rd_num_2), .R2(multiplexer_3_out),
    .PC_EN(forwardbubblegen_1_pc_en), .IF_ID_EN(forwardbubblegen_1_if_id_en),
    .IF_ID_FLUSH(forwardbubblegen_1_if_id_flush), .ID_EX_FLUSH(forwardbubblegen_1_id_ex_flush),
    .ID_EX_EN(forwardbubblegen_1_id_ex_en), .EX_MEM_EN(forwardbubblegen_1_ex_mem_en),
    .MEM_WB_EN(forwardbubblegen_1_mem_wb_en), .R1ForwardSrc(forwardbubblegen_1_r1forwardsrc),
    .R2ForwardSrc(forwardbubblegen_1_r2forwardsrc), .EX_MemToReg(id_ex_1_memtoreg_2), .LoadUse(LoadUse),
    .Flush(Flush), .Intr(pull_resistor_2_node), .PredictFail(pull_resistor_1_node));  // open: Stall
  Button \u_继续运行  (.out(Go));
  LED led_1 (.in(W1));
  LED led_2 (.in(W2));
  LED led_3 (.in(W3));
  Pull_Resistor pull_resistor_1 (.node(pull_resistor_1_node));
  Pull_Resistor pull_resistor_2 (.node(pull_resistor_2_node));
  // Probe on PCType
  Multiplexer #(.select(2), .width(32), .enable("false")) multiplexer_1 (
    .in0(IF_PCp4), .in2(RegRelJmp), .in3(PCRelJmp), .out(multiplexer_1_out), .sel(PCType));  // open: in1
  // Probe on multiplexer_1_out
  Hex_Digit_Display hex_digit_display_1 (.value(LedData[31:28]));  // open: dp
  // Probe on IF_PC[19:0]
  // RiscV_Probe riscv_probe_1: pin names not known; wires that end beside it: IF_IR
  Hex_Digit_Display hex_digit_display_2 (.value(LedData[27:24]));  // open: dp
  Hex_Digit_Display hex_digit_display_3 (.value(LedData[23:20]));  // open: dp
  // Probe on ID_PC[19:0]
  // RiscV_Probe riscv_probe_2: pin names not known; wires that end beside it: ID_IR
  Register #(.width(32), .Select("low")) PC (
    .D(multiplexer_1_out), .en(forwardbubblegen_1_pc_en), .Q(IF_PC), .clk(CLK), .clr(RST));
  Hex_Digit_Display hex_digit_display_4 (.value(LedData[19:16]));  // open: dp
  Hex_Digit_Display hex_digit_display_5 (.value(LedData[15:12]));  // open: dp
  Hex_Digit_Display hex_digit_display_6 (.value(LedData[11:8]));  // open: dp
  Hex_Digit_Display hex_digit_display_7 (.value(LedData[7:4]));  // open: dp
  // Probe on EX_PC[19:0]
  // RiscV_Probe riscv_probe_3: pin names not known; wires that end beside it: EX_IR
  ROM #(.addrWidth(10), .dataWidth(32), .Select("high")) rom_1 (.addr(IF_PC[11:2]), .data(IF_IR));
  Adder #(.width(32)) adder_1 (.a(IF_PC), .b(32'h4), .out(IF_PCp4));  // open: cin, cout
  Hex_Digit_Display hex_digit_display_8 (.value(LedData[3:0]));  // open: dp
  IF_ID if_id_1 (
    .IR(IF_IR), .PC(IF_PC), .FLUSH(forwardbubblegen_1_if_id_flush), .IR_2(ID_IR), .PC_2(ID_PC), .RST(RST),
    .EN(forwardbubblegen_1_if_id_en), .CLK(CLK));  // open: PredictBranch, PredictBranch_2
  // Probe on \总周期数 
  // Probe on M_PC[19:0]
  // RiscV_Probe riscv_probe_4: pin names not known; wires that end beside it: MEM_IR
  // Probe on \总周期数 
  // Probe on \无条件分支数 
  // Probe on \条件分支成功数 
  // Probe on \插入气泡数 
  // Probe on \LoadUse次数 
  \单周期硬布线控制器  \u_单周期硬布线控制器_1  (
    .Funct({ID_IR[30], ID_IR[25], ID_IR[14:12]}), .OP(ID_IR[6:2]), .ALU_OP(\单周期硬布线控制器_1_alu_op ),
    .MemToReg(\单周期硬布线控制器_1_memtoreg ), .MemWrite(\单周期硬布线控制器_1_memwrite ), .ALU_SRC(\单周期硬布线控制器_1_alu_src ),
    .RegWrite(\单周期硬布线控制器_1_regwrite ), .ecall(\单周期硬布线控制器_1_ecall ), .S_type(\单周期硬布线控制器_1_s_type ),
    .JALR(\单周期硬布线控制器_1_jalr ), .Beq(\单周期硬布线控制器_1_beq ), .JAL(JAL), .Bne(\单周期硬布线控制器_1_bne ), .in_3(ID_IR[21]),
    .uret(\单周期硬布线控制器_1_uret ), .Func3(\单周期硬布线控制器_1_func3 ), .ALU_RESULT(\单周期硬布线控制器_1_alu_result ),
    .Blt_u(\单周期硬布线控制器_1_blt_u ), .R1Dep(\单周期硬布线控制器_1_r1dep ), .R2Dep(\单周期硬布线控制器_1_r2dep ),
    .LegitIR(ID_IR[1:0]));  // open: CSR
  Multiplexer #(.width(5), .enable("false")) multiplexer_2 (
    .in0(ID_IR[19:15]), .in1(5'b01010), .out(multiplexer_2_out), .sel(\单周期硬布线控制器_1_ecall ));
  Multiplexer #(.width(5), .enable("false")) multiplexer_3 (
    .in0(ID_IR[24:20]), .in1(5'b10001), .out(multiplexer_3_out), .sel(\单周期硬布线控制器_1_ecall ));
  // Probe on IF_PC[11:0]
  // Probe on WB_PC[19:0]
  // RiscV_Probe riscv_probe_5: pin names not known; wires that end beside it: WB_IR
  // Probe on multiplexer_2_out
  // Probe on multiplexer_3_out
  // Probe on WB_Rd
  Multiplexer #(.width(12), .enable("false")) multiplexer_4 (
    .in0(ID_IR[31:20]), .in1({ID_IR[31:25], ID_IR[11:7]}), .out(multiplexer_4_out), .sel(\单周期硬布线控制器_1_s_type ));
  assign bit_extender_1_out = {{19{ID_IR[31]}}, {ID_IR[31], ID_IR[7], ID_IR[30:25], ID_IR[11:8], 1'b0}};  // Bit_Extender bit_extender_1
  Multiplexer #(.width(32), .enable("false")) multiplexer_5 (
    .in0(bit_extender_1_out), .in1(bit_extender_2_out), .out(multiplexer_5_out), .sel(JAL));
  assign bit_extender_2_out = {{11{ID_IR[31]}}, {ID_IR[31], ID_IR[19:12], ID_IR[20], ID_IR[30:21], 1'b0}};  // Bit_Extender bit_extender_2
  // Probe on EX_PC[11:0]
  // Probe on ID_PC[11:0]
  not not_1 (not_1_out, CLK);
  assign bit_extender_3_out = {{20{multiplexer_4_out[11]}}, multiplexer_4_out};  // Bit_Extender bit_extender_3
  // Probe on M_PC[11:0]
  D_Flip_Flop #(.trigger("high"), .Pre_Clr_Positions("LEGACY"), .enable("true"), .NewFFLayout("false")) d_ff_1 (.Q(d_ff_1_q));  // open: clk, D, Qn, preset, en, reset
  // Probe on 13'h33a
  Regifile regifile_1 (
    .Din(RDin), .Clk(not_1_out), .R1(regifile_1_r1), .R2(regifile_1_r2), .WE(RegWrite), .W_num(WB_Rd),
    .R1_num(multiplexer_2_out), .R2_num(multiplexer_3_out));
  // Probe on bit_extender_3_out
  // Probe on WB_PC[11:0]
  Comparator #(.width(13)) comparator_1 (
    .a(CNT_num), .b(13'h33a), .eq(comparator_1_eq), .lt(comparator_1_lt));  // open: gt
  Clock clock_1 (.out(clock_1_out));
  ID_EX id_ex_1 (
    .IR(ID_IR), .PC(ID_PC), .FLUSH(forwardbubblegen_1_id_ex_flush), .IR_2(EX_IR), .PC_2(EX_PC), .RST(RST),
    .EN(forwardbubblegen_1_id_ex_en), .CLK(CLK), .URET(\单周期硬布线控制器_1_uret ), .URET_2(id_ex_1_uret_2),
    .JALR(\单周期硬布线控制器_1_jalr ), .JALR_2(id_ex_1_jalr_2), .JAL(JAL), .JAL_2(id_ex_1_jal_2),
    .BEQ(\单周期硬布线控制器_1_beq ), .BEQ_2(id_ex_1_beq_2), .BNE(\单周期硬布线控制器_1_bne ), .BNE_2(id_ex_1_bne_2),
    .BLT_U(\单周期硬布线控制器_1_blt_u ), .BLT_U_2(id_ex_1_blt_u_2), .MemToReg(\单周期硬布线控制器_1_memtoreg ),
    .MemToReg_2(id_ex_1_memtoreg_2), .MemWrite(\单周期硬布线控制器_1_memwrite ), .MemWrite_2(id_ex_1_memwrite_2),
    .AluOP(\单周期硬布线控制器_1_alu_op ), .AluOP_2(id_ex_1_aluop_2), .AluResult(\单周期硬布线控制器_1_alu_result ),
    .AluResult_2(pctype_1_linktoreg[1]), .AluSrcB(\单周期硬布线控制器_1_alu_src ), .AluSrcB_2(id_ex_1_alusrcb_2),
    .RegWrite(\单周期硬布线控制器_1_regwrite ), .RegWrite_2(id_ex_1_regwrite_2), .MemVariant(\单周期硬布线控制器_1_func3 ),
    .MemVariant_2(id_ex_1_memvariant_2), .Rd_num(ID_IR[11:7]), .Rd_num_2(id_ex_1_rd_num_2),
    .ECALL(\单周期硬布线控制器_1_ecall ), .ECALL_2(EX_ECALL), .JmpImm(multiplexer_5_out), .JmpImm_2(id_ex_1_jmpimm_2),
    .AluImm(bit_extender_3_out), .AluImm_2(id_ex_1_aluimm_2), .R2(regifile_1_r2), .R2_2(id_ex_1_r2_2),
    .R1(regifile_1_r1), .R1_2(id_ex_1_r1_2), .R1ForwardSrc(forwardbubblegen_1_r1forwardsrc),
    .R1ForwardSrc_2(id_ex_1_r1forwardsrc_2), .R2ForwardSrc(forwardbubblegen_1_r2forwardsrc),
    .R2ForwardSrc_2(id_ex_1_r2forwardsrc_2));  // open: PredictBranch, PredictBranch_2
  nand nand_1 (nand_1_out, d_ff_1_q, comparator_1_eq);
  Counter #(.width(13), .max('h1fff), .ongoal("stay"), .behavior("old")) counter_1 (
    .count(comparator_1_lt), .Q(CNT_num), .clk(clock_1_out));  // open: load, D, carry, clr, preset
  Multiplexer #(.select(2), .width(32), .enable("false")) multiplexer_6 (
    .in0(id_ex_1_r1_2), .in1(RDin), .in2(MEM_RDin), .out(EX_R1), .sel(id_ex_1_r1forwardsrc_2));  // open: in3
  Adder #(.width(32)) adder_2 (.a(id_ex_1_jmpimm_2), .b(EX_PC), .out(PCRelJmp));  // open: cin, cout
  assign CLK = nand_1_out ? clock_1_out : 1'bz;  // Controlled_Buffer controlled_buffer_1
  PCType pctype_1 (
    .JmpType(PCType), .Jmp(pctype_1_jmp), .Eq(Eq), .Lt(Lt), .Ge(Ge), .URET(id_ex_1_uret_2),
    .JALR(id_ex_1_jalr_2), .JAL(id_ex_1_jal_2), .BEQ(id_ex_1_beq_2), .BNE(id_ex_1_bne_2),
    .BLT_U(id_ex_1_blt_u_2), .LinkToReg(pctype_1_linktoreg[0]), .UncondJmp(UncondJmp), .CondBranch(CondBranch));  // open: ImmJmp, UncertainJmp, BranchInstr
  Multiplexer #(.select(2), .width(32), .enable("false")) multiplexer_7 (
    .in0(id_ex_1_r2_2), .in1(RDin), .in2(MEM_RDin), .out(EX_R2), .sel(id_ex_1_r2forwardsrc_2));  // open: in3
  Multiplexer #(.width(32), .enable("false")) multiplexer_8 (
    .in0(EX_R2), .in1(id_ex_1_aluimm_2), .out(multiplexer_8_out), .sel(id_ex_1_alusrcb_2));
  Adder #(.width(32)) adder_3 (.a(EX_PC), .b(32'h4), .out(EX_PCp4));  // open: cin, cout
  Pull_Resistor #(.pull(1)) pull_resistor_3 (.node(CLK));
  ALU alu_1 (
    .X(EX_R1), .Y(multiplexer_8_out), .AluOP(id_ex_1_aluop_2), .Equal(Eq), .Result(RegRelJmp),
    .Result_2(alu_1_result_2), .out_4(Ge), .out_6(Lt));
  Multiplexer #(.select(2), .width(32), .enable("false")) multiplexer_9 (
    .in0(RegRelJmp), .in1(EX_PCp4), .in2(alu_1_result_2), .out(multiplexer_9_out), .sel(pctype_1_linktoreg));  // open: in3
  EX_MEM ex_mem_1 (
    .EN(forwardbubblegen_1_ex_mem_en), .MemToReg(id_ex_1_memtoreg_2), .MemToReg_2(ex_mem_1_memtoreg_2),
    .MemWrite(id_ex_1_memwrite_2), .MemWrite_2(MemWrite), .RegWrite(id_ex_1_regwrite_2),
    .RegWrite_2(ex_mem_1_regwrite_2), .MemVariant(id_ex_1_memvariant_2),
    .MemVariant_2(ex_mem_1_memvariant_2), .Halt(EX_Halt), .Halt_2(ex_mem_1_halt_2),
    .Result(multiplexer_9_out), .Result_2(MEM_RDin), .MemWriteData(EX_R2), .MemWriteData_2(MDin),
    .Rd_num(id_ex_1_rd_num_2), .Rd_num_2(ex_mem_1_rd_num_2), .IR(EX_IR), .IR_2(MEM_IR), .PC(EX_PC),
    .PC_2(M_PC), .FLUSH(1'b0), .RST(RST), .CLK(CLK));
  // Probe on MEM_RDin
  BitSelector #(.width(32), .group(8)) bitselector_1 (.in(ram_1_data), .out(bitselector_1_out), .sel(MEM_RDin[1:0]));
  RAM #(.addrWidth(10), .dataWidth(32), .bus("separate"), .Select("high"), .simpleMode("false")) ram_1 (
    .addr(MEM_RDin[11:2]), .din(MDin), .data(ram_1_data), .str(MemWrite), .sel(1'b1), .clk(CLK), .clr(RST));  // open: ld
  BitSelector #(.width(32), .group(16)) bitselector_2 (.in(ram_1_data), .out(bitselector_2_out), .sel(MEM_RDin[1]));
  assign bit_extender_4_out = {{24{bitselector_1_out[7]}}, bitselector_1_out};  // Bit_Extender bit_extender_4
  Multiplexer #(.width(32), .enable("false")) multiplexer_10 (
    .in0(bit_extender_4_out), .in1(bit_extender_5_out), .out(multiplexer_10_out),
    .sel(ex_mem_1_memvariant_2[2]));
  assign bit_extender_5_out = {{24{1'b0}}, bitselector_1_out};  // Bit_Extender bit_extender_5
  assign bit_extender_6_out = {{16{bitselector_2_out[15]}}, bitselector_2_out};  // Bit_Extender bit_extender_6
  Multiplexer #(.width(32), .enable("false")) multiplexer_11 (
    .in0(bit_extender_6_out), .in1(bit_extender_7_out), .out(multiplexer_11_out),
    .sel(ex_mem_1_memvariant_2[2]));
  assign bit_extender_7_out = {{16{1'b0}}, bitselector_2_out};  // Bit_Extender bit_extender_7
  Multiplexer #(.select(2), .width(32), .enable("false")) multiplexer_12 (
    .in0(multiplexer_10_out), .in1(multiplexer_11_out), .in2(ram_1_data), .out(multiplexer_12_out),
    .sel(ex_mem_1_memvariant_2[1:0]));  // open: in3
  MEM_WB mem_wb_1 (
    .EN(forwardbubblegen_1_mem_wb_en), .MemToReg(ex_mem_1_memtoreg_2), .MemToReg_2(mem_wb_1_memtoreg_2),
    .RegWrite(ex_mem_1_regwrite_2), .RegWrite_2(RegWrite), .Halt(ex_mem_1_halt_2), .Halt_2(mem_wb_1_halt_2),
    .Result(MEM_RDin), .Result_2(mem_wb_1_result_2), .MemReadData(multiplexer_12_out),
    .MemReadData_2(mem_wb_1_memreaddata_2), .Rd_num(ex_mem_1_rd_num_2), .Rd_num_2(WB_Rd), .IR(MEM_IR),
    .IR_2(WB_IR), .PC(M_PC), .PC_2(WB_PC), .FLUSH(1'b0), .RST(RST), .CLK(CLK));
  // Probe on mem_wb_1_memtoreg_2
  Multiplexer #(.width(32), .enable("false")) multiplexer_13 (
    .in0(mem_wb_1_result_2), .in1(mem_wb_1_memreaddata_2), .out(RDin), .sel(mem_wb_1_memtoreg_2));
  // Probe on RDin
  S_R_Flip_Flop #(.trigger("latch")) s_r_ff_1 (
    .S(mem_wb_1_halt_2), .R(1'b0), .Q(halt), .reset(or_1_out));  // open: Qn, preset
  or or_1 (or_1_out, Go, RST);
  not not_2 (not_2_out, halt);
  Counter #(.width(16), .max('hffff)) NXC (
    .count(not_2_out), .Q(\总周期数 ), .clk(CLK), .clr(RST));  // open: load, D, carry, preset, down
  and and_1 (and_1_out, ~halt, UncondJmp);  // AND_Gate
  Counter #(.width(16), .max('hffff)) counter_2 (
    .count(and_1_out), .Q(\无条件分支数 ), .clk(CLK), .clr(RST));  // open: load, D, carry, preset, down
  Comparator #(.width(32)) comparator_2 (.a(EX_R2), .b(32'h22), .eq(comparator_2_eq));  // open: gt, lt
  and and_2 (and_2_out, EX_ECALL, comparator_2_eq);
  and and_3 (EX_Halt, ~comparator_2_eq, EX_ECALL);  // AND_Gate
  and and_4 (and_4_out, ~halt, CondBranch);  // AND_Gate
  and and_5 (and_5_out, ~halt, LoadUse);  // AND_Gate
  Register #(.width(32), .Select("low")) register_1 (.D(EX_R1), .en(and_2_out), .Q(LedData), .clk(CLK), .clr(RST));
  Counter #(.width(16), .max('hffff)) counter_3 (
    .count(and_4_out), .Q(\条件分支成功数 ), .clk(CLK), .clr(RST));  // open: load, D, carry, preset, down
  Counter #(.width(16), .max('hffff)) counter_4 (
    .count(and_5_out), .Q(\LoadUse次数 ), .clk(CLK), .clr(RST));  // open: load, D, carry, preset, down
  and and_6 (and_6_out, ~halt, Flush);  // AND_Gate
  Counter #(.width(16), .max('hffff)) counter_5 (
    .count(and_6_out), .Q(\插入气泡数 ), .clk(CLK), .clr(RST));  // open: load, D, carry, preset, down

  // Other names for the same wires on the sheet: MEM_PC[31:0] = M_PC

  // Notes on the sheet:
  //   中断源
  //   时空图监测，可删除
  //   中断等待指示
  //   数码管输出
  //   指令存储器
  //   contents of rom_1 (hex, n*v repeats v):
  //   100493 100006f 100493 200913 300993 100006f 100493 200913 300993 100006f 100493 200913 300993
  //   100006f 100493 200913 300993 3c4000ef 100413 100493 1f49493 900533 2200893 73 24d493 48463 fedff06f
  //   900533 2200893 73 100493 249493 900533 2200893 73 48463 fedff06f 100493 1f49493 900533 2200893 73
  //   4034d493 900533 2200893 73 4044d493 900533 2200893 73 4044d493 900533 2200893 73 4044d493 900533
  //   2200893 73 4044d493 900533 2200893 73 4044d493 900533 2200893 73 4044d493 900533 2200893 73 4044d493
  //   900533 2200893 73 100413 1f41993 41f9d993 433 c00913 300b13 140413 f47413 800293 100313 499993
  //   89e9b3 1300533 2200893 73 406282b3 fe0294e3 140413 f00f93 1f47433 1c41413 800293 100313 49d993
  //   89e9b3 1300533 2200893 73 406282b3 fe0294e3 1c45413 406b0b33 b0463 f95ff06f 2b3 fff2c293 829293
  //   ff2e293 500533 2200893 73 fff00413 493 84a023 140413 448493 84a023 140413 448493 84a023 140413
  //   448493 84a023 140413 448493 84a023 140413 448493 84a023 140413 448493 84a023 140413 448493 84a023
  //   140413 448493 84a023 140413 448493 84a023 140413 448493 84a023 140413 448493 84a023 140413 448493
  //   84a023 140413 448493 84a023 140413 448493 84a023 140413 448493 84a023 140413 448493 140413 433
  //   3c00493 42983 4aa03 149a2b3 28663 134a023 1442023 ffc48493 fe9412e3 800533 2200893 73 440413 3c00493
  //   fc9416e3 3200893 73 200293 1100493 849493 1148493 1049493 900533 2200893 73 1c00e13 254d4b3 900533
  //   2200893 73 fffe0e13 fe0e16e3 a00893 73 8800493 849493 4848493 8700913 891913 5490913 2997933 1091913
  //   11096913 1200533 2200893 73 a00893 73 313 1000e13 8400493 849493 8348493 400913 891913 490913 849493
  //   8248493 849493 8148493 891913 490913 891913 490913 932023 12484b3 430313 fffe0e13 fe0e18e3 2000e13
  //   313 30483 900533 2200893 73 130313 fffe0e13 fe0e14e3 a00893 73 ff100493 900533 2200893 73 148493
  //   fe9068e3 900533 2200893 73 a00893 73 413 140413 800533 2200893 73 240413 800533 2200893 73 340413
  //   800533 2200893 73 440413 800533 2200893 73 540413 800533 2200893 73 640413 800533 2200893 73 740413
  //   800533 2200893 73 840413 800533 2200893 2200893 73 8067
  //   Rd[4:0]
  //   JALR
  //   URET
  //   I-Imm[11:0]
  //   S-Imm[11:0]
  //   B-Imm[12:1]
  //   J-Imm[20:1]
  //   JAL
  //   Beq
  //   Bne
  //   Blt[u]
  //   MemToReg
  //   MemWrite
  //   AluOP
  //   AluResult
  //   AluSrcB
  //   RegWrite
  //   MemVariant
  //   I/S-ImmType
  //   控制位
  //   流水调试日志用
  //   暂停节拍，不能为0
  //   戳工具置1进入计数暂停模式，ctrl+k时钟自动运行到对应节拍暂停
  //   ctrl+k关闭时钟连续运行，将控制位置零，进入单步调试模式调试
  //   可计数暂停的时钟源
  //   为方便自动评测，需要输出流水线各段保存的PC值，注意是PC不是PC+4，另外ID段寄存器写入信息，Mem段内存写入信息也要输出
  //   数据存储器
endmodule

module \中断按键参考电路  (
  input  \同步清零信号 ,
  output \与中断屏蔽位与 
);

  wire \_1号中断_out , and_1_out, clock_1_out, d_ff_1_q, or_1_out, or_2_out;

  Clock clock_1 (.out(clock_1_out));
  Button \_1号中断  (.out(\_1号中断_out ));
  LED \_1号中断等待指示灯  (.in(or_1_out));
  or or_1 (or_1_out, \与中断屏蔽位与 , d_ff_1_q);
  D_Flip_Flop #(.Pre_Clr_Positions("LEGACY"), .enable("true"), .NewFFLayout("false")) d_ff_1 (
    .clk(\_1号中断_out ), .D(1'b1), .Q(d_ff_1_q), .reset(\与中断屏蔽位与 ));  // open: Qn, preset, en
  or or_2 (or_2_out, d_ff_1_q, \与中断屏蔽位与 );
  and and_1 (and_1_out, or_2_out, ~\同步清零信号 );  // AND_Gate
  D_Flip_Flop #(.Pre_Clr_Positions("LEGACY"), .enable("true"), .NewFFLayout("false")) IR1 (
    .clk(clock_1_out), .D(and_1_out), .Q(\与中断屏蔽位与 ));  // open: Qn, preset, en, reset

  // Notes on the sheet:
  //   中断信号采样参考电路
  //   Reset 
endmodule

module \单周期_单级中断  (
  input  IR1,
  input  IR2,
  input  IR3,
  output RegWrite,
  output MemWrite,
  output [31:0] PC,
  output [31:0] IR,
  output [31:0] RDin,
  output [31:0] MDin,
  output [31:0] LedData
);

  wire and_1_out, and_2_out, and_3_out, and_5_out, CLK, clock_1_out, comparator_1_eq, comparator_2_eq,
       comparator_3_eq, comparator_3_lt, comparator_4_eq, comparator_5_eq, comparator_6_eq, comparator_7_eq,
       d_ff_1_q, d_ff_2_q, d_ff_3_q, d_ff_4_q, ecall, Eq, Ge, Go, halt, IE, Intr, IR1_q, IR1_t, IR1Rst,
       IR2_q, IR2_t, IR2Rst, IR3_q, IR3_t, IR3Rst, IRA, IRB, IRC, JAL, LinkToReg, Lt, nand_1_out, not_1_out,
       not_2_out, not_3_out, or_4_out, or_5_out, or_6_out, or_7_out, or_11_out, priority_encoder_1_gs, RST,
       URET, W1, W2, W3, \单周期硬布线控制器_1_alu_result , \单周期硬布线控制器_1_alu_src , \单周期硬布线控制器_1_beq ,
       \单周期硬布线控制器_1_blt_u , \单周期硬布线控制器_1_bne , \单周期硬布线控制器_1_jalr , \单周期硬布线控制器_1_s_type ;
  wire [0:0] \单周期硬布线控制器_1_memtoreg ;
  wire [1:0] CurIntrID_q, PCType, priority_encoder_1_out, \单周期硬布线控制器_1_func3 ;
  wire [2:2] \单周期硬布线控制器_1_func3_2 ;
  wire [3:0] \单周期硬布线控制器_1_alu_op ;
  wire [4:0] multiplexer_3_out, multiplexer_4_out;
  wire [7:0] bitselector_1_out;
  wire [9:0] multiplexer_9_out_2;
  wire [11:0] multiplexer_5_out;
  wire [12:0] CNT_num;
  wire [15:0] bitselector_2_out, \总周期数 ;
  wire [31:0] alu_1_result_2, bit_extender_1_out, bit_extender_2_out, bit_extender_3_out, bit_extender_4_out,
       bit_extender_5_out, bit_extender_6_out, bit_extender_7_out, EPCSave, IntrEntr, IntrRet,
       multiplexer_2_out, multiplexer_7_out, multiplexer_8_out, multiplexer_9_out, multiplexer_10_out,
       multiplexer_11_out, multiplexer_12_out, PCp4, PCRelJmp, R1, ram_1_data, RegRelJmp;

  Button \u_继续运行  (.out(Go));
  Button _1 ();  // open: out
  Button _2 ();  // open: out
  Button _3 ();  // open: out
  Button \u_总复位  (.out(RST));
  LED led_1 (.in(W1));
  LED led_2 (.in(W2));
  LED led_3 (.in(W3));
  // Probe on PCType
  Multiplexer #(.select(2), .width(32), .enable("false")) multiplexer_1 (
    .in0(PCp4), .in1(IntrRet), .in2(RegRelJmp), .in3(PCRelJmp), .out(EPCSave), .sel(PCType));
  LED \_1号中断等待指示灯  (.in(W1));
  LED \_2号中断等待指示灯  (.in(W2));
  LED \_3号中断等待指示灯  (.in(W3));
  Hex_Digit_Display hex_digit_display_1 (.value(LedData[31:28]));  // open: dp
  Multiplexer #(.width(32), .enable("false")) multiplexer_2 (
    .in0(EPCSave), .in1(IntrEntr), .out(multiplexer_2_out), .sel(Intr));
  not not_1 (not_1_out, halt);
  Adder #(.width(32)) adder_1 (.a(PC), .b(32'h4), .out(PCp4));  // open: cin, cout
  or or_1 (W1, IR1_q, d_ff_1_q);
  or or_2 (W2, IR2_q, d_ff_2_q);
  or or_3 (W3, IR3_q, d_ff_3_q);
  Hex_Digit_Display hex_digit_display_2 (.value(LedData[27:24]));  // open: dp
  Hex_Digit_Display hex_digit_display_3 (.value(LedData[23:20]));  // open: dp
  Register #(.width(32), .Select("low")) u_PC (.D(multiplexer_2_out), .en(not_1_out), .Q(PC), .clk(CLK), .clr(RST));
  not not_2 (not_2_out, halt);
  Counter #(.width(16), .max('hffff)) NXC (
    .count(not_2_out), .Q(\总周期数 ), .clk(CLK), .clr(RST));  // open: load, D, carry, preset, down
  D_Flip_Flop #(.Pre_Clr_Positions("LEGACY"), .enable("true"), .NewFFLayout("false")) d_ff_1 (
    .clk(IR1_t), .D(1'b1), .Q(d_ff_1_q), .reset(IR1_q));  // open: Qn, preset, en
  D_Flip_Flop #(.Pre_Clr_Positions("LEGACY"), .enable("true"), .NewFFLayout("false")) d_ff_2 (
    .clk(IR2_t), .D(1'b1), .Q(d_ff_2_q), .reset(IR2_q));  // open: Qn, preset, en
  D_Flip_Flop #(.Pre_Clr_Positions("LEGACY"), .enable("true"), .NewFFLayout("false")) d_ff_3 (
    .clk(IR3_t), .D(1'b1), .Q(d_ff_3_q), .reset(IR3_q));  // open: Qn, preset, en
  Hex_Digit_Display hex_digit_display_4 (.value(LedData[15:12]));  // open: dp
  Hex_Digit_Display hex_digit_display_5 (.value(LedData[19:16]));  // open: dp
  // Probe on PC
  or or_4 (or_4_out, d_ff_1_q, IR1_q);
  and and_1 (and_1_out, or_4_out, ~IR1Rst);  // AND_Gate
  or or_5 (or_5_out, d_ff_2_q, IR2_q);
  and and_2 (and_2_out, or_5_out, ~IR2Rst);  // AND_Gate
  or or_6 (or_6_out, d_ff_3_q, IR3_q);
  and and_3 (and_3_out, or_6_out, ~IR3Rst);  // AND_Gate
  Hex_Digit_Display hex_digit_display_6 (.value(LedData[7:4]));  // open: dp
  Hex_Digit_Display hex_digit_display_7 (.value(LedData[11:8]));  // open: dp
  // Probe on \总周期数 
  // RiscV_Probe riscv_probe_1: pin names not known; wires that end beside it: IR
  D_Flip_Flop #(.Pre_Clr_Positions("LEGACY"), .enable("true"), .NewFFLayout("false")) u_IR1 (
    .clk(CLK), .D(and_1_out), .Q(IR1_q), .reset(RST));  // open: Qn, preset, en
  D_Flip_Flop #(.Pre_Clr_Positions("LEGACY"), .enable("true"), .NewFFLayout("false")) u_IR2 (
    .clk(CLK), .D(and_2_out), .Q(IR2_q), .reset(RST));  // open: Qn, preset, en
  D_Flip_Flop #(.Pre_Clr_Positions("LEGACY"), .enable("true"), .NewFFLayout("false")) u_IR3 (
    .clk(CLK), .D(and_3_out), .Q(IR3_q), .reset(RST));  // open: Qn, preset, en
  Hex_Digit_Display hex_digit_display_8 (.value(LedData[3:0]));  // open: dp
  ROM #(.addrWidth(10), .dataWidth(32), .Select("high")) rom_1 (.addr(PC[11:2]), .data(IR));
  Priority_Encoder #(.select(2), .disabled(0)) priority_encoder_1 (
    .in1(IR1_q), .in2(IR2_q), .in3(IR3_q), .out(priority_encoder_1_out), .gs(priority_encoder_1_gs));  // open: in0, en_out, en_in
  Comparator #(.width(16), .mode("unsigned")) comparator_1 (
    .a(\总周期数 ), .b({16{1'b0}}), .eq(comparator_1_eq));  // open: gt, lt
  not not_3 (not_3_out, Intr);
  or or_7 (or_7_out, Intr, URET);
  or or_8 (IR1_t, IR1, IRA);
  PCType pctype_1 (
    .JmpType(PCType), .Eq(Eq), .Lt(Lt), .Ge(Ge), .URET(URET), .JALR(\单周期硬布线控制器_1_jalr ), .JAL(JAL),
    .BEQ(\单周期硬布线控制器_1_beq ), .BNE(\单周期硬布线控制器_1_bne ), .BLT_U(\单周期硬布线控制器_1_blt_u ), .LinkToReg(LinkToReg));  // open: Jmp, UncondJmp, CondBranch, ImmJmp, UncertainJmp, BranchInstr
  \单周期硬布线控制器  \u_单周期硬布线控制器_1  (
    .Funct({IR[30], IR[25], IR[14:12]}), .OP(IR[6:2]), .ALU_OP(\单周期硬布线控制器_1_alu_op ),
    .MemToReg(\单周期硬布线控制器_1_memtoreg [0]), .MemWrite(MemWrite), .ALU_SRC(\单周期硬布线控制器_1_alu_src ),
    .RegWrite(RegWrite), .ecall(ecall), .S_type(\单周期硬布线控制器_1_s_type ), .JALR(\单周期硬布线控制器_1_jalr ),
    .Beq(\单周期硬布线控制器_1_beq ), .JAL(JAL), .Bne(\单周期硬布线控制器_1_bne ), .in_3(IR[21]), .uret(URET),
    .Func3({\单周期硬布线控制器_1_func3_2 [2], \单周期硬布线控制器_1_func3 }), .ALU_RESULT(\单周期硬布线控制器_1_alu_result ),
    .Blt_u(\单周期硬布线控制器_1_blt_u ), .LegitIR(IR[1:0]));  // open: R1Dep, R2Dep, CSR
  Multiplexer #(.width(5), .enable("false")) multiplexer_3 (
    .in0(IR[19:15]), .in1(5'b01010), .out(multiplexer_3_out), .sel(ecall));
  Multiplexer #(.width(5), .enable("false")) multiplexer_4 (
    .in0(IR[24:20]), .in1(5'b10001), .out(multiplexer_4_out), .sel(ecall));
  Multiplexer #(.width(12), .enable("false")) multiplexer_5 (
    .in0(IR[31:20]), .in1({IR[31:25], IR[11:7]}), .out(multiplexer_5_out), .sel(\单周期硬布线控制器_1_s_type ));
  assign bit_extender_1_out = {{19{IR[31]}}, {IR[31], IR[7], IR[30:25], IR[11:8], 1'b0}};  // Bit_Extender bit_extender_1
  assign bit_extender_2_out = {{11{IR[31]}}, {IR[31], IR[19:12], IR[20], IR[30:21], 1'b0}};  // Bit_Extender bit_extender_2
  Multiplexer #(.select(2), .width(32), .enable("false")) multiplexer_6 (
    .in1(32'h30ac), .in2(32'h3150), .in3(32'h31f4), .out(IntrEntr), .sel(priority_encoder_1_out));  // open: in0
  Pull_Resistor pull_resistor_1 (.node(priority_encoder_1_out));
  and and_4 (Intr, priority_encoder_1_gs, IE);
  Register #(.width(1), .Select("low")) u_IE (
    .D(not_3_out), .en(or_7_out), .Q(IE), .clk(CLK), .clr(RST), .preset(comparator_1_eq));  // open: cs
  or or_9 (IR2_t, IR2, IRB);
  // Probe on multiplexer_3_out
  // Probe on multiplexer_4_out
  // Probe on IR[11:7]
  Adder #(.width(32)) adder_2 (.a(PC), .b(multiplexer_7_out), .out(PCRelJmp));  // open: cin, cout
  Multiplexer #(.width(32), .enable("false")) multiplexer_7 (
    .in0(bit_extender_1_out), .in1(bit_extender_2_out), .out(multiplexer_7_out), .sel(JAL));
  // Probe on multiplexer_7_out
  Register #(.width(2), .Select("low")) CurIntrID (
    .D(priority_encoder_1_out), .en(Intr), .Q(CurIntrID_q), .clk(CLK), .clr(RST));
  Register #(.width(32), .Select("low")) EPC (.D(EPCSave), .en(Intr), .Q(IntrRet), .clk(CLK), .clr(RST));
  Regifile regifile_1 (
    .Din(RDin), .Clk(CLK), .R1(R1), .R2(MDin), .WE(RegWrite), .W_num(IR[11:7]), .R1_num(multiplexer_3_out),
    .R2_num(multiplexer_4_out));
  assign bit_extender_3_out = {{20{multiplexer_5_out[11]}}, multiplexer_5_out};  // Bit_Extender bit_extender_3
  // Probe on bit_extender_3_out
  Demultiplexer #(.select(2), .enable("false")) demultiplexer_1 (
    .out1(IR1Rst), .out2(IR2Rst), .out3(IR3Rst), .in(URET), .sel(CurIntrID_q));  // open: out0
  or or_10 (IR3_t, IR3, IRC);
  // Probe on R1
  Multiplexer #(.width(32), .enable("false")) multiplexer_8 (
    .in0(MDin), .in1(bit_extender_3_out), .out(multiplexer_8_out), .sel(\单周期硬布线控制器_1_alu_src ));
  // Probe on multiplexer_8_out
  // Probe on \单周期硬布线控制器_1_alu_op 
  ALU alu_1 (
    .X(R1), .Y(multiplexer_8_out), .AluOP(\单周期硬布线控制器_1_alu_op ), .Equal(Eq), .Result(RegRelJmp),
    .Result_2(alu_1_result_2), .out_4(Ge), .out_6(Lt));
  and and_5 (and_5_out, ecall, comparator_2_eq);
  Comparator #(.width(32)) comparator_2 (.a(MDin), .b(32'h22), .eq(comparator_2_eq));  // open: gt, lt
  Multiplexer #(.width(32), .enable("false")) multiplexer_9 (
    .in0(RegRelJmp), .in1(alu_1_result_2),
    .out({multiplexer_9_out[31:12], multiplexer_9_out_2, multiplexer_9_out[1:0]}),
    .sel(\单周期硬布线控制器_1_alu_result ));
  Register #(.width(32), .Select("low")) register_1 (.D(R1), .en(and_5_out), .Q(LedData), .clk(CLK), .clr(RST));
  and and_6 (halt, ~comparator_2_eq, ecall, ~Go);  // AND_Gate
  // Probe on {multiplexer_9_out[31:12], multiplexer_9_out_2, multiplexer_9_out[1:0]}
  BitSelector #(.width(32), .group(8)) bitselector_1 (
    .in(ram_1_data), .out(bitselector_1_out), .sel(multiplexer_9_out[1:0]));
  RAM #(.addrWidth(10), .dataWidth(32), .bus("separate"), .Select("high"), .simpleMode("false")) ram_1 (
    .addr(multiplexer_9_out_2), .din(MDin), .data(ram_1_data), .str(MemWrite), .sel(1'b1), .clk(CLK),
    .clr(RST));  // open: ld
  BitSelector #(.width(32), .group(16)) bitselector_2 (
    .in(ram_1_data), .out(bitselector_2_out), .sel(multiplexer_9_out[1]));
  assign bit_extender_4_out = {{24{bitselector_1_out[7]}}, bitselector_1_out};  // Bit_Extender bit_extender_4
  assign bit_extender_5_out = {{24{1'b0}}, bitselector_1_out};  // Bit_Extender bit_extender_5
  assign bit_extender_6_out = {{16{bitselector_2_out[15]}}, bitselector_2_out};  // Bit_Extender bit_extender_6
  assign bit_extender_7_out = {{16{1'b0}}, bitselector_2_out};  // Bit_Extender bit_extender_7
  Multiplexer #(.width(32), .enable("false")) multiplexer_10 (
    .in0(bit_extender_4_out), .in1(bit_extender_5_out), .out(multiplexer_10_out),
    .sel(\单周期硬布线控制器_1_func3_2 [2]));
  Multiplexer #(.select(2), .width(32), .enable("false")) multiplexer_11 (
    .in0(multiplexer_10_out), .in1(multiplexer_12_out), .in2(ram_1_data), .out(multiplexer_11_out),
    .sel(\单周期硬布线控制器_1_func3 ));  // open: in3
  Multiplexer #(.width(32), .enable("false")) multiplexer_12 (
    .in0(bit_extender_6_out), .in1(bit_extender_7_out), .out(multiplexer_12_out),
    .sel(\单周期硬布线控制器_1_func3_2 [2]));
  D_Flip_Flop #(.trigger("high"), .Pre_Clr_Positions("LEGACY"), .enable("true"), .NewFFLayout("false")) d_ff_4 (.Q(d_ff_4_q));  // open: clk, D, Qn, preset, en, reset
  // Probe on 13'hc
  // Probe on {LinkToReg, \单周期硬布线控制器_1_memtoreg [0]}
  Multiplexer #(.select(2), .width(32), .enable("false")) multiplexer_13 (
    .in0({multiplexer_9_out[31:12], multiplexer_9_out_2, multiplexer_9_out[1:0]}), .in1(multiplexer_11_out),
    .in2(PCp4), .out(RDin), .sel({LinkToReg, \单周期硬布线控制器_1_memtoreg [0]}));  // open: in3
  // Probe on RDin
  Comparator #(.width(13)) comparator_3 (
    .a(CNT_num), .b(13'hc), .eq(comparator_3_eq), .lt(comparator_3_lt));  // open: gt
  Clock clock_1 (.out(clock_1_out));
  // Probe on \总周期数 
  Counter #(.width(13), .max('h1fff), .ongoal("stay"), .behavior("old")) counter_1 (
    .count(comparator_3_lt), .Q(CNT_num), .clk(clock_1_out));  // open: load, D, carry, clr, preset
  nand nand_1 (nand_1_out, d_ff_4_q, comparator_3_eq);
  Comparator #(.width(16)) comparator_4 (.a(16'h23b), .b(\总周期数 ), .eq(comparator_4_eq));  // open: gt, lt
  Comparator #(.width(16)) comparator_5 (.a(\总周期数 ), .b(16'h1), .eq(comparator_5_eq));  // open: gt, lt
  Comparator #(.width(16)) comparator_6 (.a(\总周期数 ), .b(16'h4), .eq(comparator_6_eq));  // open: gt, lt
  Comparator #(.width(16)) comparator_7 (.a(\总周期数 ), .b(16'h7), .eq(comparator_7_eq));  // open: gt, lt
  assign CLK = nand_1_out ? clock_1_out : 1'bz;  // Controlled_Buffer controlled_buffer_1
  Pull_Resistor #(.pull(1)) pull_resistor_2 (.node(CLK));
  or or_11 (or_11_out, comparator_4_eq, comparator_5_eq);
  assign IRA = or_11_out ? ~CLK : 1'bz;  // Controlled_Inverter controlled_inverter_1
  assign IRB = comparator_6_eq ? ~CLK : 1'bz;  // Controlled_Inverter controlled_inverter_2
  assign IRC = comparator_7_eq ? ~CLK : 1'bz;  // Controlled_Inverter controlled_inverter_3
  Pull_Resistor pull_resistor_3 (.node(IRA));
  Pull_Resistor pull_resistor_4 (.node(IRB));
  Pull_Resistor pull_resistor_5 (.node(IRC));

  // Other names for the same wires on the sheet: R2[31:0] = MDin

  // Notes on the sheet:
  //   中断源
  //   中断等待指示
  //   总复位信号应将除ROM以外所有存储组件全部清零
  //   数码管输出
  //   数码管输出应该用寄存器锁存，否则显示数据只能一闪而过
  //   指令探针
  //   指令存储器
  //   Reset 
  //   Reset 
  //   Reset 
  //   指令字
  //   contents of rom_1 (hex, n*v repeats v):
  //   7d000113 100413 1f41993 41f9d993 433 c00913 800b13 140413 f47413 800293 100313 499993 89e9b3 1300533
  //   2200893 73 406282b3 fe0294e3 140413 f00f93 1f47433 1c41413 800293 100313 49d993 89e9b3 1300533
  //   2200893 73 406282b3 fe0294e3 1c45413 406b0b33 b0463 f95ff06f 2b3 fff2c293 1029293 fff2e293 500533
  //   2200893 73 f5dff06f 1112023 410113 a12023 410113 812023 410113 1312023 410113 1412023 410113 1512023
  //   410113 1612023 410113 100b13 300a13 100a93 1600433 441413 14469b3 1300533 2200893 73 fe0416e3
  //   415a0a33 fe0a10e3 ffc10113 12b03 ffc10113 12a83 ffc10113 12a03 ffc10113 12983 ffc10113 12403
  //   ffc10113 12503 ffc10113 12883 200073 1112023 410113 a12023 410113 812023 410113 1312023 410113
  //   1412023 410113 1512023 410113 1612023 410113 200b13 300a13 100a93 1600433 441413 14469b3 1300533
  //   2200893 73 fe0416e3 415a0a33 fe0a10e3 ffc10113 12b03 ffc10113 12a83 ffc10113 12a03 ffc10113 12983
  //   ffc10113 12403 ffc10113 12503 ffc10113 12883 200073 1112023 410113 a12023 410113 812023 410113
  //   1312023 410113 1412023 410113 1512023 410113 1612023 410113 300b13 300a13 100a93 1600433 441413
  //   14469b3 1300533 2200893 73 fe0416e3 415a0a33 fe0a10e3 ffc10113 12b03 ffc10113 12a83 ffc10113 12a03
  //   ffc10113 12983 ffc10113 12403 ffc10113 12503 ffc10113 12883 200073
  //   JALR
  //   URET
  //   I-Imm[11:0]
  //   S-Imm[11:0]
  //   B-Imm[12:1]
  //   J-Imm[20:1]
  //   JAL
  //   Beq
  //   Bne
  //   Blt[u]
  //   MemToReg
  //   MemWrite
  //   AluOP
  //   AluResult
  //   AluSrcB
  //   RegWrite
  //   I/S-ImmType
  //   为方便自动评测，需要输出PC，IR，寄存器堆写如数据RDin
  //   数据存储器
  //   RAM写使能MemWrite、RAM写入数据MDin等信号
  //   控制位
  //   暂停节拍，不能为0
  //   戳工具置1进入计数暂停模式，ctrl+k时钟自动运行到对应节拍暂停
  //   ctrl+k关闭时钟连续运行，将控制位置零，进入单步调试模式调试
  //   单级中断测试信号模拟器
  //   可计数暂停的时钟源
endmodule

module CSRSubsystem (
  input  EN,
  input  PRESET,
  input  [2:0] Type,
  input  [11:0] CSRAddr,
  input  [4:0] R1_Uimm,
  input  [4:0] Rd,
  input  [31:0] R1Data,
  input  URET,
  input  Intr,
  input  CLK,
  input  RST,
  output IE
);

  wire comparator_1_eq, comparator_2_eq, CSRRCI, CSRRSI, or_1_out, or_2_out;

  Comparator #(.width(3)) comparator_1 (.a(3'b110), .b(Type), .eq(comparator_1_eq));  // open: gt, lt
  Comparator #(.width(3)) comparator_2 (.a(Type), .b(3'b111), .eq(comparator_2_eq));  // open: gt, lt
  and and_1 (CSRRSI, EN, comparator_1_eq);
  and and_2 (CSRRCI, EN, comparator_2_eq);
  or or_1 (or_1_out, CSRRSI, ~Intr);  // OR_Gate
  or or_2 (or_2_out, CSRRCI, CSRRSI, URET, Intr);
  Register #(.width(1), .Select("low")) register_1 (
    .D(or_1_out), .en(or_2_out), .Q(IE), .clk(CLK), .clr(RST), .preset(PRESET));  // open: cs
endmodule

module \单周期_多级中断  (
  input  IR1,
  input  IR2,
  input  IR3,
  output RegWrite,
  output MemWrite,
  output [31:0] PC,
  output [31:0] IR,
  output [31:0] RDin,
  output [31:0] MDin,
  output [31:0] LedData
);

  wire and_1_out, and_2_out, and_3_out, and_5_out, CLK, clock_1_out, comparator_1_eq, comparator_2_eq,
       comparator_4_eq, comparator_4_lt, comparator_5_eq, comparator_6_eq, comparator_7_eq, comparator_8_eq,
       comparator_9_eq, CSR, d_ff_1_q, d_ff_2_q, d_ff_3_q, d_ff_4_q, decoder_1_out1, decoder_1_out2,
       decoder_1_out3, decoder_2_out0, decoder_2_out1, decoder_2_out2, ecall, Eq, Ge, Go, halt, IE, Intr,
       IR1_q, IR1_t, IR1Rst, IR2_q, IR2_t, IR2Rst, IR3_q, IR3_t, IR3Rst, IRA, IRB, IRC, JAL, LinkToReg, Lt,
       nand_1_out, not_1_out, not_2_out, or_4_out, or_5_out, or_6_out, or_10_out, or_11_out, or_12_out,
       Priority, priority_encoder_1_gs, RST, URET, W1, W2, W3, \单周期硬布线控制器_1_alu_result ,
       \单周期硬布线控制器_1_alu_src , \单周期硬布线控制器_1_beq , \单周期硬布线控制器_1_blt_u , \单周期硬布线控制器_1_bne , \单周期硬布线控制器_1_jalr ,
       \单周期硬布线控制器_1_memtoreg , \单周期硬布线控制器_1_s_type ;
  wire [1:0] CurIntrID, IntrID, multiplexer_10_out, multiplexer_11_out, PCType, priority_encoder_2_out,
       register_5_q, register_6_q, register_7_q, StackTop, \单周期硬布线控制器_1_func3 ;
  wire [2:2] \单周期硬布线控制器_1_func3_2 ;
  wire [3:0] \单周期硬布线控制器_1_alu_op ;
  wire [4:0] multiplexer_3_out, multiplexer_4_out;
  wire [7:0] bitselector_1_out;
  wire [9:0] multiplexer_9_out_2;
  wire [11:0] multiplexer_5_out;
  wire [12:0] CNT_num;
  wire [15:0] bitselector_2_out, \总周期数 ;
  wire [31:0] alu_1_result_2, bit_extender_1_out, bit_extender_2_out, bit_extender_3_out, bit_extender_4_out,
       bit_extender_5_out, bit_extender_6_out, bit_extender_7_out, CSRData, EPCSave, IntrEntr, IntrRet,
       multiplexer_2_out, multiplexer_7_out, multiplexer_8_out, multiplexer_9_out, multiplexer_12_out,
       multiplexer_13_out, multiplexer_14_out, PCp4, PCRelJmp, R1, ram_1_data, register_2_q, register_3_q,
       register_4_q, RegRelJmp;

  Button \u_继续运行  (.out(Go));
  Button _1 ();  // open: out
  Button _2 ();  // open: out
  Button _3 ();  // open: out
  Button \u_总复位  (.out(RST));
  LED led_1 (.in(W1));
  LED led_2 (.in(W2));
  LED led_3 (.in(W3));
  // Probe on PCType
  Multiplexer #(.select(2), .width(32), .enable("false")) multiplexer_1 (
    .in0(PCp4), .in1(IntrRet), .in2(RegRelJmp), .in3(PCRelJmp), .out(EPCSave), .sel(PCType));
  LED \_1号中断等待指示灯  (.in(W1));
  LED \_2号中断等待指示灯  (.in(W2));
  LED \_3号中断等待指示灯  (.in(W3));
  Hex_Digit_Display hex_digit_display_1 (.value(LedData[31:28]));  // open: dp
  Multiplexer #(.width(32), .enable("false")) multiplexer_2 (
    .in0(EPCSave), .in1(IntrEntr), .out(multiplexer_2_out), .sel(Intr));
  not not_1 (not_1_out, halt);
  Adder #(.width(32)) adder_1 (.a(PC), .b(32'h4), .out(PCp4));  // open: cin, cout
  or or_1 (W1, IR1_q, d_ff_1_q);
  or or_2 (W2, IR2_q, d_ff_2_q);
  or or_3 (W3, IR3_q, d_ff_3_q);
  Hex_Digit_Display hex_digit_display_2 (.value(LedData[23:20]));  // open: dp
  Hex_Digit_Display hex_digit_display_3 (.value(LedData[27:24]));  // open: dp
  Register #(.width(32), .Select("low")) u_PC (.D(multiplexer_2_out), .en(not_1_out), .Q(PC), .clk(CLK), .clr(RST));
  not not_2 (not_2_out, halt);
  Counter #(.width(16), .max('hffff)) NXC (
    .count(not_2_out), .Q(\总周期数 ), .clk(CLK), .clr(RST));  // open: load, D, carry, preset, down
  D_Flip_Flop #(.Pre_Clr_Positions("LEGACY"), .enable("true"), .NewFFLayout("false")) d_ff_1 (
    .clk(IR1_t), .D(1'b1), .Q(d_ff_1_q), .reset(IR1_q));  // open: Qn, preset, en
  D_Flip_Flop #(.Pre_Clr_Positions("LEGACY"), .enable("true"), .NewFFLayout("false")) d_ff_2 (
    .clk(IR2_t), .D(1'b1), .Q(d_ff_2_q), .reset(IR2_q));  // open: Qn, preset, en
  D_Flip_Flop #(.Pre_Clr_Positions("LEGACY"), .enable("true"), .NewFFLayout("false")) d_ff_3 (
    .clk(IR3_t), .D(1'b1), .Q(d_ff_3_q), .reset(IR3_q));  // open: Qn, preset, en
  Hex_Digit_Display hex_digit_display_4 (.value(LedData[15:12]));  // open: dp
  Hex_Digit_Display hex_digit_display_5 (.value(LedData[19:16]));  // open: dp
  // Probe on PC
  or or_4 (or_4_out, d_ff_1_q, IR1_q);
  and and_1 (and_1_out, or_4_out, ~IR1Rst);  // AND_Gate
  or or_5 (or_5_out, d_ff_2_q, IR2_q);
  and and_2 (and_2_out, or_5_out, ~IR2Rst);  // AND_Gate
  or or_6 (or_6_out, d_ff_3_q, IR3_q);
  and and_3 (and_3_out, or_6_out, ~IR3Rst);  // AND_Gate
  Hex_Digit_Display hex_digit_display_6 (.value(LedData[7:4]));  // open: dp
  Hex_Digit_Display hex_digit_display_7 (.value(LedData[11:8]));  // open: dp
  // Probe on \总周期数 
  // RiscV_Probe riscv_probe_1: pin names not known; wires that end beside it: IR
  D_Flip_Flop #(.Pre_Clr_Positions("LEGACY"), .enable("true"), .NewFFLayout("false")) u_IR1 (
    .clk(CLK), .D(and_1_out), .Q(IR1_q), .reset(RST));  // open: Qn, preset, en
  D_Flip_Flop #(.Pre_Clr_Positions("LEGACY"), .enable("true"), .NewFFLayout("false")) u_IR2 (
    .clk(CLK), .D(and_2_out), .Q(IR2_q), .reset(RST));  // open: Qn, preset, en
  D_Flip_Flop #(.Pre_Clr_Positions("LEGACY"), .enable("true"), .NewFFLayout("false")) u_IR3 (
    .clk(CLK), .D(and_3_out), .Q(IR3_q), .reset(RST));  // open: Qn, preset, en
  Hex_Digit_Display hex_digit_display_8 (.value(LedData[3:0]));  // open: dp
  ROM #(.addrWidth(10), .dataWidth(32), .Select("high")) rom_1 (.addr(PC[11:2]), .data(IR));
  Priority_Encoder #(.select(2), .disabled(0)) priority_encoder_1 (
    .in1(IR1_q), .in2(IR2_q), .in3(IR3_q), .out(IntrID), .gs(priority_encoder_1_gs));  // open: in0, en_out, en_in
  or or_7 (IR1_t, IR1, IRA);
  PCType pctype_1 (
    .JmpType(PCType), .Eq(Eq), .Lt(Lt), .Ge(Ge), .URET(URET), .JALR(\单周期硬布线控制器_1_jalr ), .JAL(JAL),
    .BEQ(\单周期硬布线控制器_1_beq ), .BNE(\单周期硬布线控制器_1_bne ), .BLT_U(\单周期硬布线控制器_1_blt_u ), .LinkToReg(LinkToReg));  // open: Jmp, UncondJmp, CondBranch, ImmJmp, UncertainJmp, BranchInstr
  \单周期硬布线控制器  \u_单周期硬布线控制器_1  (
    .Funct({IR[30], IR[25], IR[14:12]}), .OP(IR[6:2]), .ALU_OP(\单周期硬布线控制器_1_alu_op ),
    .MemToReg(\单周期硬布线控制器_1_memtoreg ), .MemWrite(MemWrite), .ALU_SRC(\单周期硬布线控制器_1_alu_src ),
    .RegWrite(RegWrite), .ecall(ecall), .S_type(\单周期硬布线控制器_1_s_type ), .JALR(\单周期硬布线控制器_1_jalr ),
    .Beq(\单周期硬布线控制器_1_beq ), .JAL(JAL), .Bne(\单周期硬布线控制器_1_bne ), .in_3(IR[21]), .uret(URET),
    .Func3({\单周期硬布线控制器_1_func3_2 [2], \单周期硬布线控制器_1_func3 }), .ALU_RESULT(\单周期硬布线控制器_1_alu_result ),
    .Blt_u(\单周期硬布线控制器_1_blt_u ), .LegitIR(IR[1:0]), .CSR(CSR));  // open: R1Dep, R2Dep
  Multiplexer #(.width(5), .enable("false")) multiplexer_3 (
    .in0(IR[19:15]), .in1(5'b01010), .out(multiplexer_3_out), .sel(ecall));
  Multiplexer #(.width(5), .enable("false")) multiplexer_4 (
    .in0(IR[24:20]), .in1(5'b10001), .out(multiplexer_4_out), .sel(ecall));
  Multiplexer #(.width(12), .enable("false")) multiplexer_5 (
    .in0(IR[31:20]), .in1({IR[31:25], IR[11:7]}), .out(multiplexer_5_out), .sel(\单周期硬布线控制器_1_s_type ));
  assign bit_extender_1_out = {{19{IR[31]}}, {IR[31], IR[7], IR[30:25], IR[11:8], 1'b0}};  // Bit_Extender bit_extender_1
  assign bit_extender_2_out = {{11{IR[31]}}, {IR[31], IR[19:12], IR[20], IR[30:21], 1'b0}};  // Bit_Extender bit_extender_2
  Comparator #(.width(16), .mode("unsigned")) comparator_1 (
    .a(\总周期数 ), .b({16{1'b0}}), .eq(comparator_1_eq));  // open: gt, lt
  CSRSubsystem csrsubsystem_1 (
    .EN(CSR), .Type(IR[14:12]), .CSRAddr(IR[31:20]), .R1_Uimm(IR[19:15]), .Rd(IR[11:7]), .R1Data(R1),
    .URET(URET), .Intr(Intr), .IE(IE), .CLK(CLK), .RST(RST), .PRESET(comparator_1_eq));
  Multiplexer #(.select(2), .width(32), .enable("false")) multiplexer_6 (
    .in1(32'h30ac), .in2(32'h3158), .in3(32'h3204), .out(IntrEntr), .sel(IntrID));  // open: in0
  Pull_Resistor pull_resistor_1 (.node(IntrID));
  and and_4 (Intr, priority_encoder_1_gs, IE, Priority);
  or or_8 (IR2_t, IR2, IRB);
  // Probe on multiplexer_3_out
  // Probe on multiplexer_4_out
  // Probe on IR[11:7]
  Adder #(.width(32)) adder_2 (.a(PC), .b(multiplexer_7_out), .out(PCRelJmp));  // open: cin, cout
  Multiplexer #(.width(32), .enable("false")) multiplexer_7 (
    .in0(bit_extender_1_out), .in1(bit_extender_2_out), .out(multiplexer_7_out), .sel(JAL));
  // Probe on multiplexer_7_out
  Regifile regifile_1 (
    .Din(RDin), .Clk(CLK), .R1(R1), .R2(MDin), .WE(RegWrite), .W_num(IR[11:7]), .R1_num(multiplexer_3_out),
    .R2_num(multiplexer_4_out));
  // Probe on bit_extender_3_out
  assign bit_extender_3_out = {{20{multiplexer_5_out[11]}}, multiplexer_5_out};  // Bit_Extender bit_extender_3
  Demultiplexer #(.select(2), .enable("false")) demultiplexer_1 (
    .out1(IR1Rst), .out2(IR2Rst), .out3(IR3Rst), .in(URET), .sel(IntrID));  // open: out0
  or or_9 (IR3_t, IR3, IRC);
  // Probe on R1
  // Probe on multiplexer_8_out
  Multiplexer #(.width(32), .enable("false")) multiplexer_8 (
    .in0(MDin), .in1(bit_extender_3_out), .out(multiplexer_8_out), .sel(\单周期硬布线控制器_1_alu_src ));
  // Probe on \单周期硬布线控制器_1_alu_op 
  ALU alu_1 (
    .X(R1), .Y(multiplexer_8_out), .AluOP(\单周期硬布线控制器_1_alu_op ), .Equal(Eq), .Result(RegRelJmp),
    .Result_2(alu_1_result_2), .out_4(Ge), .out_6(Lt));
  and and_5 (and_5_out, ecall, comparator_2_eq);
  Comparator #(.width(32)) comparator_2 (.a(MDin), .b(32'h22), .eq(comparator_2_eq));  // open: gt, lt
  Multiplexer #(.width(32), .enable("false")) multiplexer_9 (
    .in0(RegRelJmp), .in1(alu_1_result_2),
    .out({multiplexer_9_out[31:12], multiplexer_9_out_2, multiplexer_9_out[1:0]}),
    .sel(\单周期硬布线控制器_1_alu_result ));
  Register #(.width(32), .Select("low")) register_1 (.D(R1), .en(and_5_out), .Q(LedData), .clk(CLK), .clr(RST));
  and and_6 (halt, ~comparator_2_eq, ecall, ~Go);  // AND_Gate
  or or_10 (or_10_out, Intr, URET);
  Decoder #(.select(2), .enable("false")) decoder_1 (
    .out1(decoder_1_out1), .out2(decoder_1_out2), .out3(decoder_1_out3), .sel(multiplexer_10_out));  // open: out0
  Multiplexer #(.width(2), .enable("false")) multiplexer_10 (
    .in0(2'b00), .in1(IntrID), .out(multiplexer_10_out), .sel(Intr));
  Multiplexer #(.width(2), .enable("false")) multiplexer_11 (
    .in0(2'b11), .in1(StackTop), .out(multiplexer_11_out), .sel(Intr));
  Counter #(.width(2), .max('h3)) counter_1 (
    .count(or_10_out), .Q(StackTop), .clk(CLK), .clr(RST), .down(URET));  // open: load, D, carry, preset
  // Probe on {multiplexer_9_out[31:12], multiplexer_9_out_2, multiplexer_9_out[1:0]}
  BitSelector #(.width(32), .group(8)) bitselector_1 (
    .in(ram_1_data), .out(bitselector_1_out), .sel(multiplexer_9_out[1:0]));
  RAM #(.addrWidth(10), .dataWidth(32), .bus("separate"), .Select("high"), .simpleMode("false")) ram_1 (
    .addr(multiplexer_9_out_2), .din(MDin), .data(ram_1_data), .str(MemWrite), .sel(1'b1), .clk(CLK),
    .clr(RST));  // open: ld
  BitSelector #(.width(32), .group(16)) bitselector_2 (
    .in(ram_1_data), .out(bitselector_2_out), .sel(multiplexer_9_out[1]));
  Decoder #(.select(2), .enable("false")) decoder_2 (
    .out0(decoder_2_out0), .out1(decoder_2_out1), .out2(decoder_2_out2), .sel(multiplexer_11_out));  // open: out3
  assign bit_extender_4_out = {{24{bitselector_1_out[7]}}, bitselector_1_out};  // Bit_Extender bit_extender_4
  assign bit_extender_5_out = {{24{1'b0}}, bitselector_1_out};  // Bit_Extender bit_extender_5
  assign bit_extender_6_out = {{16{bitselector_2_out[15]}}, bitselector_2_out};  // Bit_Extender bit_extender_6
  assign bit_extender_7_out = {{16{1'b0}}, bitselector_2_out};  // Bit_Extender bit_extender_7
  Register #(.width(32), .Select("low")) register_2 (
    .D(EPCSave), .en(decoder_1_out1), .Q(register_2_q), .clk(CLK), .clr(RST));
  Register #(.width(32), .Select("low")) register_3 (
    .D(EPCSave), .en(decoder_1_out2), .Q(register_3_q), .clk(CLK), .clr(RST));
  Register #(.width(32), .Select("low")) register_4 (
    .D(EPCSave), .en(decoder_1_out3), .Q(register_4_q), .clk(CLK), .clr(RST));
  Register #(.width(2), .Select("low")) register_5 (
    .D(IntrID), .en(decoder_2_out0), .Q(register_5_q), .clk(CLK), .clr(RST));
  Register #(.width(2), .Select("low")) register_6 (
    .D(IntrID), .en(decoder_2_out1), .Q(register_6_q), .clk(CLK), .clr(RST));
  Register #(.width(2), .Select("low")) register_7 (
    .D(IntrID), .en(decoder_2_out2), .Q(register_7_q), .clk(CLK), .clr(RST));
  Multiplexer #(.width(32), .enable("false")) multiplexer_12 (
    .in0(bit_extender_4_out), .in1(bit_extender_5_out), .out(multiplexer_12_out),
    .sel(\单周期硬布线控制器_1_func3_2 [2]));
  Multiplexer #(.select(2), .width(32), .enable("false")) multiplexer_13 (
    .in0(multiplexer_12_out), .in1(multiplexer_14_out), .in2(ram_1_data), .out(multiplexer_13_out),
    .sel(\单周期硬布线控制器_1_func3 ));  // open: in3
  Multiplexer #(.width(32), .enable("false")) multiplexer_14 (
    .in0(bit_extender_6_out), .in1(bit_extender_7_out), .out(multiplexer_14_out),
    .sel(\单周期硬布线控制器_1_func3_2 [2]));
  Multiplexer #(.select(2), .width(2), .enable("false")) multiplexer_15 (
    .in0(2'b00), .in1(register_5_q), .in2(register_6_q), .in3(register_7_q), .out(CurIntrID), .sel(StackTop));
  D_Flip_Flop #(.trigger("high"), .Pre_Clr_Positions("LEGACY"), .enable("true"), .NewFFLayout("false")) d_ff_4 (.Q(d_ff_4_q));  // open: clk, D, Qn, preset, en, reset
  // Probe on 13'hc
  Priority_Encoder #(.select(2)) priority_encoder_2 (
    .in0(1'b0), .in1(\单周期硬布线控制器_1_memtoreg ), .in2(LinkToReg), .in3(CSR), .out(priority_encoder_2_out));  // open: gs, en_out, en_in
  Pull_Resistor pull_resistor_2 (.node(priority_encoder_2_out));
  // Probe on priority_encoder_2_out
  Multiplexer #(.select(2), .width(32), .enable("false")) multiplexer_16 (
    .in0({multiplexer_9_out[31:12], multiplexer_9_out_2, multiplexer_9_out[1:0]}), .in1(multiplexer_13_out),
    .in2(PCp4), .in3(CSRData), .out(RDin), .sel(priority_encoder_2_out));
  // Probe on RDin
  Multiplexer #(.select(2), .width(32), .enable("false")) multiplexer_17 (
    .in1(register_2_q), .in2(register_3_q), .in3(register_4_q), .out(IntrRet), .sel(CurIntrID));  // open: in0
  Comparator #(.width(2), .mode("unsigned")) comparator_3 (.a(CurIntrID), .b(IntrID), .lt(Priority));  // open: gt, eq
  Comparator #(.width(13)) comparator_4 (
    .a(CNT_num), .b(13'hc), .eq(comparator_4_eq), .lt(comparator_4_lt));  // open: gt
  Clock clock_1 (.out(clock_1_out));
  Counter #(.width(13), .max('h1fff), .ongoal("stay"), .behavior("old")) counter_2 (
    .count(comparator_4_lt), .Q(CNT_num), .clk(clock_1_out));  // open: load, D, carry, clr, preset
  Comparator #(.width(16)) comparator_5 (.a(\总周期数 ), .b(16'h7), .eq(comparator_5_eq));  // open: gt, lt
  Comparator #(.width(16)) comparator_6 (.a(\总周期数 ), .b(16'h241), .eq(comparator_6_eq));  // open: gt, lt
  nand nand_1 (nand_1_out, d_ff_4_q, comparator_4_eq);
  Comparator #(.width(16)) comparator_7 (.a(16'h258), .b(\总周期数 ), .eq(comparator_7_eq));  // open: gt, lt
  or or_11 (or_11_out, comparator_7_eq, comparator_8_eq);
  Comparator #(.width(16)) comparator_8 (.a(\总周期数 ), .b(16'h1), .eq(comparator_8_eq));  // open: gt, lt
  Comparator #(.width(16)) comparator_9 (.a(\总周期数 ), .b(16'h4), .eq(comparator_9_eq));  // open: gt, lt
  or or_12 (or_12_out, comparator_5_eq, comparator_6_eq);
  assign CLK = nand_1_out ? clock_1_out : 1'bz;  // Controlled_Buffer controlled_buffer_1
  Pull_Resistor #(.pull(1)) pull_resistor_3 (.node(CLK));
  Pull_Resistor pull_resistor_4 (.node(IRA));
  assign IRA = or_11_out ? ~CLK : 1'bz;  // Controlled_Inverter controlled_inverter_1
  Pull_Resistor pull_resistor_5 (.node(IRB));
  assign IRB = comparator_9_eq ? ~CLK : 1'bz;  // Controlled_Inverter controlled_inverter_2
  Pull_Resistor pull_resistor_6 (.node(IRC));
  assign IRC = or_12_out ? ~CLK : 1'bz;  // Controlled_Inverter controlled_inverter_3

  // Other names for the same wires on the sheet: R2[31:0] = MDin

  // Notes on the sheet:
  //   中断源
  //   中断等待指示
  //   总复位信号应将除ROM以外所有存储组件全部清零
  //   数码管输出
  //   数码管输出应该用寄存器锁存，否则显示数据只能一闪而过
  //   指令探针
  //   指令存储器
  //   Reset 
  //   Reset 
  //   Reset 
  //   指令字
  //   contents of rom_1 (hex, n*v repeats v):
  //   7d000113 100413 1f41993 41f9d993 433 c00913 800b13 140413 f47413 800293 100313 499993 89e9b3 1300533
  //   2200893 73 406282b3 fe0294e3 140413 f00f93 1f47433 1c41413 800293 100313 49d993 89e9b3 1300533
  //   2200893 73 406282b3 fe0294e3 1c45413 406b0b33 b0463 f95ff06f 2b3 fff2c293 1029293 fff2e293 500533
  //   2200893 73 f5dff06f 1112023 410113 a12023 410113 812023 410113 1312023 410113 1412023 410113 1512023
  //   410113 1612023 410113 40e073 100b13 300a13 100a93 1600433 441413 14469b3 1300533 2200893 73 fe0416e3
  //   415a0a33 fe0a10e3 40f073 ffc10113 12b03 ffc10113 12a83 ffc10113 12a03 ffc10113 12983 ffc10113 12403
  //   ffc10113 12503 ffc10113 12883 200073 1112023 410113 a12023 410113 812023 410113 1312023 410113
  //   1412023 410113 1512023 410113 1612023 410113 40e073 200b13 300a13 100a93 1600433 441413 14469b3
  //   1300533 2200893 73 fe0416e3 415a0a33 fe0a10e3 40f073 ffc10113 12b03 ffc10113 12a83 ffc10113 12a03
  //   ffc10113 12983 ffc10113 12403 ffc10113 12503 ffc10113 12883 200073 1112023 410113 a12023 410113
  //   812023 410113 1312023 410113 1412023 410113 1512023 410113 1612023 410113 40e073 300b13 300a13
  //   100a93 1600433 441413 14469b3 1300533 2200893 73 fe0416e3 415a0a33 fe0a10e3 40f073 ffc10113 12b03
  //   ffc10113 12a83 ffc10113 12a03 ffc10113 12983 ffc10113 12403 ffc10113 12503 ffc10113 12883 200073
  //   JALR
  //   URET
  //   I-Imm[11:0]
  //   S-Imm[11:0]
  //   B-Imm[12:1]
  //   J-Imm[20:1]
  //   CSRAccType
  //   I-Imm/CSRAddr
  //   R1#/UImm
  //   Rd
  //   R1Data
  //   JAL
  //   Beq
  //   Bne
  //   Blt[u]
  //   MemToReg
  //   MemWrite
  //   AluOP
  //   AluResult
  //   AluSrcB
  //   RegWrite
  //   I/S-ImmType
  //   为方便自动评测，需要输出PC，IR，寄存器堆写如数据RDin
  //   数据存储器
  //   RAM写使能MemWrite、RAM写入数据MDin等信号
  //   控制位
  //   暂停节拍，不能为0
  //   戳工具置1进入计数暂停模式，ctrl+k时钟自动运行到对应节拍暂停
  //   ctrl+k关闭时钟连续运行，将控制位置零，进入单步调试模式调试
  //   多级中断测试信号模拟器
  //   可计数暂停的时钟源
endmodule

module \重定向流水线_单级中断  (
  input  IR1,
  input  IR2,
  input  IR3,
  output RegWrite,
  output MemWrite,
  output [31:0] IF_PC,
  output [31:0] ID_PC,
  output [31:0] EX_PC,
  output [31:0] M_PC,
  output [31:0] WB_PC,
  output [31:0] RDin,
  output [31:0] MDin,
  output [31:0] LedData
);

  wire and_1_out, and_2_out, and_3_out, and_5_out, and_6_out, and_8_out, and_9_out, and_10_out, CLK,
       clock_1_out, comparator_1_eq, comparator_2_eq, comparator_3_eq, comparator_3_lt, comparator_4_eq,
       comparator_5_eq, comparator_6_eq, comparator_7_eq, comparator_8_eq, CondBranch, d_ff_1_q, d_ff_2_q,
       d_ff_3_q, d_ff_4_q, Eq, EX_ECALL, EX_Halt, ex_mem_1_halt_2, ex_mem_1_memtoreg_2, ex_mem_1_regwrite_2,
       Flush, forwardbubblegen_1_ex_mem_en, forwardbubblegen_1_id_ex_en, forwardbubblegen_1_id_ex_flush,
       forwardbubblegen_1_if_id_en, forwardbubblegen_1_if_id_flush, forwardbubblegen_1_mem_wb_en,
       forwardbubblegen_1_pc_en, Ge, Go, halt, id_ex_1_alusrcb_2, id_ex_1_beq_2, id_ex_1_blt_u_2,
       id_ex_1_bne_2, id_ex_1_jal_2, id_ex_1_jalr_2, id_ex_1_memtoreg_2, id_ex_1_memwrite_2,
       id_ex_1_regwrite_2, IE, Intr, IR1_M, IR1_q, IR1_t, IR1Rst, IR2_M, IR2_q, IR2_t, IR2Rst, IR3_M, IR3_q,
       IR3_t, IR3Rst, IRA, IRB, IRC, JAL, LoadUse, Lt, mem_wb_1_halt_2, mem_wb_1_memtoreg_2, nand_1_out,
       not_1_out, not_2_out, not_3_out, or_4_out, or_5_out, or_6_out, or_7_out, or_8_out, or_12_out,
       or_13_out, pctype_1_jmp, priority_encoder_1_gs, pull_resistor_1_node, pull_resistor_2_node, RST,
       UncondJmp, URET, W1, W2, W3, \单周期硬布线控制器_1_alu_result , \单周期硬布线控制器_1_alu_src , \单周期硬布线控制器_1_beq ,
       \单周期硬布线控制器_1_blt_u , \单周期硬布线控制器_1_bne , \单周期硬布线控制器_1_ecall , \单周期硬布线控制器_1_jalr ,
       \单周期硬布线控制器_1_memtoreg , \单周期硬布线控制器_1_memwrite , \单周期硬布线控制器_1_r1dep , \单周期硬布线控制器_1_r2dep ,
       \单周期硬布线控制器_1_regwrite , \单周期硬布线控制器_1_s_type , \单周期硬布线控制器_1_uret ;
  wire [1:0] CurIntrID_q, forwardbubblegen_1_r1forwardsrc, forwardbubblegen_1_r2forwardsrc,
       id_ex_1_r1forwardsrc_2, id_ex_1_r2forwardsrc_2, PCType, pctype_1_linktoreg, priority_encoder_1_out;
  wire [2:0] ex_mem_1_memvariant_2, id_ex_1_memvariant_2, \单周期硬布线控制器_1_func3 ;
  wire [3:0] id_ex_1_aluop_2, \单周期硬布线控制器_1_alu_op ;
  wire [4:0] ex_mem_1_rd_num_2, id_ex_1_rd_num_2, multiplexer_3_out, multiplexer_4_out, WB_Rd;
  wire [7:0] bitselector_1_out;
  wire [11:0] multiplexer_6_out;
  wire [12:0] CNT_num;
  wire [15:0] bitselector_2_out, \LoadUse次数 , \总周期数 , \插入气泡数 , \无条件分支数 , \条件分支成功数 ;
  wire [31:0] alu_1_result_2, bit_extender_1_out, bit_extender_2_out, bit_extender_3_out, bit_extender_4_out,
       bit_extender_5_out, bit_extender_6_out, bit_extender_7_out, EX_IR, EX_PCp4, EX_R1, EX_R2,
       id_ex_1_aluimm_2, id_ex_1_jmpimm_2, id_ex_1_r1_2, id_ex_1_r2_2, ID_IR, IF_IR, IF_PCp4, IntrEntr,
       IntrRet, MEM_IR, MEM_RDin, mem_wb_1_memreaddata_2, mem_wb_1_result_2, multiplexer_1_out,
       multiplexer_2_out, multiplexer_7_out, multiplexer_8_out, multiplexer_10_out, multiplexer_12_out,
       multiplexer_13_out, multiplexer_14_out, multiplexer_15_out, multiplexer_16_out, PCRelJmp, ram_1_data,
       regifile_1_r1, regifile_1_r2, RegRelJmp, WB_IR, WB_PCp4;

  Button \u_总复位  (.out(RST));
  Button _1 (.out(IR1_M));
  Button _2 (.out(IR2_M));
  Button _3 (.out(IR3_M));
  // Probe on \总周期数 
  // Probe on \总周期数 
  ForwardBubbleGen forwardbubblegen_1 (
    .Halt(halt), .R1Dep(\单周期硬布线控制器_1_r1dep ), .EX_RegWrite(id_ex_1_regwrite_2), .EX_Rd(id_ex_1_rd_num_2),
    .R1(multiplexer_3_out), .Jmp(or_8_out), .R2Dep(\单周期硬布线控制器_1_r2dep ), .MEM_RegWrite(ex_mem_1_regwrite_2),
    .MEM_Rd(ex_mem_1_rd_num_2), .R2(multiplexer_4_out), .PC_EN(forwardbubblegen_1_pc_en),
    .IF_ID_EN(forwardbubblegen_1_if_id_en), .IF_ID_FLUSH(forwardbubblegen_1_if_id_flush),
    .ID_EX_FLUSH(forwardbubblegen_1_id_ex_flush), .ID_EX_EN(forwardbubblegen_1_id_ex_en),
    .EX_MEM_EN(forwardbubblegen_1_ex_mem_en), .MEM_WB_EN(forwardbubblegen_1_mem_wb_en),
    .R1ForwardSrc(forwardbubblegen_1_r1forwardsrc), .R2ForwardSrc(forwardbubblegen_1_r2forwardsrc),
    .EX_MemToReg(id_ex_1_memtoreg_2), .LoadUse(LoadUse), .Flush(Flush), .Intr(pull_resistor_1_node),
    .PredictFail(pull_resistor_2_node));  // open: Stall
  Button \u_继续运行  (.out(Go));
  LED led_1 (.in(W1));
  LED led_2 (.in(W2));
  LED led_3 (.in(W3));
  Pull_Resistor pull_resistor_1 (.node(pull_resistor_1_node));
  Pull_Resistor pull_resistor_2 (.node(pull_resistor_2_node));
  // Probe on PCType
  // Probe on multiplexer_1_out
  Multiplexer #(.select(2), .width(32), .enable("false")) multiplexer_1 (
    .in0(IF_PCp4), .in1(IntrRet), .in2(RegRelJmp), .in3(PCRelJmp), .out(multiplexer_1_out), .sel(PCType));
  LED \_1号中断等待指示灯  (.in(W1));
  LED \_2号中断等待指示灯  (.in(W2));
  LED \_3号中断等待指示灯  (.in(W3));
  Hex_Digit_Display hex_digit_display_1 (.value(LedData[31:28]));  // open: dp
  // Probe on IF_PC[19:0]
  // RiscV_Probe riscv_probe_1: pin names not known; wires that end beside it: IF_IR
  Multiplexer #(.width(32), .enable("false")) multiplexer_2 (
    .in0(multiplexer_1_out), .in1(IntrEntr), .out(multiplexer_2_out), .sel(Intr));
  or or_1 (W1, IR1_q, d_ff_1_q);
  or or_2 (W2, IR2_q, d_ff_2_q);
  or or_3 (W3, IR3_q, d_ff_3_q);
  Hex_Digit_Display hex_digit_display_2 (.value(LedData[27:24]));  // open: dp
  Hex_Digit_Display hex_digit_display_3 (.value(LedData[23:20]));  // open: dp
  // Probe on ID_PC[19:0]
  // RiscV_Probe riscv_probe_2: pin names not known; wires that end beside it: ID_IR
  Register #(.width(32), .Select("low")) PC (
    .D(multiplexer_2_out), .en(forwardbubblegen_1_pc_en), .Q(IF_PC), .clk(CLK), .clr(RST));
  D_Flip_Flop #(.Pre_Clr_Positions("LEGACY"), .enable("true"), .NewFFLayout("false")) d_ff_1 (
    .clk(IR1_t), .D(1'b1), .Q(d_ff_1_q), .reset(IR1_q));  // open: Qn, preset, en
  D_Flip_Flop #(.Pre_Clr_Positions("LEGACY"), .enable("true"), .NewFFLayout("false")) d_ff_2 (
    .clk(IR2_t), .D(1'b1), .Q(d_ff_2_q), .reset(IR2_q));  // open: Qn, preset, en
  D_Flip_Flop #(.Pre_Clr_Positions("LEGACY"), .enable("true"), .NewFFLayout("false")) d_ff_3 (
    .clk(IR3_t), .D(1'b1), .Q(d_ff_3_q), .reset(IR3_q));  // open: Qn, preset, en
  Hex_Digit_Display hex_digit_display_4 (.value(LedData[19:16]));  // open: dp
  Hex_Digit_Display hex_digit_display_5 (.value(LedData[15:12]));  // open: dp
  or or_4 (or_4_out, d_ff_1_q, IR1_q);
  and and_1 (and_1_out, or_4_out, ~IR1Rst);  // AND_Gate
  or or_5 (or_5_out, d_ff_2_q, IR2_q);
  and and_2 (and_2_out, or_5_out, ~IR2Rst);  // AND_Gate
  or or_6 (or_6_out, d_ff_3_q, IR3_q);
  and and_3 (and_3_out, or_6_out, ~IR3Rst);  // AND_Gate
  Hex_Digit_Display hex_digit_display_6 (.value(LedData[11:8]));  // open: dp
  Hex_Digit_Display hex_digit_display_7 (.value(LedData[7:4]));  // open: dp
  // Probe on EX_PC[19:0]
  // RiscV_Probe riscv_probe_3: pin names not known; wires that end beside it: EX_IR
  ROM #(.addrWidth(10), .dataWidth(32), .Select("high")) rom_1 (.addr(IF_PC[11:2]), .data(IF_IR));
  Adder #(.width(32)) adder_1 (.a(IF_PC), .b(32'h4), .out(IF_PCp4));  // open: cin, cout
  D_Flip_Flop #(.Pre_Clr_Positions("LEGACY"), .enable("true"), .NewFFLayout("false")) u_IR1 (
    .clk(CLK), .D(and_1_out), .Q(IR1_q), .reset(RST));  // open: Qn, preset, en
  D_Flip_Flop #(.Pre_Clr_Positions("LEGACY"), .enable("true"), .NewFFLayout("false")) u_IR2 (
    .clk(CLK), .D(and_2_out), .Q(IR2_q), .reset(RST));  // open: Qn, preset, en
  D_Flip_Flop #(.Pre_Clr_Positions("LEGACY"), .enable("true"), .NewFFLayout("false")) u_IR3 (
    .clk(CLK), .D(and_3_out), .Q(IR3_q), .reset(RST));  // open: Qn, preset, en
  Hex_Digit_Display hex_digit_display_8 (.value(LedData[3:0]));  // open: dp
  IF_ID if_id_1 (
    .IR(IF_IR), .PC(IF_PC), .FLUSH(forwardbubblegen_1_if_id_flush), .IR_2(ID_IR), .PC_2(ID_PC), .RST(RST),
    .EN(forwardbubblegen_1_if_id_en), .CLK(CLK));  // open: PredictBranch, PredictBranch_2
  // Probe on \总周期数 
  // Probe on M_PC[19:0]
  // RiscV_Probe riscv_probe_4: pin names not known; wires that end beside it: MEM_IR
  Priority_Encoder #(.select(2), .disabled(0)) priority_encoder_1 (
    .in1(IR1_q), .in2(IR2_q), .in3(IR3_q), .out(priority_encoder_1_out), .gs(priority_encoder_1_gs));  // open: in0, en_out, en_in
  Comparator #(.width(16), .mode("unsigned")) comparator_1 (
    .a(\总周期数 ), .b({16{1'b0}}), .eq(comparator_1_eq));  // open: gt, lt
  not not_1 (not_1_out, Intr);
  or or_7 (or_7_out, Intr, URET);
  // Probe on \总周期数 
  // Probe on \无条件分支数 
  // Probe on \条件分支成功数 
  // Probe on \插入气泡数 
  // Probe on \LoadUse次数 
  \单周期硬布线控制器  \u_单周期硬布线控制器_1  (
    .Funct({ID_IR[30], ID_IR[25], ID_IR[14:12]}), .OP(ID_IR[6:2]), .ALU_OP(\单周期硬布线控制器_1_alu_op ),
    .MemToReg(\单周期硬布线控制器_1_memtoreg ), .MemWrite(\单周期硬布线控制器_1_memwrite ), .ALU_SRC(\单周期硬布线控制器_1_alu_src ),
    .RegWrite(\单周期硬布线控制器_1_regwrite ), .ecall(\单周期硬布线控制器_1_ecall ), .S_type(\单周期硬布线控制器_1_s_type ),
    .JALR(\单周期硬布线控制器_1_jalr ), .Beq(\单周期硬布线控制器_1_beq ), .JAL(JAL), .Bne(\单周期硬布线控制器_1_bne ), .in_3(ID_IR[21]),
    .uret(\单周期硬布线控制器_1_uret ), .Func3(\单周期硬布线控制器_1_func3 ), .ALU_RESULT(\单周期硬布线控制器_1_alu_result ),
    .Blt_u(\单周期硬布线控制器_1_blt_u ), .R1Dep(\单周期硬布线控制器_1_r1dep ), .R2Dep(\单周期硬布线控制器_1_r2dep ),
    .LegitIR(ID_IR[1:0]));  // open: CSR
  Multiplexer #(.width(5), .enable("false")) multiplexer_3 (
    .in0(ID_IR[19:15]), .in1(5'b01010), .out(multiplexer_3_out), .sel(\单周期硬布线控制器_1_ecall ));
  Multiplexer #(.width(5), .enable("false")) multiplexer_4 (
    .in0(ID_IR[24:20]), .in1(5'b10001), .out(multiplexer_4_out), .sel(\单周期硬布线控制器_1_ecall ));
  Multiplexer #(.select(2), .width(32), .enable("false")) multiplexer_5 (
    .in1(32'h30ac), .in2(32'h3150), .in3(32'h31f4), .out(IntrEntr), .sel(priority_encoder_1_out));  // open: in0
  Pull_Resistor pull_resistor_3 (.node(priority_encoder_1_out));
  and and_4 (Intr, priority_encoder_1_gs, IE);
  Register #(.width(1), .Select("low")) u_IE (
    .D(not_1_out), .en(or_7_out), .Q(IE), .clk(CLK), .clr(RST), .preset(comparator_1_eq));  // open: cs
  // Probe on IF_PC[11:0]
  // Probe on WB_PC[19:0]
  // RiscV_Probe riscv_probe_5: pin names not known; wires that end beside it: WB_IR
  // Probe on multiplexer_3_out
  // Probe on multiplexer_4_out
  // Probe on WB_Rd
  Multiplexer #(.width(12), .enable("false")) multiplexer_6 (
    .in0(ID_IR[31:20]), .in1({ID_IR[31:25], ID_IR[11:7]}), .out(multiplexer_6_out), .sel(\单周期硬布线控制器_1_s_type ));
  assign bit_extender_1_out = {{19{ID_IR[31]}}, {ID_IR[31], ID_IR[7], ID_IR[30:25], ID_IR[11:8], 1'b0}};  // Bit_Extender bit_extender_1
  Multiplexer #(.width(32), .enable("false")) multiplexer_7 (
    .in0(bit_extender_1_out), .in1(bit_extender_2_out), .out(multiplexer_7_out), .sel(JAL));
  assign bit_extender_2_out = {{11{ID_IR[31]}}, {ID_IR[31], ID_IR[19:12], ID_IR[20], ID_IR[30:21], 1'b0}};  // Bit_Extender bit_extender_2
  Register #(.width(2), .Select("low")) CurIntrID (
    .D(priority_encoder_1_out), .en(Intr), .Q(CurIntrID_q), .clk(CLK), .clr(RST));
  // Probe on ID_PC[11:0]
  // Probe on EX_PC[11:0]
  not not_2 (not_2_out, CLK);
  assign bit_extender_3_out = {{20{multiplexer_6_out[11]}}, multiplexer_6_out};  // Bit_Extender bit_extender_3
  Demultiplexer #(.select(2), .enable("false")) demultiplexer_1 (
    .out1(IR1Rst), .out2(IR2Rst), .out3(IR3Rst), .in(URET), .sel(CurIntrID_q));  // open: out0
  // Probe on M_PC[11:0]
  D_Flip_Flop #(.trigger("high"), .Pre_Clr_Positions("LEGACY"), .enable("true"), .NewFFLayout("false")) d_ff_4 (.Q(d_ff_4_q));  // open: clk, D, Qn, preset, en, reset
  // Probe on 13'h2bf
  Regifile regifile_1 (
    .Din(RDin), .Clk(not_2_out), .R1(regifile_1_r1), .R2(regifile_1_r2), .WE(RegWrite), .W_num(WB_Rd),
    .R1_num(multiplexer_3_out), .R2_num(multiplexer_4_out));
  // Probe on bit_extender_3_out
  Comparator #(.width(32), .mode("unsigned")) comparator_2 (
    .a(ID_IR), .b({32{1'b0}}), .eq(comparator_2_eq));  // open: gt, lt
  // Probe on WB_PC[11:0]
  Comparator #(.width(13)) comparator_3 (
    .a(CNT_num), .b(13'h2bf), .eq(comparator_3_eq), .lt(comparator_3_lt));  // open: gt
  Clock clock_1 (.out(clock_1_out));
  ID_EX id_ex_1 (
    .IR(ID_IR), .PC(ID_PC), .FLUSH(forwardbubblegen_1_id_ex_flush), .IR_2(EX_IR), .PC_2(EX_PC), .RST(RST),
    .EN(forwardbubblegen_1_id_ex_en), .CLK(CLK), .URET(\单周期硬布线控制器_1_uret ), .URET_2(URET),
    .JALR(\单周期硬布线控制器_1_jalr ), .JALR_2(id_ex_1_jalr_2), .JAL(JAL), .JAL_2(id_ex_1_jal_2),
    .BEQ(\单周期硬布线控制器_1_beq ), .BEQ_2(id_ex_1_beq_2), .BNE(\单周期硬布线控制器_1_bne ), .BNE_2(id_ex_1_bne_2),
    .BLT_U(\单周期硬布线控制器_1_blt_u ), .BLT_U_2(id_ex_1_blt_u_2), .MemToReg(\单周期硬布线控制器_1_memtoreg ),
    .MemToReg_2(id_ex_1_memtoreg_2), .MemWrite(\单周期硬布线控制器_1_memwrite ), .MemWrite_2(id_ex_1_memwrite_2),
    .AluOP(\单周期硬布线控制器_1_alu_op ), .AluOP_2(id_ex_1_aluop_2), .AluResult(\单周期硬布线控制器_1_alu_result ),
    .AluResult_2(pctype_1_linktoreg[1]), .AluSrcB(\单周期硬布线控制器_1_alu_src ), .AluSrcB_2(id_ex_1_alusrcb_2),
    .RegWrite(\单周期硬布线控制器_1_regwrite ), .RegWrite_2(id_ex_1_regwrite_2), .MemVariant(\单周期硬布线控制器_1_func3 ),
    .MemVariant_2(id_ex_1_memvariant_2), .Rd_num(ID_IR[11:7]), .Rd_num_2(id_ex_1_rd_num_2),
    .ECALL(\单周期硬布线控制器_1_ecall ), .ECALL_2(EX_ECALL), .JmpImm(multiplexer_7_out), .JmpImm_2(id_ex_1_jmpimm_2),
    .AluImm(bit_extender_3_out), .AluImm_2(id_ex_1_aluimm_2), .R2(regifile_1_r2), .R2_2(id_ex_1_r2_2),
    .R1(regifile_1_r1), .R1_2(id_ex_1_r1_2), .R1ForwardSrc(forwardbubblegen_1_r1forwardsrc),
    .R1ForwardSrc_2(id_ex_1_r1forwardsrc_2), .R2ForwardSrc(forwardbubblegen_1_r2forwardsrc),
    .R2ForwardSrc_2(id_ex_1_r2forwardsrc_2));  // open: PredictBranch, PredictBranch_2
  Multiplexer #(.width(32), .enable("false")) multiplexer_8 (
    .in0(ID_PC), .in1(IF_PC), .out(multiplexer_8_out), .sel(comparator_2_eq));
  nand nand_1 (nand_1_out, d_ff_4_q, comparator_3_eq);
  Counter #(.width(13), .max('h1fff), .ongoal("stay"), .behavior("old")) counter_1 (
    .count(comparator_3_lt), .Q(CNT_num), .clk(clock_1_out));  // open: load, D, carry, clr, preset
  Multiplexer #(.select(2), .width(32), .enable("false")) multiplexer_9 (
    .in0(id_ex_1_r1_2), .in1(RDin), .in2(MEM_RDin), .out(EX_R1), .sel(id_ex_1_r1forwardsrc_2));  // open: in3
  Adder #(.width(32)) adder_2 (.a(id_ex_1_jmpimm_2), .b(EX_PC), .out(PCRelJmp));  // open: cin, cout
  Multiplexer #(.select(2), .width(32), .enable("false")) multiplexer_10 (
    .in0(multiplexer_8_out), .in1(IntrRet), .in2(RegRelJmp), .in3(PCRelJmp), .out(multiplexer_10_out),
    .sel(PCType));
  assign CLK = nand_1_out ? clock_1_out : 1'bz;  // Controlled_Buffer controlled_buffer_1
  or or_8 (or_8_out, pctype_1_jmp, Intr);
  PCType pctype_1 (
    .JmpType(PCType), .Jmp(pctype_1_jmp), .Eq(Eq), .Lt(Lt), .Ge(Ge), .URET(URET), .JALR(id_ex_1_jalr_2),
    .JAL(id_ex_1_jal_2), .BEQ(id_ex_1_beq_2), .BNE(id_ex_1_bne_2), .BLT_U(id_ex_1_blt_u_2),
    .LinkToReg(pctype_1_linktoreg[0]), .UncondJmp(UncondJmp), .CondBranch(CondBranch));  // open: ImmJmp, UncertainJmp, BranchInstr
  Multiplexer #(.select(2), .width(32), .enable("false")) multiplexer_11 (
    .in0(id_ex_1_r2_2), .in1(RDin), .in2(MEM_RDin), .out(EX_R2), .sel(id_ex_1_r2forwardsrc_2));  // open: in3
  Multiplexer #(.width(32), .enable("false")) multiplexer_12 (
    .in0(EX_R2), .in1(id_ex_1_aluimm_2), .out(multiplexer_12_out), .sel(id_ex_1_alusrcb_2));
  Adder #(.width(32)) adder_3 (.a(EX_PC), .b(32'h4), .out(EX_PCp4));  // open: cin, cout
  Register #(.width(32), .Select("low")) EPC (.D(multiplexer_10_out), .en(Intr), .Q(IntrRet), .clk(CLK), .clr(RST));
  Pull_Resistor #(.pull(1)) pull_resistor_4 (.node(CLK));
  ALU alu_1 (
    .X(EX_R1), .Y(multiplexer_12_out), .AluOP(id_ex_1_aluop_2), .Equal(Eq), .Result(RegRelJmp),
    .Result_2(alu_1_result_2), .out_4(Ge), .out_6(Lt));
  Multiplexer #(.select(2), .width(32), .enable("false")) multiplexer_13 (
    .in0(RegRelJmp), .in1(EX_PCp4), .in2(alu_1_result_2), .out(multiplexer_13_out), .sel(pctype_1_linktoreg));  // open: in3
  or or_9 (IR1_t, IR1, IR1_M, IRA);
  EX_MEM ex_mem_1 (
    .EN(forwardbubblegen_1_ex_mem_en), .MemToReg(id_ex_1_memtoreg_2), .MemToReg_2(ex_mem_1_memtoreg_2),
    .MemWrite(id_ex_1_memwrite_2), .MemWrite_2(MemWrite), .RegWrite(id_ex_1_regwrite_2),
    .RegWrite_2(ex_mem_1_regwrite_2), .MemVariant(id_ex_1_memvariant_2),
    .MemVariant_2(ex_mem_1_memvariant_2), .Halt(EX_Halt), .Halt_2(ex_mem_1_halt_2),
    .Result(multiplexer_13_out), .Result_2(MEM_RDin), .MemWriteData(EX_R2), .MemWriteData_2(MDin),
    .Rd_num(id_ex_1_rd_num_2), .Rd_num_2(ex_mem_1_rd_num_2), .IR(EX_IR), .IR_2(MEM_IR), .PC(EX_PC),
    .PC_2(M_PC), .FLUSH(1'b0), .RST(RST), .CLK(CLK));
  or or_10 (IR2_t, IR2, IR2_M, IRB);
  or or_11 (IR3_t, IR3, IR3_M, IRC);
  // Probe on MEM_RDin
  BitSelector #(.width(32), .group(8)) bitselector_1 (.in(ram_1_data), .out(bitselector_1_out), .sel(MEM_RDin[1:0]));
  RAM #(.addrWidth(10), .dataWidth(32), .bus("separate"), .Select("high"), .simpleMode("false")) ram_1 (
    .addr(MEM_RDin[11:2]), .din(MDin), .data(ram_1_data), .str(MemWrite), .sel(1'b1), .clk(CLK), .clr(RST));  // open: ld
  BitSelector #(.width(32), .group(16)) bitselector_2 (.in(ram_1_data), .out(bitselector_2_out), .sel(MEM_RDin[1]));
  assign bit_extender_4_out = {{24{bitselector_1_out[7]}}, bitselector_1_out};  // Bit_Extender bit_extender_4
  Multiplexer #(.width(32), .enable("false")) multiplexer_14 (
    .in0(bit_extender_4_out), .in1(bit_extender_5_out), .out(multiplexer_14_out),
    .sel(ex_mem_1_memvariant_2[2]));
  assign bit_extender_5_out = {{24{1'b0}}, bitselector_1_out};  // Bit_Extender bit_extender_5
  assign bit_extender_6_out = {{16{bitselector_2_out[15]}}, bitselector_2_out};  // Bit_Extender bit_extender_6
  Multiplexer #(.width(32), .enable("false")) multiplexer_15 (
    .in0(bit_extender_6_out), .in1(bit_extender_7_out), .out(multiplexer_15_out),
    .sel(ex_mem_1_memvariant_2[2]));
  assign bit_extender_7_out = {{16{1'b0}}, bitselector_2_out};  // Bit_Extender bit_extender_7
  Multiplexer #(.select(2), .width(32), .enable("false")) multiplexer_16 (
    .in0(multiplexer_14_out), .in1(multiplexer_15_out), .in2(ram_1_data), .out(multiplexer_16_out),
    .sel(ex_mem_1_memvariant_2[1:0]));  // open: in3
  MEM_WB mem_wb_1 (
    .EN(forwardbubblegen_1_mem_wb_en), .MemToReg(ex_mem_1_memtoreg_2), .MemToReg_2(mem_wb_1_memtoreg_2),
    .RegWrite(ex_mem_1_regwrite_2), .RegWrite_2(RegWrite), .Halt(ex_mem_1_halt_2), .Halt_2(mem_wb_1_halt_2),
    .Result(MEM_RDin), .Result_2(mem_wb_1_result_2), .MemReadData(multiplexer_16_out),
    .MemReadData_2(mem_wb_1_memreaddata_2), .Rd_num(ex_mem_1_rd_num_2), .Rd_num_2(WB_Rd), .IR(MEM_IR),
    .IR_2(WB_IR), .PC(M_PC), .PC_2(WB_PC), .FLUSH(1'b0), .RST(RST), .CLK(CLK));
  // Probe on mem_wb_1_memtoreg_2
  Multiplexer #(.width(32), .enable("false")) multiplexer_17 (
    .in0(mem_wb_1_result_2), .in1(mem_wb_1_memreaddata_2), .out(RDin), .sel(mem_wb_1_memtoreg_2));
  // Probe on RDin
  Adder #(.width(32)) adder_4 (.a(WB_PC), .b(32'h4), .out(WB_PCp4));  // open: cin, cout
  S_R_Flip_Flop #(.trigger("latch")) s_r_ff_1 (
    .S(mem_wb_1_halt_2), .R(1'b0), .Q(halt), .reset(or_12_out));  // open: Qn, preset
  or or_12 (or_12_out, Go, RST);
  not not_3 (not_3_out, halt);
  Counter #(.width(16), .max('hffff)) NXC (
    .count(not_3_out), .Q(\总周期数 ), .clk(CLK), .clr(RST));  // open: load, D, carry, preset, down
  and and_5 (and_5_out, ~halt, UncondJmp);  // AND_Gate
  Counter #(.width(16), .max('hffff)) counter_2 (
    .count(and_5_out), .Q(\无条件分支数 ), .clk(CLK), .clr(RST));  // open: load, D, carry, preset, down
  Comparator #(.width(32)) comparator_4 (.a(EX_R2), .b(32'h22), .eq(comparator_4_eq));  // open: gt, lt
  and and_6 (and_6_out, EX_ECALL, comparator_4_eq);
  and and_7 (EX_Halt, ~comparator_4_eq, EX_ECALL);  // AND_Gate
  // Probe on \总周期数 
  and and_8 (and_8_out, ~halt, CondBranch);  // AND_Gate
  and and_9 (and_9_out, ~halt, LoadUse);  // AND_Gate
  Register #(.width(32), .Select("low")) register_1 (.D(EX_R1), .en(and_6_out), .Q(LedData), .clk(CLK), .clr(RST));
  Counter #(.width(16), .max('hffff)) counter_3 (
    .count(and_8_out), .Q(\条件分支成功数 ), .clk(CLK), .clr(RST));  // open: load, D, carry, preset, down
  Counter #(.width(16), .max('hffff)) counter_4 (
    .count(and_9_out), .Q(\LoadUse次数 ), .clk(CLK), .clr(RST));  // open: load, D, carry, preset, down
  Comparator #(.width(16)) comparator_5 (.a(16'h2c0), .b(\总周期数 ), .eq(comparator_5_eq));  // open: gt, lt
  or or_13 (or_13_out, comparator_5_eq, comparator_6_eq);
  Comparator #(.width(16)) comparator_6 (.a(\总周期数 ), .b(16'h1), .eq(comparator_6_eq));  // open: gt, lt
  Comparator #(.width(16)) comparator_7 (.a(\总周期数 ), .b(16'h4), .eq(comparator_7_eq));  // open: gt, lt
  Comparator #(.width(16)) comparator_8 (.a(\总周期数 ), .b(16'h7), .eq(comparator_8_eq));  // open: gt, lt
  Pull_Resistor pull_resistor_5 (.node(IRA));
  assign IRA = or_13_out ? ~CLK : 1'bz;  // Controlled_Inverter controlled_inverter_1
  Pull_Resistor pull_resistor_6 (.node(IRB));
  assign IRB = comparator_7_eq ? ~CLK : 1'bz;  // Controlled_Inverter controlled_inverter_2
  Pull_Resistor pull_resistor_7 (.node(IRC));
  assign IRC = comparator_8_eq ? ~CLK : 1'bz;  // Controlled_Inverter controlled_inverter_3
  and and_10 (and_10_out, ~halt, Flush);  // AND_Gate
  Counter #(.width(16), .max('hffff)) counter_5 (
    .count(and_10_out), .Q(\插入气泡数 ), .clk(CLK), .clr(RST));  // open: load, D, carry, preset, down

  // Other names for the same wires on the sheet: MEM_PC[31:0] = M_PC

  // Notes on the sheet:
  //   中断源
  //   时空图监测，可删除
  //   中断等待指示
  //   数码管输出
  //   指令存储器
  //   contents of rom_1 (hex, n*v repeats v):
  //   7d000113 100413 1f41993 41f9d993 433 c00913 800b13 140413 f47413 800293 100313 499993 89e9b3 1300533
  //   2200893 73 406282b3 fe0294e3 140413 f00f93 1f47433 1c41413 800293 100313 49d993 89e9b3 1300533
  //   2200893 73 406282b3 fe0294e3 1c45413 406b0b33 b0463 f95ff06f 2b3 fff2c293 1029293 fff2e293 500533
  //   2200893 73 f5dff06f 1112023 410113 a12023 410113 812023 410113 1312023 410113 1412023 410113 1512023
  //   410113 1612023 410113 100b13 300a13 100a93 1600433 441413 14469b3 1300533 2200893 73 fe0416e3
  //   415a0a33 fe0a10e3 ffc10113 12b03 ffc10113 12a83 ffc10113 12a03 ffc10113 12983 ffc10113 12403
  //   ffc10113 12503 ffc10113 12883 200073 1112023 410113 a12023 410113 812023 410113 1312023 410113
  //   1412023 410113 1512023 410113 1612023 410113 200b13 300a13 100a93 1600433 441413 14469b3 1300533
  //   2200893 73 fe0416e3 415a0a33 fe0a10e3 ffc10113 12b03 ffc10113 12a83 ffc10113 12a03 ffc10113 12983
  //   ffc10113 12403 ffc10113 12503 ffc10113 12883 200073 1112023 410113 a12023 410113 812023 410113
  //   1312023 410113 1412023 410113 1512023 410113 1612023 410113 300b13 300a13 100a93 1600433 441413
  //   14469b3 1300533 2200893 73 fe0416e3 415a0a33 fe0a10e3 ffc10113 12b03 ffc10113 12a83 ffc10113 12a03
  //   ffc10113 12983 ffc10113 12403 ffc10113 12503 ffc10113 12883 200073
  //   Reset 
  //   Reset 
  //   Reset 
  //   Rd[4:0]
  //   JALR
  //   URET
  //   I-Imm[11:0]
  //   S-Imm[11:0]
  //   B-Imm[12:1]
  //   J-Imm[20:1]
  //   JAL
  //   Beq
  //   Bne
  //   Blt[u]
  //   MemToReg
  //   MemWrite
  //   AluOP
  //   AluResult
  //   AluSrcB
  //   RegWrite
  //   MemVariant
  //   I/S-ImmType
  //   控制位
  //   流水调试日志用
  //   暂停节拍，不能为0
  //   戳工具置1进入计数暂停模式，ctrl+k时钟自动运行到对应节拍暂停
  //   ctrl+k关闭时钟连续运行，将控制位置零，进入单步调试模式调试
  //   可计数暂停的时钟源
  //   为方便自动评测，需要输出流水线各段保存的PC值，注意是PC不是PC+4，另外ID段寄存器写入信息，Mem段内存写入信息也要输出
  //   数据存储器
  //   单级中断测试信号模拟器
endmodule
module BranchBufferUnit (
  input  [31:0] IF_InstrAddr,
  input  EX_Write,
  input  [31:0] EX_InstrAddr,
  input  [31:0] EX_TargetAddr,
  input  EN,
  input  EX_Preset,
  input  [1:0] EX_PresetPredict,
  input  EX_Branch,
  input  CLK,
  input  RST,
  output IF_Hit,
  output EX_Hit,
  output [31:0] TargetAddr,
  output [15:0] LastUsed,
  output PredictJmp
);

  wire d_ff_1_q, not_1_out;
  wire [0:0] PredictState_q;
  wire [31:0] InstrAddr_q;

  Pull_Resistor pull_resistor_1 (.node(EX_Write));
  Pull_Resistor pull_resistor_2 (.node(EX_Preset));
  Pull_Resistor pull_resistor_3 (.node(EX_Branch));
  D_Flip_Flop #(.Pre_Clr_Positions("LEGACY"), .NewFFLayout("false")) d_ff_1 (
    .clk(CLK), .D(EX_Write), .Q(d_ff_1_q));  // open: Qn, preset, reset
  not not_1 (not_1_out, EX_Branch);
  Register #(.width(32), .Select("low")) InstrAddr (
    .D(EX_InstrAddr), .en(EX_Write), .Q(InstrAddr_q), .clk(CLK), .clr(RST));
  Register #(.width(32), .Select("low")) u_TargetAddr (
    .D(EX_TargetAddr), .en(EX_Write), .Q(TargetAddr), .clk(CLK), .clr(RST));
  Counter #(.width(16), .max('hffff), .ongoal("stay")) u_LastUsed (
    .load(RST), .D({16{1'b1}}), .count(EN), .Q(LastUsed), .clk(CLK), .clr(d_ff_1_q));  // open: carry, preset, down
  Counter #(.width(2), .max('h3), .ongoal("stay")) PredictState (
    .load(EX_Preset), .D(EX_PresetPredict), .count(EX_Write), .Q({PredictJmp, PredictState_q[0]}), .clk(CLK),
    .down(not_1_out));  // open: carry, clr, preset
  Comparator #(.width(32), .mode("unsigned")) comparator_1 (
    .a(IF_InstrAddr), .b(InstrAddr_q), .eq(IF_Hit));  // open: gt, lt
  Comparator #(.width(32), .mode("unsigned")) comparator_2 (
    .a(EX_InstrAddr), .b(InstrAddr_q), .eq(EX_Hit));  // open: gt, lt
endmodule

module BranchTargetBuffer (
  input  [31:0] IF_InstrAddr,
  input  [31:0] EX_InstrAddr,
  input  [31:0] EX_TargetAddr,
  input  [1:0] EX_PresetState,
  input  EX_Branch,
  input  EX_Check,
  input  EN,
  input  CLK,
  input  RST,
  input  EX_BranchPredicted,
  output [31:0] IF_TargetAddrPredicted,
  output IF_BranchPredicted,
  output EX_PredictFail,
  output EX_PredictSuccess
);

  wire and_1_out, comparator_1_lt, comparator_2_lt, comparator_3_lt, comparator_4_lt, comparator_5_lt,
       comparator_6_lt, comparator_8_eq, demultiplexer_1_out0, demultiplexer_1_out1, demultiplexer_1_out2,
       demultiplexer_1_out3, demultiplexer_1_out4, demultiplexer_1_out5, demultiplexer_1_out6,
       demultiplexer_1_out7, demultiplexer_2_out0, demultiplexer_2_out1, demultiplexer_2_out2,
       demultiplexer_2_out3, demultiplexer_2_out4, demultiplexer_2_out5, demultiplexer_2_out6,
       demultiplexer_2_out7, EX_Hit, EX_Hit0, EX_Hit1, EX_Hit2, EX_Hit3, EX_Hit4, EX_Hit5, EX_Hit6, EX_Hit7,
       IF_Hit, IF_Hit0, IF_Hit1, IF_Hit2, IF_Hit3, IF_Hit4, IF_Hit5, IF_Hit6, IF_Hit7, multiplexer_5_out,
       multiplexer_7_out, multiplexer_12_out, nand_1_out, not_1_out, or_1_out, Predict0, Predict1, Predict2,
       Predict3, Predict4, Predict5, Predict6, Predict7, xnor_1_out;
  wire [2:0] EX_HitSlot, FreeSlot, IF_HitSlot, WriteSlot;
  wire [15:0] branchbufferunit_1_lastused, branchbufferunit_2_lastused, branchbufferunit_3_lastused,
       branchbufferunit_4_lastused, branchbufferunit_5_lastused, branchbufferunit_6_lastused,
       branchbufferunit_7_lastused, branchbufferunit_8_lastused, multiplexer_1_out, multiplexer_2_out,
       multiplexer_3_out, multiplexer_4_out, multiplexer_6_out, multiplexer_8_out;
  wire [31:0] EX_TargetAddrPredicted, TargetAddr0, TargetAddr1, TargetAddr2, TargetAddr3, TargetAddr4,
       TargetAddr5, TargetAddr6, TargetAddr7;

  Demultiplexer #(.select(3), .enable("false")) demultiplexer_1 (
    .out0(demultiplexer_1_out0), .out1(demultiplexer_1_out1), .out2(demultiplexer_1_out2),
    .out3(demultiplexer_1_out3), .out4(demultiplexer_1_out4), .out5(demultiplexer_1_out5),
    .out6(demultiplexer_1_out6), .out7(demultiplexer_1_out7), .in(EX_Check), .sel(WriteSlot));
  and and_1 (and_1_out, EX_Check, ~EX_Hit);  // AND_Gate
  Demultiplexer #(.select(3), .enable("false")) demultiplexer_2 (
    .out0(demultiplexer_2_out0), .out1(demultiplexer_2_out1), .out2(demultiplexer_2_out2),
    .out3(demultiplexer_2_out3), .out4(demultiplexer_2_out4), .out5(demultiplexer_2_out5),
    .out6(demultiplexer_2_out6), .out7(demultiplexer_2_out7), .in(and_1_out), .sel(WriteSlot));
  Pull_Resistor pull_resistor_1 (.node(EX_PresetState));
  BranchBufferUnit branchbufferunit_1 (
    .IF_InstrAddr(IF_InstrAddr), .EX_Write(demultiplexer_1_out0), .EX_InstrAddr(EX_InstrAddr),
    .EX_TargetAddr(EX_TargetAddr), .EX_Preset(demultiplexer_2_out0), .EX_PresetPredict(EX_PresetState),
    .EX_Branch(EX_Branch), .IF_Hit(IF_Hit0), .EX_Hit(EX_Hit0), .TargetAddr(TargetAddr0),
    .LastUsed(branchbufferunit_1_lastused), .PredictJmp(Predict0), .CLK(CLK), .RST(RST), .EN(EN));
  BranchBufferUnit branchbufferunit_2 (
    .IF_InstrAddr(IF_InstrAddr), .EX_Write(demultiplexer_1_out1), .EX_InstrAddr(EX_InstrAddr),
    .EX_TargetAddr(EX_TargetAddr), .EX_Preset(demultiplexer_2_out1), .EX_PresetPredict(EX_PresetState),
    .EX_Branch(EX_Branch), .IF_Hit(IF_Hit1), .EX_Hit(EX_Hit1), .TargetAddr(TargetAddr1),
    .LastUsed(branchbufferunit_2_lastused), .PredictJmp(Predict1), .CLK(CLK), .RST(RST), .EN(EN));
  BranchBufferUnit branchbufferunit_3 (
    .IF_InstrAddr(IF_InstrAddr), .EX_Write(demultiplexer_1_out2), .EX_InstrAddr(EX_InstrAddr),
    .EX_TargetAddr(EX_TargetAddr), .EX_Preset(demultiplexer_2_out2), .EX_PresetPredict(EX_PresetState),
    .EX_Branch(EX_Branch), .IF_Hit(IF_Hit2), .EX_Hit(EX_Hit2), .TargetAddr(TargetAddr2),
    .LastUsed(branchbufferunit_3_lastused), .PredictJmp(Predict2), .CLK(CLK), .RST(RST), .EN(EN));
  BranchBufferUnit branchbufferunit_4 (
    .IF_InstrAddr(IF_InstrAddr), .EX_Write(demultiplexer_1_out3), .EX_InstrAddr(EX_InstrAddr),
    .EX_TargetAddr(EX_TargetAddr), .EX_Preset(demultiplexer_2_out3), .EX_PresetPredict(EX_PresetState),
    .EX_Branch(EX_Branch), .IF_Hit(IF_Hit3), .EX_Hit(EX_Hit3), .TargetAddr(TargetAddr3),
    .LastUsed(branchbufferunit_4_lastused), .PredictJmp(Predict3), .CLK(CLK), .RST(RST), .EN(EN));
  BranchBufferUnit branchbufferunit_5 (
    .IF_InstrAddr(IF_InstrAddr), .EX_Write(demultiplexer_1_out4), .EX_InstrAddr(EX_InstrAddr),
    .EX_TargetAddr(EX_TargetAddr), .EX_Preset(demultiplexer_2_out4), .EX_PresetPredict(EX_PresetState),
    .EX_Branch(EX_Branch), .IF_Hit(IF_Hit4), .EX_Hit(EX_Hit4), .TargetAddr(TargetAddr4),
    .LastUsed(branchbufferunit_5_lastused), .PredictJmp(Predict4), .CLK(CLK), .RST(RST), .EN(EN));
  BranchBufferUnit branchbufferunit_6 (
    .IF_InstrAddr(IF_InstrAddr), .EX_Write(demultiplexer_1_out5), .EX_InstrAddr(EX_InstrAddr),
    .EX_TargetAddr(EX_TargetAddr), .EX_Preset(demultiplexer_2_out5), .EX_PresetPredict(EX_PresetState),
    .EX_Branch(EX_Branch), .IF_Hit(IF_Hit5), .EX_Hit(EX_Hit5), .TargetAddr(TargetAddr5),
    .LastUsed(branchbufferunit_6_lastused), .PredictJmp(Predict5), .CLK(CLK), .RST(RST), .EN(EN));
  BranchBufferUnit branchbufferunit_7 (
    .IF_InstrAddr(IF_InstrAddr), .EX_Write(demultiplexer_1_out6), .EX_InstrAddr(EX_InstrAddr),
    .EX_TargetAddr(EX_TargetAddr), .EX_Preset(demultiplexer_2_out6), .EX_PresetPredict(EX_PresetState),
    .EX_Branch(EX_Branch), .IF_Hit(IF_Hit6), .EX_Hit(EX_Hit6), .TargetAddr(TargetAddr6),
    .LastUsed(branchbufferunit_7_lastused), .PredictJmp(Predict6), .CLK(CLK), .RST(RST), .EN(EN));
  BranchBufferUnit branchbufferunit_8 (
    .IF_InstrAddr(IF_InstrAddr), .EX_Write(demultiplexer_1_out7), .EX_InstrAddr(EX_InstrAddr),
    .EX_TargetAddr(EX_TargetAddr), .EX_Preset(demultiplexer_2_out7), .EX_PresetPredict(EX_PresetState),
    .EX_Branch(EX_Branch), .IF_Hit(IF_Hit7), .EX_Hit(EX_Hit7), .TargetAddr(TargetAddr7),
    .LastUsed(branchbufferunit_8_lastused), .PredictJmp(Predict7), .CLK(CLK), .RST(RST), .EN(EN));
  Comparator #(.width(16), .mode("unsigned")) comparator_1 (
    .a(branchbufferunit_1_lastused), .b(branchbufferunit_2_lastused), .lt(comparator_1_lt));  // open: gt, eq
  Comparator #(.width(16), .mode("unsigned")) comparator_2 (
    .a(branchbufferunit_3_lastused), .b(branchbufferunit_4_lastused), .lt(comparator_2_lt));  // open: gt, eq
  Comparator #(.width(16), .mode("unsigned")) comparator_3 (
    .a(branchbufferunit_5_lastused), .b(branchbufferunit_6_lastused), .lt(comparator_3_lt));  // open: gt, eq
  Comparator #(.width(16), .mode("unsigned")) comparator_4 (
    .a(branchbufferunit_7_lastused), .b(branchbufferunit_8_lastused), .lt(comparator_4_lt));  // open: gt, eq
  Multiplexer #(.width(16), .enable("false")) multiplexer_1 (
    .in0(branchbufferunit_1_lastused), .in1(branchbufferunit_2_lastused), .out(multiplexer_1_out),
    .sel(comparator_1_lt));
  Multiplexer #(.width(16), .enable("false")) multiplexer_2 (
    .in0(branchbufferunit_3_lastused), .in1(branchbufferunit_4_lastused), .out(multiplexer_2_out),
    .sel(comparator_2_lt));
  Multiplexer #(.width(16), .enable("false")) multiplexer_3 (
    .in0(branchbufferunit_5_lastused), .in1(branchbufferunit_6_lastused), .out(multiplexer_3_out),
    .sel(comparator_3_lt));
  Multiplexer #(.width(16), .enable("false")) multiplexer_4 (
    .in0(branchbufferunit_7_lastused), .in1(branchbufferunit_8_lastused), .out(multiplexer_4_out),
    .sel(comparator_4_lt));
  Multiplexer #(.enable("false")) multiplexer_5 (
    .in0(comparator_1_lt), .in1(comparator_2_lt), .out(multiplexer_5_out), .sel(comparator_5_lt));
  Comparator #(.width(16), .mode("unsigned")) comparator_5 (
    .a(multiplexer_1_out), .b(multiplexer_2_out), .lt(comparator_5_lt));  // open: gt, eq
  Multiplexer #(.width(16), .enable("false")) multiplexer_6 (
    .in0(multiplexer_1_out), .in1(multiplexer_2_out), .out(multiplexer_6_out), .sel(comparator_5_lt));
  Multiplexer #(.enable("false")) multiplexer_7 (
    .in0(comparator_3_lt), .in1(comparator_4_lt), .out(multiplexer_7_out), .sel(comparator_6_lt));
  Comparator #(.width(16), .mode("unsigned")) comparator_6 (
    .a(multiplexer_3_out), .b(multiplexer_4_out), .lt(comparator_6_lt));  // open: gt, eq
  Multiplexer #(.width(16), .enable("false")) multiplexer_8 (
    .in0(multiplexer_3_out), .in1(multiplexer_4_out), .out(multiplexer_8_out), .sel(comparator_6_lt));
  Multiplexer #(.enable("false")) multiplexer_9 (
    .in0(multiplexer_5_out), .in1(multiplexer_7_out), .out(FreeSlot[0]), .sel(FreeSlot[2]));
  Multiplexer #(.enable("false")) multiplexer_10 (
    .in0(comparator_5_lt), .in1(comparator_6_lt), .out(FreeSlot[1]), .sel(FreeSlot[2]));
  Comparator #(.width(16), .mode("unsigned")) comparator_7 (
    .a(multiplexer_6_out), .b(multiplexer_8_out), .lt(FreeSlot[2]));  // open: gt, eq
  Pull_Resistor pull_resistor_2 (.node(IF_HitSlot));
  Priority_Encoder priority_encoder_1 (
    .in0(IF_Hit0), .in1(IF_Hit1), .in2(IF_Hit2), .in3(IF_Hit3), .in4(IF_Hit4), .in5(IF_Hit5), .in6(IF_Hit6),
    .in7(IF_Hit7), .out(IF_HitSlot), .gs(IF_Hit));  // open: en_out, en_in
  Multiplexer #(.select(3), .width(32), .enable("false")) multiplexer_11 (
    .in0(TargetAddr0), .in1(TargetAddr1), .in2(TargetAddr2), .in3(TargetAddr3), .in4(TargetAddr4),
    .in5(TargetAddr5), .in6(TargetAddr6), .in7(TargetAddr7), .out(IF_TargetAddrPredicted), .sel(IF_HitSlot));
  Multiplexer #(.select(3), .enable("false")) multiplexer_12 (
    .in0(Predict0), .in1(Predict1), .in2(Predict2), .in3(Predict3), .in4(Predict4), .in5(Predict5),
    .in6(Predict6), .in7(Predict7), .out(multiplexer_12_out), .sel(IF_HitSlot));
  and and_2 (IF_BranchPredicted, multiplexer_12_out, IF_Hit);
  Comparator #(.width(32), .mode("unsigned")) comparator_8 (
    .a(EX_TargetAddrPredicted), .b(EX_TargetAddr), .eq(comparator_8_eq));  // open: gt, lt
  Pull_Resistor pull_resistor_3 (.node(EX_HitSlot));
  Priority_Encoder priority_encoder_2 (
    .in0(EX_Hit0), .in1(EX_Hit1), .in2(EX_Hit2), .in3(EX_Hit3), .in4(EX_Hit4), .in5(EX_Hit5), .in6(EX_Hit6),
    .in7(EX_Hit7), .out(EX_HitSlot), .gs(EX_Hit));  // open: en_out, en_in
  Multiplexer #(.select(3), .width(32), .enable("false")) multiplexer_13 (
    .in0(TargetAddr0), .in1(TargetAddr1), .in2(TargetAddr2), .in3(TargetAddr3), .in4(TargetAddr4),
    .in5(TargetAddr5), .in6(TargetAddr6), .in7(TargetAddr7), .out(EX_TargetAddrPredicted), .sel(EX_HitSlot));
  Multiplexer #(.width(3), .enable("false")) multiplexer_14 (
    .in0(FreeSlot), .in1(EX_HitSlot), .out(WriteSlot), .sel(EX_Hit));
  or or_1 (or_1_out, ~EX_Hit, comparator_8_eq);  // OR_Gate
  nand nand_1 (nand_1_out, or_1_out, xnor_1_out);
  xnor xnor_1 (xnor_1_out, EX_BranchPredicted, EX_Branch);
  and and_3 (EX_PredictSuccess, EX_Check, not_1_out);
  not not_1 (not_1_out, nand_1_out);
  and and_4 (EX_PredictFail, nand_1_out, EX_Check);

  // Other names for the same wires on the sheet: IF_PredictJmp = IF_BranchPredicted
endmodule

module \分支预测流水线  (
  output RegWrite,
  output MemWrite,
  output [31:0] IF_PC,
  output [31:0] ID_PC,
  output [31:0] EX_PC,
  output [31:0] M_PC,
  output [31:0] WB_PC,
  output [31:0] RDin,
  output [31:0] MDin,
  output [31:0] LedData
);

  wire and_1_out, and_2_out, and_3_out, and_5_out, and_6_out, and_7_out, and_8_out, and_9_out, and_10_out,
       and_11_out, and_12_out, BranchInstr, CLK, clock_1_out, comparator_1_eq, comparator_2_eq,
       comparator_2_lt, comparator_3_eq, CondBranch, d_ff_1_q, Eq, EX_BranchPredicted, EX_Check, EX_ECALL,
       EX_Halt, EX_Jmp, ex_mem_1_halt_2, ex_mem_1_memtoreg_2, ex_mem_1_regwrite_2, EX_PredictFail, Flush,
       forwardbubblegen_1_ex_mem_en, forwardbubblegen_1_id_ex_en, forwardbubblegen_1_id_ex_flush,
       forwardbubblegen_1_if_id_en, forwardbubblegen_1_if_id_flush, forwardbubblegen_1_mem_wb_en,
       forwardbubblegen_1_pc_en, Ge, Go, halt, id_ex_1_alusrcb_2, id_ex_1_beq_2, id_ex_1_blt_u_2,
       id_ex_1_bne_2, id_ex_1_memtoreg_2, id_ex_1_memwrite_2, id_ex_1_regwrite_2, id_ex_1_uret_2,
       IF_BranchPredicted, if_id_1_predictbranch_2, IR1, IR2, IR3, JAL, JALR, LoadUse, Lt, mem_wb_1_halt_2,
       mem_wb_1_memtoreg_2, nand_1_out, not_1_out, not_2_out, not_3_out, not_4_out, or_2_out, PredictSuccess,
       pull_resistor_1_node, pull_resistor_2_node, RST, UncondJmp, W1, W2, W3, \单周期硬布线控制器_1_alu_result ,
       \单周期硬布线控制器_1_alu_src , \单周期硬布线控制器_1_beq , \单周期硬布线控制器_1_blt_u , \单周期硬布线控制器_1_bne , \单周期硬布线控制器_1_ecall ,
       \单周期硬布线控制器_1_jal , \单周期硬布线控制器_1_jalr , \单周期硬布线控制器_1_memtoreg , \单周期硬布线控制器_1_memwrite ,
       \单周期硬布线控制器_1_r1dep , \单周期硬布线控制器_1_r2dep , \单周期硬布线控制器_1_regwrite , \单周期硬布线控制器_1_s_type ,
       \单周期硬布线控制器_1_uret ;
  wire [1:0] forwardbubblegen_1_r1forwardsrc, forwardbubblegen_1_r2forwardsrc, id_ex_1_r1forwardsrc_2,
       id_ex_1_r2forwardsrc_2, PCType, pctype_1_linktoreg, priority_encoder_1_out;
  wire [1:1] or_1_out;
  wire [2:0] ex_mem_1_memvariant_2, id_ex_1_memvariant_2, \单周期硬布线控制器_1_func3 ;
  wire [3:0] id_ex_1_aluop_2, \单周期硬布线控制器_1_alu_op ;
  wire [4:0] ex_mem_1_rd_num_2, id_ex_1_rd_num_2, multiplexer_3_out, multiplexer_4_out, WB_Rd;
  wire [7:0] bitselector_1_out;
  wire [11:0] multiplexer_5_out;
  wire [12:0] CNT_num;
  wire [15:0] bitselector_2_out, \LoadUse次数 , \总周期数 , \插入气泡数 , \无条件分支数 , \无条件直接跳转 , \无条件相对跳转 , \条件分支成功数 ,
       \条件分支指令数 , \跳转预测失败数 , \跳转预测成功数 ;
  wire [31:0] alu_1_result_2, bit_extender_1_out, bit_extender_2_out, bit_extender_3_out, bit_extender_4_out,
       bit_extender_5_out, bit_extender_6_out, bit_extender_7_out, DynamicPredictPC, EX_IR, EX_PCp4, EX_R1,
       EX_R2, id_ex_1_aluimm_2, id_ex_1_jmpimm_2, id_ex_1_r1_2, id_ex_1_r2_2, ID_IR, IF_IR, IF_JALTargetAddr,
       IF_PCp4, MEM_IR, MEM_RDin, mem_wb_1_memreaddata_2, mem_wb_1_result_2, multiplexer_1_out,
       multiplexer_2_out, multiplexer_9_out, multiplexer_10_out, multiplexer_11_out, multiplexer_12_out,
       multiplexer_13_out, multiplexer_14_out, PCRelJmp, PredictedPC, ram_1_data, regifile_1_r1,
       regifile_1_r2, RegRelJmp, WB_IR, WB_PCp4;

  Button \u_总复位  (.out(RST));
  Button _1 (.out(IR1));
  Button _2 (.out(IR2));
  Button _3 (.out(IR3));
  // Probe on \总周期数 
  // Probe on \总周期数 
  ForwardBubbleGen forwardbubblegen_1 (
    .Halt(halt), .R1Dep(\单周期硬布线控制器_1_r1dep ), .EX_RegWrite(id_ex_1_regwrite_2), .EX_Rd(id_ex_1_rd_num_2),
    .R1(multiplexer_3_out), .Jmp(EX_PredictFail), .R2Dep(\单周期硬布线控制器_1_r2dep ),
    .MEM_RegWrite(ex_mem_1_regwrite_2), .MEM_Rd(ex_mem_1_rd_num_2), .R2(multiplexer_4_out),
    .PC_EN(forwardbubblegen_1_pc_en), .IF_ID_EN(forwardbubblegen_1_if_id_en),
    .IF_ID_FLUSH(forwardbubblegen_1_if_id_flush), .ID_EX_FLUSH(forwardbubblegen_1_id_ex_flush),
    .ID_EX_EN(forwardbubblegen_1_id_ex_en), .EX_MEM_EN(forwardbubblegen_1_ex_mem_en),
    .MEM_WB_EN(forwardbubblegen_1_mem_wb_en), .R1ForwardSrc(forwardbubblegen_1_r1forwardsrc),
    .R2ForwardSrc(forwardbubblegen_1_r2forwardsrc), .EX_MemToReg(id_ex_1_memtoreg_2), .LoadUse(LoadUse),
    .Flush(Flush), .Intr(pull_resistor_1_node), .PredictFail(pull_resistor_2_node));  // open: Stall
  Button \u_继续运行  (.out(Go));
  LED led_1 (.in(W1));
  LED led_2 (.in(W2));
  LED led_3 (.in(W3));
  Pull_Resistor pull_resistor_1 (.node(pull_resistor_1_node));
  Pull_Resistor pull_resistor_2 (.node(pull_resistor_2_node));
  // Probe on PCType
  Multiplexer #(.select(2), .width(32), .enable("false")) multiplexer_1 (
    .in0(EX_PCp4), .in2(RegRelJmp), .in3(PCRelJmp), .out(multiplexer_1_out), .sel(PCType));  // open: in1
  // Probe on multiplexer_1_out
  Hex_Digit_Display hex_digit_display_1 (.value(LedData[31:28]));  // open: dp
  // Probe on IF_PC[19:0]
  // RiscV_Probe riscv_probe_1: pin names not known; wires that end beside it: IF_IR
  not not_1 (not_1_out, EX_PredictFail);
  Multiplexer #(.width(32), .enable("false")) multiplexer_2 (
    .in0(multiplexer_1_out), .in1(PredictedPC), .out(multiplexer_2_out), .sel(not_1_out));
  Hex_Digit_Display hex_digit_display_2 (.value(LedData[27:24]));  // open: dp
  Hex_Digit_Display hex_digit_display_3 (.value(LedData[23:20]));  // open: dp
  // Probe on ID_PC[19:0]
  // RiscV_Probe riscv_probe_2: pin names not known; wires that end beside it: ID_IR
  Register #(.width(32), .Select("low")) PC (
    .D(multiplexer_2_out), .en(forwardbubblegen_1_pc_en), .Q(IF_PC), .clk(CLK), .clr(RST));
  Hex_Digit_Display hex_digit_display_4 (.value(LedData[19:16]));  // open: dp
  Hex_Digit_Display hex_digit_display_5 (.value(LedData[15:12]));  // open: dp
  Hex_Digit_Display hex_digit_display_6 (.value(LedData[7:4]));  // open: dp
  Hex_Digit_Display hex_digit_display_7 (.value(LedData[11:8]));  // open: dp
  // Probe on EX_PC[19:0]
  // RiscV_Probe riscv_probe_3: pin names not known; wires that end beside it: EX_IR
  ROM #(.addrWidth(10), .dataWidth(32), .Select("high")) rom_1 (.addr(IF_PC[11:2]), .data(IF_IR));
  Adder #(.width(32)) adder_1 (.a(IF_PC), .b(32'h4), .out(IF_PCp4));  // open: cin, cout
  Hex_Digit_Display hex_digit_display_8 (.value(LedData[3:0]));  // open: dp
  IF_ID if_id_1 (
    .IR(IF_IR), .PC(IF_PC), .FLUSH(forwardbubblegen_1_if_id_flush), .IR_2(ID_IR), .PC_2(ID_PC), .RST(RST),
    .EN(forwardbubblegen_1_if_id_en), .CLK(CLK), .PredictBranch(IF_BranchPredicted),
    .PredictBranch_2(if_id_1_predictbranch_2));
  // Probe on \总周期数 
  // Probe on M_PC[19:0]
  // RiscV_Probe riscv_probe_4: pin names not known; wires that end beside it: MEM_IR
  // Probe on \总周期数 
  // Probe on \无条件分支数 
  // Probe on \条件分支成功数 
  // Probe on \插入气泡数 
  // Probe on \LoadUse次数 
  \单周期硬布线控制器  \u_单周期硬布线控制器_1  (
    .Funct({ID_IR[30], ID_IR[25], ID_IR[14:12]}), .OP(ID_IR[6:2]), .ALU_OP(\单周期硬布线控制器_1_alu_op ),
    .MemToReg(\单周期硬布线控制器_1_memtoreg ), .MemWrite(\单周期硬布线控制器_1_memwrite ), .ALU_SRC(\单周期硬布线控制器_1_alu_src ),
    .RegWrite(\单周期硬布线控制器_1_regwrite ), .ecall(\单周期硬布线控制器_1_ecall ), .S_type(\单周期硬布线控制器_1_s_type ),
    .JALR(\单周期硬布线控制器_1_jalr ), .Beq(\单周期硬布线控制器_1_beq ), .JAL(\单周期硬布线控制器_1_jal ), .Bne(\单周期硬布线控制器_1_bne ),
    .in_3(ID_IR[21]), .uret(\单周期硬布线控制器_1_uret ), .Func3(\单周期硬布线控制器_1_func3 ),
    .ALU_RESULT(\单周期硬布线控制器_1_alu_result ), .Blt_u(\单周期硬布线控制器_1_blt_u ), .R1Dep(\单周期硬布线控制器_1_r1dep ),
    .R2Dep(\单周期硬布线控制器_1_r2dep ), .LegitIR(ID_IR[1:0]));  // open: CSR
  Multiplexer #(.width(5), .enable("false")) multiplexer_3 (
    .in0(ID_IR[19:15]), .in1(5'b01010), .out(multiplexer_3_out), .sel(\单周期硬布线控制器_1_ecall ));
  Multiplexer #(.width(5), .enable("false")) multiplexer_4 (
    .in0(ID_IR[24:20]), .in1(5'b10001), .out(multiplexer_4_out), .sel(\单周期硬布线控制器_1_ecall ));
  // Probe on WB_PC[19:0]
  // RiscV_Probe riscv_probe_5: pin names not known; wires that end beside it: WB_IR
  // Probe on multiplexer_3_out
  // Probe on multiplexer_4_out
  // Probe on WB_Rd
  Multiplexer #(.width(12), .enable("false")) multiplexer_5 (
    .in0(ID_IR[31:20]), .in1({ID_IR[31:25], ID_IR[11:7]}), .out(multiplexer_5_out), .sel(\单周期硬布线控制器_1_s_type ));
  assign bit_extender_1_out = {{19{ID_IR[31]}}, {ID_IR[31], ID_IR[7], ID_IR[30:25], ID_IR[11:8], 1'b0}};  // Bit_Extender bit_extender_1
  assign bit_extender_2_out = {{11{IF_IR[31]}}, {IF_IR[31], IF_IR[19:12], IF_IR[20], IF_IR[30:21], 1'b0}};  // Bit_Extender bit_extender_2
  Adder #(.width(32)) adder_2 (.a(bit_extender_2_out), .b(IF_PC), .out(IF_JALTargetAddr));  // open: cin, cout
  // Probe on \无条件直接跳转 
  // Probe on \无条件相对跳转 
  // Probe on \条件分支指令数 
  // Probe on \跳转预测成功数 
  // Probe on \跳转预测失败数 
  not not_2 (not_2_out, CLK);
  assign bit_extender_3_out = {{20{multiplexer_5_out[11]}}, multiplexer_5_out};  // Bit_Extender bit_extender_3
  Comparator #(.width(5), .mode("unsigned")) comparator_1 (
    .a(IF_IR[6:2]), .b(5'b11011), .eq(comparator_1_eq));  // open: gt, lt
  D_Flip_Flop #(.trigger("high"), .Pre_Clr_Positions("LEGACY"), .enable("true"), .NewFFLayout("false")) d_ff_1 (.Q(d_ff_1_q));  // open: clk, D, Qn, preset, en, reset
  // Probe on 13'h38
  Regifile regifile_1 (
    .Din(RDin), .Clk(not_2_out), .R1(regifile_1_r1), .R2(regifile_1_r2), .WE(RegWrite), .W_num(WB_Rd),
    .R1_num(multiplexer_3_out), .R2_num(multiplexer_4_out));
  // Probe on bit_extender_3_out
  and and_1 (and_1_out, IF_IR[6], IF_BranchPredicted);
  Priority_Encoder #(.select(2)) priority_encoder_1 (
    .in0(1'b1), .in1(and_1_out), .in3(comparator_1_eq), .out(priority_encoder_1_out));  // open: in2, gs, en_out, en_in
  Multiplexer #(.select(2), .width(32), .enable("false")) multiplexer_6 (
    .in0(IF_PCp4), .in1(DynamicPredictPC), .in3(IF_JALTargetAddr), .out(PredictedPC),
    .sel(priority_encoder_1_out));  // open: in2
  // Probe on IF_PC[11:0]
  Comparator #(.width(13)) comparator_2 (
    .a(CNT_num), .b(13'h38), .eq(comparator_2_eq), .lt(comparator_2_lt));  // open: gt
  Clock clock_1 (.out(clock_1_out));
  ID_EX id_ex_1 (
    .IR(ID_IR), .PC(ID_PC), .PredictBranch(if_id_1_predictbranch_2), .FLUSH(forwardbubblegen_1_id_ex_flush),
    .IR_2(EX_IR), .PC_2(EX_PC), .PredictBranch_2(EX_BranchPredicted), .RST(RST),
    .EN(forwardbubblegen_1_id_ex_en), .CLK(CLK), .URET(\单周期硬布线控制器_1_uret ), .URET_2(id_ex_1_uret_2),
    .JALR(\单周期硬布线控制器_1_jalr ), .JALR_2(JALR), .JAL(\单周期硬布线控制器_1_jal ), .JAL_2(JAL), .BEQ(\单周期硬布线控制器_1_beq ),
    .BEQ_2(id_ex_1_beq_2), .BNE(\单周期硬布线控制器_1_bne ), .BNE_2(id_ex_1_bne_2), .BLT_U(\单周期硬布线控制器_1_blt_u ),
    .BLT_U_2(id_ex_1_blt_u_2), .MemToReg(\单周期硬布线控制器_1_memtoreg ), .MemToReg_2(id_ex_1_memtoreg_2),
    .MemWrite(\单周期硬布线控制器_1_memwrite ), .MemWrite_2(id_ex_1_memwrite_2), .AluOP(\单周期硬布线控制器_1_alu_op ),
    .AluOP_2(id_ex_1_aluop_2), .AluResult(\单周期硬布线控制器_1_alu_result ), .AluResult_2(pctype_1_linktoreg[1]),
    .AluSrcB(\单周期硬布线控制器_1_alu_src ), .AluSrcB_2(id_ex_1_alusrcb_2), .RegWrite(\单周期硬布线控制器_1_regwrite ),
    .RegWrite_2(id_ex_1_regwrite_2), .MemVariant(\单周期硬布线控制器_1_func3 ), .MemVariant_2(id_ex_1_memvariant_2),
    .Rd_num(ID_IR[11:7]), .Rd_num_2(id_ex_1_rd_num_2), .ECALL(\单周期硬布线控制器_1_ecall ), .ECALL_2(EX_ECALL),
    .JmpImm(bit_extender_1_out), .JmpImm_2(id_ex_1_jmpimm_2), .AluImm(bit_extender_3_out),
    .AluImm_2(id_ex_1_aluimm_2), .R2(regifile_1_r2), .R2_2(id_ex_1_r2_2), .R1(regifile_1_r1),
    .R1_2(id_ex_1_r1_2), .R1ForwardSrc(forwardbubblegen_1_r1forwardsrc),
    .R1ForwardSrc_2(id_ex_1_r1forwardsrc_2), .R2ForwardSrc(forwardbubblegen_1_r2forwardsrc),
    .R2ForwardSrc_2(id_ex_1_r2forwardsrc_2));
  // Probe on ID_PC[11:0]
  // Probe on EX_PC[11:0]
  nand nand_1 (nand_1_out, d_ff_1_q, comparator_2_eq);
  Counter #(.width(13), .max('h1fff), .ongoal("stay"), .behavior("old")) counter_1 (
    .count(comparator_2_lt), .Q(CNT_num), .clk(clock_1_out));  // open: load, D, carry, clr, preset
  Multiplexer #(.select(2), .width(32), .enable("false")) multiplexer_7 (
    .in0(id_ex_1_r1_2), .in1(RDin), .in2(MEM_RDin), .out(EX_R1), .sel(id_ex_1_r1forwardsrc_2));  // open: in3
  Adder #(.width(32)) adder_3 (.a(id_ex_1_jmpimm_2), .b(EX_PC), .out(PCRelJmp));  // open: cin, cout
  Adder #(.width(32)) adder_4 (.a(EX_PC), .b(32'h4), .out(EX_PCp4));  // open: cin, cout
  BranchTargetBuffer branchtargetbuffer_1 (
    .IF_InstrAddr(IF_PC), .EX_InstrAddr(EX_PC), .EX_TargetAddr(multiplexer_10_out),
    .EX_PresetState({2{or_1_out[1]}}), .EX_Branch(EX_Jmp), .EX_Check(EX_Check),
    .IF_TargetAddrPredicted(DynamicPredictPC), .IF_BranchPredicted(IF_BranchPredicted),
    .EX_PredictFail(EX_PredictFail), .CLK(CLK), .RST(RST), .EX_BranchPredicted(EX_BranchPredicted),
    .EX_PredictSuccess(PredictSuccess), .EN(not_3_out));
  not not_3 (not_3_out, halt);
  // Probe on M_PC[11:0]
  // Probe on WB_PC[11:0]
  assign CLK = nand_1_out ? clock_1_out : 1'bz;  // Controlled_Buffer controlled_buffer_1
  PCType pctype_1 (
    .JmpType(PCType), .Jmp(EX_Jmp), .Eq(Eq), .Lt(Lt), .Ge(Ge), .URET(id_ex_1_uret_2), .JALR(JALR), .JAL(JAL),
    .BEQ(id_ex_1_beq_2), .BNE(id_ex_1_bne_2), .BLT_U(id_ex_1_blt_u_2), .LinkToReg(pctype_1_linktoreg[0]),
    .UncondJmp(UncondJmp), .CondBranch(CondBranch), .UncertainJmp(EX_Check), .BranchInstr(BranchInstr));  // open: ImmJmp
  Multiplexer #(.select(2), .width(32), .enable("false")) multiplexer_8 (
    .in0(id_ex_1_r2_2), .in1(RDin), .in2(MEM_RDin), .out(EX_R2), .sel(id_ex_1_r2forwardsrc_2));  // open: in3
  Multiplexer #(.width(32), .enable("false")) multiplexer_9 (
    .in0(EX_R2), .in1(id_ex_1_aluimm_2), .out(multiplexer_9_out), .sel(id_ex_1_alusrcb_2));
  Pull_Resistor #(.pull(1)) pull_resistor_3 (.node(CLK));
  ALU alu_1 (
    .X(EX_R1), .Y(multiplexer_9_out), .AluOP(id_ex_1_aluop_2), .Equal(Eq), .Result(RegRelJmp),
    .Result_2(alu_1_result_2), .out_4(Ge), .out_6(Lt));
  Multiplexer #(.width(32), .enable("false")) multiplexer_10 (
    .in0(PCRelJmp), .in1(RegRelJmp), .out(multiplexer_10_out), .sel(JALR));
  Multiplexer #(.select(2), .width(32), .enable("false")) multiplexer_11 (
    .in0(RegRelJmp), .in1(EX_PCp4), .in2(alu_1_result_2), .out(multiplexer_11_out), .sel(pctype_1_linktoreg));  // open: in3
  or or_1 (or_1_out[1], JALR, EX_Jmp);
  EX_MEM ex_mem_1 (
    .EN(forwardbubblegen_1_ex_mem_en), .MemToReg(id_ex_1_memtoreg_2), .MemToReg_2(ex_mem_1_memtoreg_2),
    .MemWrite(id_ex_1_memwrite_2), .MemWrite_2(MemWrite), .RegWrite(id_ex_1_regwrite_2),
    .RegWrite_2(ex_mem_1_regwrite_2), .MemVariant(id_ex_1_memvariant_2),
    .MemVariant_2(ex_mem_1_memvariant_2), .Halt(EX_Halt), .Halt_2(ex_mem_1_halt_2),
    .Result(multiplexer_11_out), .Result_2(MEM_RDin), .MemWriteData(EX_R2), .MemWriteData_2(MDin),
    .Rd_num(id_ex_1_rd_num_2), .Rd_num_2(ex_mem_1_rd_num_2), .IR(EX_IR), .IR_2(MEM_IR), .PC(EX_PC),
    .PC_2(M_PC), .FLUSH(1'b0), .RST(RST), .CLK(CLK));
  // Probe on MEM_RDin
  BitSelector #(.width(32), .group(8)) bitselector_1 (.in(ram_1_data), .out(bitselector_1_out), .sel(MEM_RDin[1:0]));
  RAM #(.addrWidth(10), .dataWidth(32), .bus("separate"), .Select("high"), .simpleMode("false")) ram_1 (
    .addr(MEM_RDin[11:2]), .din(MDin), .data(ram_1_data), .str(MemWrite), .sel(1'b1), .clk(CLK), .clr(RST));  // open: ld
  BitSelector #(.width(32), .group(16)) bitselector_2 (.in(ram_1_data), .out(bitselector_2_out), .sel(MEM_RDin[1]));
  assign bit_extender_4_out = {{24{bitselector_1_out[7]}}, bitselector_1_out};  // Bit_Extender bit_extender_4
  Multiplexer #(.width(32), .enable("false")) multiplexer_12 (
    .in0(bit_extender_4_out), .in1(bit_extender_5_out), .out(multiplexer_12_out),
    .sel(ex_mem_1_memvariant_2[2]));
  assign bit_extender_5_out = {{24{1'b0}}, bitselector_1_out};  // Bit_Extender bit_extender_5
  assign bit_extender_6_out = {{16{bitselector_2_out[15]}}, bitselector_2_out};  // Bit_Extender bit_extender_6
  Multiplexer #(.width(32), .enable("false")) multiplexer_13 (
    .in0(bit_extender_6_out), .in1(bit_extender_7_out), .out(multiplexer_13_out),
    .sel(ex_mem_1_memvariant_2[2]));
  assign bit_extender_7_out = {{16{1'b0}}, bitselector_2_out};  // Bit_Extender bit_extender_7
  Multiplexer #(.select(2), .width(32), .enable("false")) multiplexer_14 (
    .in0(multiplexer_12_out), .in1(multiplexer_13_out), .in2(ram_1_data), .out(multiplexer_14_out),
    .sel(ex_mem_1_memvariant_2[1:0]));  // open: in3
  MEM_WB mem_wb_1 (
    .EN(forwardbubblegen_1_mem_wb_en), .MemToReg(ex_mem_1_memtoreg_2), .MemToReg_2(mem_wb_1_memtoreg_2),
    .RegWrite(ex_mem_1_regwrite_2), .RegWrite_2(RegWrite), .Halt(ex_mem_1_halt_2), .Halt_2(mem_wb_1_halt_2),
    .Result(MEM_RDin), .Result_2(mem_wb_1_result_2), .MemReadData(multiplexer_14_out),
    .MemReadData_2(mem_wb_1_memreaddata_2), .Rd_num(ex_mem_1_rd_num_2), .Rd_num_2(WB_Rd), .IR(MEM_IR),
    .IR_2(WB_IR), .PC(M_PC), .PC_2(WB_PC), .FLUSH(1'b0), .RST(RST), .CLK(CLK));
  // Probe on mem_wb_1_memtoreg_2
  Multiplexer #(.width(32), .enable("false")) multiplexer_15 (
    .in0(mem_wb_1_result_2), .in1(mem_wb_1_memreaddata_2), .out(RDin), .sel(mem_wb_1_memtoreg_2));
  // Probe on RDin
  Adder #(.width(32)) adder_5 (.a(WB_PC), .b(32'h4), .out(WB_PCp4));  // open: cin, cout
  S_R_Flip_Flop #(.trigger("latch")) s_r_ff_1 (
    .S(mem_wb_1_halt_2), .R(1'b0), .Q(halt), .reset(or_2_out));  // open: Qn, preset
  or or_2 (or_2_out, Go, RST);
  not not_4 (not_4_out, halt);
  Counter #(.width(16), .max('hffff)) NXC (
    .count(not_4_out), .Q(\总周期数 ), .clk(CLK), .clr(RST));  // open: load, D, carry, preset, down
  and and_2 (and_2_out, ~halt, UncondJmp);  // AND_Gate
  Counter #(.width(16), .max('hffff)) counter_2 (
    .count(and_2_out), .Q(\无条件分支数 ), .clk(CLK), .clr(RST));  // open: load, D, carry, preset, down
  Comparator #(.width(32)) comparator_3 (.a(EX_R2), .b(32'h22), .eq(comparator_3_eq));  // open: gt, lt
  and and_3 (and_3_out, EX_ECALL, comparator_3_eq);
  and and_4 (EX_Halt, ~comparator_3_eq, EX_ECALL);  // AND_Gate
  and and_5 (and_5_out, ~halt, CondBranch);  // AND_Gate
  and and_6 (and_6_out, ~halt, LoadUse);  // AND_Gate
  Register #(.width(32), .Select("low")) register_1 (.D(EX_R1), .en(and_3_out), .Q(LedData), .clk(CLK), .clr(RST));
  Counter #(.width(16), .max('hffff)) counter_3 (
    .count(and_5_out), .Q(\条件分支成功数 ), .clk(CLK), .clr(RST));  // open: load, D, carry, preset, down
  Counter #(.width(16), .max('hffff)) counter_4 (
    .count(and_6_out), .Q(\LoadUse次数 ), .clk(CLK), .clr(RST));  // open: load, D, carry, preset, down
  and and_7 (and_7_out, ~halt, BranchInstr);  // AND_Gate
  Counter #(.width(16), .max('hffff)) counter_5 (
    .count(and_7_out), .Q(\条件分支指令数 ), .clk(CLK), .clr(RST));  // open: load, D, carry, preset, down
  and and_8 (and_8_out, ~halt, PredictSuccess);  // AND_Gate
  Counter #(.width(16), .max('hffff)) counter_6 (
    .count(and_8_out), .Q(\跳转预测成功数 ), .clk(CLK), .clr(RST));  // open: load, D, carry, preset, down
  and and_9 (and_9_out, ~halt, JAL);  // AND_Gate
  Counter #(.width(16), .max('hffff)) counter_7 (
    .count(and_9_out), .Q(\无条件直接跳转 ), .clk(CLK), .clr(RST));  // open: load, D, carry, preset, down
  and and_10 (and_10_out, ~halt, Flush);  // AND_Gate
  Counter #(.width(16), .max('hffff)) counter_8 (
    .count(and_10_out), .Q(\插入气泡数 ), .clk(CLK), .clr(RST));  // open: load, D, carry, preset, down
  and and_11 (and_11_out, ~halt, EX_PredictFail);  // AND_Gate
  Counter #(.width(16), .max('hffff)) counter_9 (
    .count(and_11_out), .Q(\跳转预测失败数 ), .clk(CLK), .clr(RST));  // open: load, D, carry, preset, down
  and and_12 (and_12_out, ~halt, JALR);  // AND_Gate
  Counter #(.width(16), .max('hffff)) counter_10 (
    .count(and_12_out), .Q(\无条件相对跳转 ), .clk(CLK), .clr(RST));  // open: load, D, carry, preset, down

  // Other names for the same wires on the sheet: MEM_PC[31:0] = M_PC

  // Notes on the sheet:
  //   中断源
  //   时空图监测，可删除
  //   中断等待指示
  //   数码管输出
  //   指令存储器
  //   contents of rom_1 (hex, n*v repeats v):
  //   100493 100006f 100493 200913 300993 100006f 100493 200913 300993 100006f 100493 200913 300993
  //   100006f 100493 200913 300993 3c4000ef 100413 100493 1f49493 900533 2200893 73 24d493 48463 fedff06f
  //   900533 2200893 73 100493 249493 900533 2200893 73 48463 fedff06f 100493 1f49493 900533 2200893 73
  //   4034d493 900533 2200893 73 4044d493 900533 2200893 73 4044d493 900533 2200893 73 4044d493 900533
  //   2200893 73 4044d493 900533 2200893 73 4044d493 900533 2200893 73 4044d493 900533 2200893 73 4044d493
  //   900533 2200893 73 100413 1f41993 41f9d993 433 c00913 300b13 140413 f47413 800293 100313 499993
  //   89e9b3 1300533 2200893 73 406282b3 fe0294e3 140413 f00f93 1f47433 1c41413 800293 100313 49d993
  //   89e9b3 1300533 2200893 73 406282b3 fe0294e3 1c45413 406b0b33 b0463 f95ff06f 2b3 fff2c293 829293
  //   ff2e293 500533 2200893 73 fff00413 493 84a023 140413 448493 84a023 140413 448493 84a023 140413
  //   448493 84a023 140413 448493 84a023 140413 448493 84a023 140413 448493 84a023 140413 448493 84a023
  //   140413 448493 84a023 140413 448493 84a023 140413 448493 84a023 140413 448493 84a023 140413 448493
  //   84a023 140413 448493 84a023 140413 448493 84a023 140413 448493 84a023 140413 448493 140413 433
  //   3c00493 42983 4aa03 149a2b3 28663 134a023 1442023 ffc48493 fe9412e3 800533 2200893 73 440413 3c00493
  //   fc9416e3 3200893 73 200293 1100493 849493 1148493 1049493 900533 2200893 73 1c00e13 254d4b3 900533
  //   2200893 73 fffe0e13 fe0e16e3 a00893 73 8800493 849493 4848493 8700913 891913 5490913 2997933 1091913
  //   11096913 1200533 2200893 73 a00893 73 313 1000e13 8400493 849493 8348493 400913 891913 490913 849493
  //   8248493 849493 8148493 891913 490913 891913 490913 932023 12484b3 430313 fffe0e13 fe0e18e3 2000e13
  //   313 30483 900533 2200893 73 130313 fffe0e13 fe0e14e3 a00893 73 ff100493 900533 2200893 73 148493
  //   fe9068e3 900533 2200893 73 a00893 73 413 140413 800533 2200893 73 240413 800533 2200893 73 340413
  //   800533 2200893 73 440413 800533 2200893 73 540413 800533 2200893 73 640413 800533 2200893 73 740413
  //   800533 2200893 73 840413 800533 2200893 2200893 73 8067
  //   Rd[4:0]
  //   JALR
  //   URET
  //   I-Imm[11:0]
  //   S-Imm[11:0]
  //   B-Imm[12:1]
  //   J-Imm[20:1]
  //   JAL
  //   Beq
  //   Bne
  //   Blt[u]
  //   MemToReg
  //   MemWrite
  //   AluOP
  //   AluResult
  //   AluSrcB
  //   RegWrite
  //   MemVariant
  //   I/S-ImmType
  //   控制位
  //   暂停节拍，不能为0
  //   戳工具置1进入计数暂停模式，ctrl+k时钟自动运行到对应节拍暂停
  //   ctrl+k关闭时钟连续运行，将控制位置零，进入单步调试模式调试
  //   流水调试日志用
  //   可计数暂停的时钟源
  //   数据存储器
  //   为方便自动评测，需要输出流水线各段保存的PC值，注意是PC不是PC+4，另外ID段寄存器写入信息，Mem段内存写入信息也要输出
endmodule

module \封装正确性测试  (
);

  wire IR1, IR2, IR3, MemW, RegW;
  wire [31:0] EX_PC, ID_PC, IF_PC, IR, LED, MDin, MDinr, MEM_PC, PC, RDin, RDinr, WB_PC;

  \单周期RISC_V  \u_单周期risc_v_1  (
    .IR1(IR1), .IR2(IR2), .IR3(IR3), .RegWrite(RegW), .MemWrite(MemW), .PC(PC), .IR(IR), .RDin(RDin),
    .MDin(MDin), .LedData(LED));
  \气泡流水线  \u_气泡流水线_1  (
    .RegWrite(RegW), .MemWrite(MemW), .IF_PC(IF_PC), .ID_PC(ID_PC), .EX_PC(EX_PC), .M_PC(MEM_PC),
    .WB_PC(WB_PC), .RDin(RDinr), .MDin(MDinr), .LedData(LED));
  \单周期_单级中断  \u_单周期_单级中断_1  (
    .IR1(IR1), .IR2(IR2), .IR3(IR3), .RegWrite(RegW), .MemWrite(MemW), .PC(PC), .IR(IR), .RDin(RDin),
    .MDin(MDin), .LedData(LED));
  \重定向流水线_单级中断  \u_重定向流水线_单级中断_1  (
    .IR1(IR1), .IR2(IR2), .IR3(IR3), .RegWrite(RegW), .MemWrite(MemW), .IF_PC(IF_PC), .ID_PC(ID_PC),
    .EX_PC(EX_PC), .M_PC(MEM_PC), .WB_PC(WB_PC), .RDin(RDinr), .MDin(MDinr), .LedData(LED));
  \理想流水线  \u_理想流水线_1  (
    .RegWrite(RegW), .MemWrite(MemW), .IF_PC(IF_PC), .ID_PC(ID_PC), .EX_PC(EX_PC), .M_PC(MEM_PC),
    .WB_PC(WB_PC), .RDin(RDinr), .MDin(MDinr), .LedData(LED));
  \重定向流水线  \u_重定向流水线_1  (
    .RegWrite(RegW), .MemWrite(MemW), .IF_PC(IF_PC), .ID_PC(ID_PC), .EX_PC(EX_PC), .M_PC(MEM_PC),
    .WB_PC(WB_PC), .RDin(RDinr), .MDin(MDinr), .LedData(LED));
  \单周期_多级中断  \u_单周期_多级中断_1  (
    .IR1(IR1), .IR2(IR2), .IR3(IR3), .RegWrite(RegW), .MemWrite(MemW), .PC(PC), .IR(IR), .RDin(RDin),
    .MDin(MDin), .LedData(LED));
  \分支预测流水线  \u_分支预测流水线_1  (
    .RegWrite(RegW), .MemWrite(MemW), .IF_PC(IF_PC), .ID_PC(ID_PC), .EX_PC(EX_PC), .M_PC(MEM_PC),
    .WB_PC(WB_PC), .RDin(RDinr), .MDin(MDinr), .LedData(LED));

  // Notes on the sheet:
  //   单周期封装测试
  //   气泡流水封装测试
  //   单周期+单级中断封装测试
  //   请检查上面封装有无位宽不匹配，引脚标签是否和连接的标签相对应，否则无法在educoder平台上正确测试
  //   理想流水封装测试
  //   重定向流水封装测试
  //   单周期+多级中断封装测试
endmodule
